// Logisim project cdm16.circ as structural Verilog: 1 circuit, main circuit CDM16
module CDM16 (
  input  go,
  input  [5:0] white1,
  input  [5:0] black1,
  input  [5:0] white2,
  input  [5:0] black2,
  input  [5:0] white3,
  input  [5:0] black3,
  input  [5:0] white4,
  input  [5:0] black4,
  input  [5:0] white5,
  input  [5:0] black5,
  input  [5:0] white6,
  input  [5:0] black6,
  input  [5:0] in_14,
  input  [5:0] in_15,
  output flag_bot_finish,
  output [5:0] white_out_1,
  output [5:0] black_out_1,
  output [5:0] white_out_2,
  output [5:0] black_out_2,
  output [5:0] white_out_3,
  output [5:0] black_out_3,
  output [5:0] white_out_4,
  output [5:0] black_out_4,
  output [5:0] white_out_5,
  output [5:0] black_out_5,
  output [5:0] white_out_6,
  output [5:0] black_out_6,
  output [5:0] out_29
);

  wire and_1_out, and_3_out, and_4_out, and_5_out, and_6_out, and_7_out, and_8_out, and_9_out, and_10_out,
       and_11_out, and_12_out, and_13_out, and_14_out, and_15_out, and_16_out, and_17_out, and_18_out,
       cdm_16_1_p2, cdm_16_1_p3, cdm_16_1_p5, cdm_16_1_p6, cdm_16_1_p7, cdm_16_1_p8, cdm_16_1_p9,
       cdm_16_1_p10, cdm_16_1_p11, cdm_16_1_p12, code, comparator_1_eq, comparator_1_lt, comparator_2_eq,
       comparator_3_eq, comparator_4_eq, comparator_5_eq, comparator_6_eq, comparator_7_eq, comparator_8_eq,
       comparator_9_eq, comparator_10_eq, comparator_12_eq, comparator_14_eq, comparator_16_eq,
       counter_1_carry, data, flag, go_t, mem, not_1_out, not_2_out, not_3_out, not_4_out, not_5_out,
       not_6_out, not_7_out, not_8_out, not_9_out, not_10_out, or_1_out, pull_resistor_6_node,
       pull_resistor_9_node, pull_resistor_10_node, pull_resistor_19_node, pull_resistor_21_node,
       pull_resistor_23_node, read_write, register_3_q, register_4_q, register_5_q, tic, transistor_2_out,
       transistor_7_out, word, write, writing;
  wire [3:0] counter_1_q, register_1_q;
  wire [15:0] address, b_1, b_2, b_3, b_4, b_5, b_6, cdm_16_1_p16, cdm_16_1_p17, cdm_16_1_p18, column,
       controlled_buffer_3_out, counter_2_q, multiplexer_1_out, multiplexer_2_out, register_6_q,
       register_7_q, register_8_q, register_9_q, register_10_q, register_11_q, register_12_q, register_13_q,
       register_14_q, register_15_q, register_16_q, register_17_q, register_18_q, register_19_q, rom_1_p4,
       row, transistor_5_out, value, w_1, w_2, w_3, w_4, w_5, w_6;

  // Debugger debugger_1: pin names not known
  Clock clock_1 (.out(tic));
  Counter #(.width(4), .max('hf)) counter_1 (
    .Q(counter_1_q), .carry(counter_1_carry), .clk(tic), .clr(not_2_out));  // open: load, D, count
  assign w_1 = {{10{1'b0}}, white1};  // Bit_Extender bit_extender_1
  assign w_2 = {{10{1'b0}}, white2};  // Bit_Extender bit_extender_2
  assign w_3 = {{10{1'b0}}, white3};  // Bit_Extender bit_extender_3
  assign w_4 = {{10{1'b0}}, white4};  // Bit_Extender bit_extender_4
  assign w_5 = {{10{1'b0}}, white5};  // Bit_Extender bit_extender_5
  assign w_6 = {{10{1'b0}}, white6};  // Bit_Extender bit_extender_6
  assign column = {{10{1'b0}}, in_14};  // Bit_Extender bit_extender_7
  not not_1 (not_1_out, tic);
  Register #(.width(4)) register_1 (.D(counter_1_q), .Q(register_1_q), .clk(not_1_out), .clr(not_2_out));  // open: en
  Multiplexer #(.select(4), .width(16), .enable("false")) multiplexer_1 (
    .in0(16'h80), .in1(16'h82), .in2(16'h84), .in3(16'h86), .in4(16'h88), .in5(16'h8a), .in6(16'h8c),
    .in7(16'h8e), .in8(16'h90), .in9(16'h92), .in10(16'h94), .in11(16'h96), .in12(16'he0), .in13(16'he5),
    .in14(16'he6), .out(multiplexer_1_out), .sel(register_1_q));  // open: in15
  Multiplexer #(.select(4), .width(16), .enable("false")) multiplexer_2 (
    .in0(w_1), .in1(w_2), .in2(w_3), .in3(w_4), .in4(w_5), .in5(w_6), .in6(b_1), .in7(b_2), .in8(b_3),
    .in9(b_4), .in10(b_5), .in11(b_6), .in12(16'h1), .in13(column), .in14(row), .out(multiplexer_2_out),
    .sel(counter_1_q));  // open: in15
  assign b_1 = {{10{1'b0}}, black1};  // Bit_Extender bit_extender_8
  assign b_2 = {{10{1'b0}}, black2};  // Bit_Extender bit_extender_9
  assign b_3 = {{10{1'b0}}, black3};  // Bit_Extender bit_extender_10
  assign b_4 = {{10{1'b0}}, black4};  // Bit_Extender bit_extender_11
  assign b_5 = {{10{1'b0}}, black5};  // Bit_Extender bit_extender_12
  assign b_6 = {{10{1'b0}}, black6};  // Bit_Extender bit_extender_13
  assign row = {{10{1'b0}}, in_15};  // Bit_Extender bit_extender_14
  assign address = writing ? multiplexer_1_out : 16'bz;  // Controlled_Buffer controlled_buffer_1
  Comparator #(.width(16), .mode("unsigned")) comparator_1 (
    .a(address), .b(16'he0), .eq(comparator_1_eq), .lt(comparator_1_lt));  // open: gt
  assign value = writing ? multiplexer_2_out : 16'bz;  // Controlled_Buffer controlled_buffer_2
  Register #(.width(1)) register_2 (.D(go), .Q(writing), .clk(go), .clr(counter_1_carry));  // open: en
  not not_2 (not_2_out, writing);
  Register #(.width(1)) register_3 (
    .D(comparator_1_eq), .en(comparator_1_eq), .Q(register_3_q), .clk(tic), .clr(comparator_1_lt));
  Pull_Resistor pull_resistor_1 (.node(comparator_1_eq));
  Pull_Resistor pull_resistor_2 (.node(comparator_1_lt));
  Transistor #(.\type ("n")) transistor_1 (.in(writing), .out(go_t), .gate(writing));
  Pull_Resistor pull_resistor_3 (.node(go_t));
  Counter #(.width(16), .max('hffff)) counter_2 (
    .Q(counter_2_q), .clk(transistor_2_out), .clr(register_4_q));  // open: load, D, count, carry
  Transistor #(.\type ("n")) transistor_2 (.in(tic), .out(transistor_2_out), .gate(and_1_out));
  not not_3 (not_3_out, flag);
  and and_1 (and_1_out, not_3_out, register_3_q);
  Comparator #(.width(16), .mode("unsigned")) comparator_2 (
    .a(counter_2_q), .b(16'h100), .eq(comparator_2_eq));  // open: gt, lt
  and and_2 (write, go_t, register_5_q);
  Transistor #(.\type ("n")) transistor_3 (.in(and_1_out), .out(flag_bot_finish), .gate(comparator_2_eq));
  Pull_Resistor pull_resistor_4 (.node(flag_bot_finish));
  Register #(.width(1)) register_4 (
    .D(flag_bot_finish), .en(flag_bot_finish), .Q(register_4_q), .clk(tic), .clr(not_4_out));
  not not_4 (not_4_out, and_1_out);
  or or_1 (or_1_out, go_t, not_5_out);
  Register #(.width(1)) register_5 (.D(or_1_out), .Q(register_5_q), .clk(not_6_out));  // open: en, clr
  not not_5 (not_5_out, flag);
  not not_6 (not_6_out, tic);
  // Probe on cdm_16_1_p2
  // Probe on cdm_16_1_p3
  // Probe on cdm_16_1_p5
  // Probe on cdm_16_1_p6
  // CdM_16 cdm_16_1: pin names not known; wires that end beside it: register_5_q, cdm_16_1_p2, cdm_16_1_p3, tic, cdm_16_1_p5, cdm_16_1_p6, cdm_16_1_p7, cdm_16_1_p8, cdm_16_1_p9, cdm_16_1_p10, cdm_16_1_p11, cdm_16_1_p12, mem, read_write, word, cdm_16_1_p16, cdm_16_1_p17, cdm_16_1_p18
  // Probe on cdm_16_1_p10
  // Probe on cdm_16_1_p11
  // Probe on cdm_16_1_p7
  // Probe on cdm_16_1_p8
  // Probe on cdm_16_1_p9
  Pull_Resistor pull_resistor_5 (.node(code));
  Pull_Resistor pull_resistor_6 (.node(pull_resistor_6_node));
  Decoder decoder_1 (.out0(code), .out1(pull_resistor_6_node), .sel(cdm_16_1_p12), .en(mem));
  assign controlled_buffer_3_out = and_3_out ? cdm_16_1_p17 : 16'bz;  // Controlled_Buffer controlled_buffer_3
  and and_3 (and_3_out, not_7_out, not_8_out);
  not not_7 (not_7_out, write);
  not not_8 (not_8_out, read_write);
  not not_9 (not_9_out, write);
  and and_4 (and_4_out, not_9_out, read_write);
  assign cdm_16_1_p18 = and_4_out ? controlled_buffer_3_out : 16'bz;  // Controlled_Buffer controlled_buffer_4
  Transistor #(.gate("br")) transistor_4 (.in(pull_resistor_6_node), .out(data), .gate(write));
  Pull_Resistor #(.pull(1)) pull_resistor_7 (.node(data));
  not not_10 (not_10_out, read_write);
  Transistor #(.\type ("n"), .width(16)) transistor_5 (.in(address), .out(transistor_5_out), .gate(write));
  Transistor #(.gate("br"), .width(16)) transistor_6 (.in(cdm_16_1_p16), .out(transistor_5_out), .gate(write));
  // Probe on transistor_5_out
  Transistor transistor_7 (.in(not_10_out), .out(transistor_7_out), .gate(write));
  Pull_Resistor #(.pull(1)) pull_resistor_8 (.node(transistor_7_out));
  Pull_Resistor pull_resistor_9 (.node(pull_resistor_9_node));
  Transistor transistor_8 (.in(word), .out(pull_resistor_9_node), .gate(write));
  Comparator #(.width(16)) comparator_3 (.a(transistor_5_out), .b(16'h80), .eq(comparator_3_eq));  // open: gt, lt
  Comparator #(.width(16)) comparator_4 (.a(transistor_5_out), .b(16'h82), .eq(comparator_4_eq));  // open: gt, lt
  Comparator #(.width(16)) comparator_5 (.a(transistor_5_out), .b(16'h84), .eq(comparator_5_eq));  // open: gt, lt
  Comparator #(.width(16)) comparator_6 (.a(transistor_5_out), .b(16'h86), .eq(comparator_6_eq));  // open: gt, lt
  Comparator #(.width(16)) comparator_7 (.a(transistor_5_out), .b(16'h88), .eq(comparator_7_eq));  // open: gt, lt
  Comparator #(.width(16)) comparator_8 (.a(transistor_5_out), .b(16'h8a), .eq(comparator_8_eq));  // open: gt, lt
  Pull_Resistor pull_resistor_10 (.node(pull_resistor_10_node));
  Transistor #(.gate("br")) transistor_9 (.in(read_write), .out(pull_resistor_10_node), .gate(write));
  Pull_Resistor pull_resistor_11 (.node(comparator_3_eq));
  Pull_Resistor pull_resistor_12 (.node(comparator_4_eq));
  Pull_Resistor pull_resistor_13 (.node(comparator_5_eq));
  Pull_Resistor pull_resistor_14 (.node(comparator_6_eq));
  Pull_Resistor pull_resistor_15 (.node(comparator_7_eq));
  Pull_Resistor pull_resistor_16 (.node(comparator_8_eq));
  // ROM rom_1: pin names not known; wires that end beside it: transistor_5_out, code, word, rom_1_p4
  // RAM ram_1: pin names not known; wires that end beside it: transistor_5_out, pull_resistor_9_node, data, tic, pull_resistor_10_node, controlled_buffer_3_out
  Transistor #(.width(16)) transistor_10 (.in(rom_1_p4), .out(controlled_buffer_3_out), .gate(write));
  Transistor #(.\type ("n"), .width(16)) transistor_11 (.in(value), .out(controlled_buffer_3_out), .gate(write));
  Register #(.width(16)) register_6 (.D(controlled_buffer_3_out), .Q(register_6_q), .clk(and_5_out));  // open: en, clr
  and and_5 (and_5_out, comparator_3_eq, data, transistor_7_out);
  Register #(.width(16)) register_7 (.D(controlled_buffer_3_out), .Q(register_7_q), .clk(and_6_out));  // open: en, clr
  and and_6 (and_6_out, comparator_4_eq, data, transistor_7_out);
  Register #(.width(16)) register_8 (.D(controlled_buffer_3_out), .Q(register_8_q), .clk(and_7_out));  // open: en, clr
  and and_7 (and_7_out, comparator_5_eq, data, transistor_7_out);
  Register #(.width(16)) register_9 (.D(controlled_buffer_3_out), .Q(register_9_q), .clk(and_8_out));  // open: en, clr
  and and_8 (and_8_out, comparator_6_eq, data, transistor_7_out);
  Register #(.width(16)) register_10 (
    .D(controlled_buffer_3_out), .Q(register_10_q), .clk(and_9_out));  // open: en, clr
  and and_9 (and_9_out, comparator_7_eq, data, transistor_7_out);
  Register #(.width(16)) register_11 (
    .D(controlled_buffer_3_out), .Q(register_11_q), .clk(and_10_out));  // open: en, clr
  and and_10 (and_10_out, comparator_8_eq, data, transistor_7_out);
  Comparator #(.width(16)) comparator_9 (.a(transistor_5_out), .b(16'he0), .eq(comparator_9_eq));  // open: gt, lt
  Bit_Extender #(.in_width(16), .out_width(6)) bit_extender_15 (.in(register_6_q), .out(white_out_1));
  Bit_Extender #(.in_width(16), .out_width(6)) bit_extender_16 (.in(register_7_q), .out(white_out_2));
  Bit_Extender #(.in_width(16), .out_width(6)) bit_extender_17 (.in(register_8_q), .out(white_out_3));
  Bit_Extender #(.in_width(16), .out_width(6)) bit_extender_18 (.in(register_9_q), .out(white_out_4));
  Bit_Extender #(.in_width(16), .out_width(6)) bit_extender_19 (.in(register_10_q), .out(white_out_5));
  Bit_Extender #(.in_width(16), .out_width(6)) bit_extender_20 (.in(register_11_q), .out(white_out_6));
  Pull_Resistor pull_resistor_17 (.node(comparator_9_eq));
  Comparator #(.width(16)) comparator_10 (.a(transistor_5_out), .b(16'h8c), .eq(comparator_10_eq));  // open: gt, lt
  Pull_Resistor pull_resistor_18 (.node(comparator_10_eq));
  Pull_Resistor pull_resistor_19 (.node(pull_resistor_19_node));
  Comparator #(.width(16)) comparator_11 (
    .a(transistor_5_out), .b(16'h8e), .eq(pull_resistor_19_node));  // open: gt, lt
  Comparator #(.width(16)) comparator_12 (.a(transistor_5_out), .b(16'h90), .eq(comparator_12_eq));  // open: gt, lt
  Pull_Resistor pull_resistor_20 (.node(comparator_12_eq));
  Pull_Resistor pull_resistor_21 (.node(pull_resistor_21_node));
  Comparator #(.width(16)) comparator_13 (
    .a(transistor_5_out), .b(16'h92), .eq(pull_resistor_21_node));  // open: gt, lt
  Comparator #(.width(16)) comparator_14 (.a(transistor_5_out), .b(16'h94), .eq(comparator_14_eq));  // open: gt, lt
  Pull_Resistor pull_resistor_22 (.node(comparator_14_eq));
  Pull_Resistor pull_resistor_23 (.node(pull_resistor_23_node));
  Comparator #(.width(16)) comparator_15 (
    .a(transistor_5_out), .b(16'h96), .eq(pull_resistor_23_node));  // open: gt, lt
  Register #(.width(16)) register_12 (
    .D(controlled_buffer_3_out), .Q(register_12_q), .clk(and_11_out));  // open: en, clr
  and and_11 (and_11_out, comparator_16_eq, data, transistor_7_out);
  Comparator #(.width(16)) comparator_16 (.a(transistor_5_out), .b(16'he4), .eq(comparator_16_eq));  // open: gt, lt
  Register #(.width(16)) register_13 (
    .D(controlled_buffer_3_out), .Q(register_13_q), .clk(and_12_out));  // open: en, clr
  Bit_Extender #(.in_width(16), .out_width(1)) bit_extender_21 (.in(register_13_q), .out(flag));
  and and_12 (and_12_out, comparator_9_eq, data, transistor_7_out);
  Bit_Extender #(.in_width(16), .out_width(6)) bit_extender_22 (.in(register_12_q), .out(out_29));
  and and_13 (and_13_out, comparator_10_eq, data, transistor_7_out);
  and and_14 (and_14_out, pull_resistor_19_node, data, transistor_7_out);
  and and_15 (and_15_out, comparator_12_eq, data, transistor_7_out);
  and and_16 (and_16_out, pull_resistor_21_node, data, transistor_7_out);
  and and_17 (and_17_out, comparator_14_eq, data, transistor_7_out);
  and and_18 (and_18_out, pull_resistor_23_node, data, transistor_7_out);
  Bit_Extender #(.in_width(16), .out_width(6)) bit_extender_23 (.in(register_14_q), .out(black_out_1));
  Register #(.width(16)) register_14 (
    .D(controlled_buffer_3_out), .Q(register_14_q), .clk(and_13_out));  // open: en, clr
  Bit_Extender #(.in_width(16), .out_width(6)) bit_extender_24 (.in(register_15_q), .out(black_out_2));
  Register #(.width(16)) register_15 (
    .D(controlled_buffer_3_out), .Q(register_15_q), .clk(and_14_out));  // open: en, clr
  Bit_Extender #(.in_width(16), .out_width(6)) bit_extender_25 (.in(register_16_q), .out(black_out_3));
  Register #(.width(16)) register_16 (
    .D(controlled_buffer_3_out), .Q(register_16_q), .clk(and_15_out));  // open: en, clr
  Bit_Extender #(.in_width(16), .out_width(6)) bit_extender_26 (.in(register_17_q), .out(black_out_4));
  Register #(.width(16)) register_17 (
    .D(controlled_buffer_3_out), .Q(register_17_q), .clk(and_16_out));  // open: en, clr
  Register #(.width(16)) register_18 (
    .D(controlled_buffer_3_out), .Q(register_18_q), .clk(and_17_out));  // open: en, clr
  Bit_Extender #(.in_width(16), .out_width(6)) bit_extender_27 (.in(register_18_q), .out(black_out_5));
  Bit_Extender #(.in_width(16), .out_width(6)) bit_extender_28 (.in(register_19_q), .out(black_out_6));
  Register #(.width(16)) register_19 (
    .D(controlled_buffer_3_out), .Q(register_19_q), .clk(and_18_out));  // open: en, clr

  // Other names for the same wires on the sheet: b_out_1[5:0] = black_out_1; b_out_2[5:0] = black_out_2;
  //   b_out_3[5:0] = black_out_3; b_out_4[5:0] = black_out_4; b_out_5[5:0] = black_out_5; b_out_6[5:0] = black_out_6;
  //   louding[5:0] = out_29; w_out_1[5:0] = white_out_1; w_out_2[5:0] = white_out_2; w_out_3[5:0] = white_out_3;
  //   w_out_4[5:0] = white_out_4; w_out_5[5:0] = white_out_5; w_out_6[5:0] = white_out_6

  // Notes on the sheet:
  //   введи здесь адресса
endmodule
