// Logisim project cdm16_harward.circ as structural Verilog: 3 circuits, main circuit CDM16
module CDM16 (
  input  [15:0] adr,
  input  [15:0] val,
  input  hold,
  input  write,
  output FLAG,
  output [15:0] BLACK_1,
  output [15:0] WHITE_1,
  output [15:0] BLACK_2,
  output [15:0] WHITE_2,
  output [15:0] BLACK_3,
  output [15:0] WHITE_3,
  output [15:0] BLACK_4,
  output [15:0] WHITE_4,
  output [15:0] BLACK_5,
  output [15:0] WHITE_5,
  output [15:0] BLACK_6,
  output [15:0] WHITE_6
);

  wire and_2_out, and_3_out, and_4_out, and_5_out, and_6_out, and_7_out, and_8_out, and_9_out, and_10_out,
       and_11_out, and_12_out, and_13_out, and_14_out, and_15_out, and_16_out, cdm_16_1_p2, cdm_16_1_p3,
       cdm_16_1_p5, cdm_16_1_p6, cdm_16_1_p7, cdm_16_1_p8, cdm_16_1_p9, cdm_16_1_p10, cdm_16_1_p11,
       cdm_16_1_p12, cdm_16_1_p13, cl, code, comparator_1_eq, comparator_3_eq, comparator_4_eq,
       comparator_6_eq, comparator_10_eq, comparator_11_eq, comparator_12_eq, comparator_13_eq, data, mem,
       not_1_out, not_2_out, not_3_out, not_4_out, not_5_out, not_6_out, or_1_out, or_2_out,
       pull_resistor_3_node, pull_resistor_7_node, pull_resistor_10_node, pull_resistor_12_node,
       pull_resistor_13_node, pull_resistor_14_node, pull_resistor_15_node, read_write, register_1_q,
       transistor_2_out, transistor_5_out, word, write_t;
  wire [15:0] cdm_16_1_p17, cdm_16_1_p18, cdm_16_1_p19, controlled_buffer_2_out, register_14_q, rom_1_p4,
       transistor_3_out;

  // Debugger debugger_1: pin names not known
  and and_1 (write_t, write, register_1_q);
  Register #(.width(1)) register_1 (.D(or_1_out), .Q(register_1_q), .clk(not_1_out));  // open: en, clr
  or or_1 (or_1_out, write, or_2_out);
  not not_1 (not_1_out, cl);
  or or_2 (or_2_out, not_2_out, hold);
  // Probe on cdm_16_1_p2
  // CdM_16 cdm_16_1: pin names not known; wires that end beside it: register_1_q, cdm_16_1_p2, cdm_16_1_p3, cl, cdm_16_1_p5, cdm_16_1_p6, cdm_16_1_p7, cdm_16_1_p8, cdm_16_1_p9, cdm_16_1_p10, cdm_16_1_p11, cdm_16_1_p12, cdm_16_1_p13, mem, read_write, word, cdm_16_1_p17, cdm_16_1_p18, cdm_16_1_p19
  Clock clock_1 (.out(cl));
  not not_2 (not_2_out, FLAG);
  // Probe on cdm_16_1_p3
  // Probe on cdm_16_1_p11
  // Probe on cdm_16_1_p5
  // Probe on cdm_16_1_p6
  // Probe on cdm_16_1_p7
  // Probe on cdm_16_1_p9
  // Probe on cdm_16_1_p10
  // Probe on cdm_16_1_p8
  // Probe on cdm_16_1_p12
  not not_3 (not_3_out, write_t);
  not not_4 (not_4_out, write_t);
  assign cdm_16_1_p19 = and_3_out ? controlled_buffer_2_out : 16'bz;  // Controlled_Buffer controlled_buffer_1
  assign controlled_buffer_2_out = and_2_out ? cdm_16_1_p18 : 16'bz;  // Controlled_Buffer controlled_buffer_2
  and and_2 (and_2_out, not_3_out, not_5_out);
  not not_5 (not_5_out, read_write);
  not not_6 (not_6_out, read_write);
  and and_3 (and_3_out, not_4_out, read_write);
  Pull_Resistor pull_resistor_1 (.node(code));
  Pull_Resistor #(.pull(1)) pull_resistor_2 (.node(data));
  Transistor #(.gate("br")) transistor_1 (.in(pull_resistor_3_node), .out(data), .gate(write_t));
  Pull_Resistor pull_resistor_3 (.node(pull_resistor_3_node));
  Decoder decoder_1 (.out0(code), .out1(pull_resistor_3_node), .sel(cdm_16_1_p13), .en(mem));
  Transistor transistor_2 (.in(not_6_out), .out(transistor_2_out), .gate(write_t));
  Pull_Resistor #(.pull(1)) pull_resistor_4 (.node(transistor_2_out));
  Transistor #(.\type ("n"), .width(16)) transistor_3 (.in(adr), .out(transistor_3_out), .gate(write_t));
  Transistor #(.gate("br"), .width(16)) transistor_4 (.in(cdm_16_1_p17), .out(transistor_3_out), .gate(write_t));
  // Probe on transistor_3_out
  Transistor transistor_5 (.in(word), .out(transistor_5_out), .gate(write_t));
  Pull_Resistor pull_resistor_5 (.node(transistor_5_out));
  Comparator #(.width(16)) comparator_1 (.a(transistor_3_out), .b(16'h80), .eq(comparator_1_eq));  // open: gt, lt
  Pull_Resistor pull_resistor_6 (.node(comparator_1_eq));
  Pull_Resistor pull_resistor_7 (.node(pull_resistor_7_node));
  Comparator #(.width(16)) comparator_2 (.a(transistor_3_out), .b(16'h82), .eq(pull_resistor_7_node));  // open: gt, lt
  Comparator #(.width(16)) comparator_3 (.a(transistor_3_out), .b(16'h84), .eq(comparator_3_eq));  // open: gt, lt
  Pull_Resistor pull_resistor_8 (.node(comparator_3_eq));
  Comparator #(.width(16)) comparator_4 (.a(transistor_3_out), .b(16'h86), .eq(comparator_4_eq));  // open: gt, lt
  Pull_Resistor pull_resistor_9 (.node(comparator_4_eq));
  Pull_Resistor pull_resistor_10 (.node(pull_resistor_10_node));
  Comparator #(.width(16)) comparator_5 (.a(transistor_3_out), .b(16'h88), .eq(pull_resistor_10_node));  // open: gt, lt
  Comparator #(.width(16)) comparator_6 (.a(transistor_3_out), .b(16'h8a), .eq(comparator_6_eq));  // open: gt, lt
  Pull_Resistor pull_resistor_11 (.node(comparator_6_eq));
  Pull_Resistor pull_resistor_12 (.node(pull_resistor_12_node));
  Transistor #(.gate("br")) transistor_6 (.in(read_write), .out(pull_resistor_12_node), .gate(write_t));
  // ROM rom_1: pin names not known; wires that end beside it: transistor_3_out, code, word, rom_1_p4
  // RAM ram_1: pin names not known; wires that end beside it: transistor_3_out, transistor_5_out, data, cl, pull_resistor_12_node, controlled_buffer_2_out
  Register #(.width(16)) register_2 (.D(controlled_buffer_2_out), .Q(WHITE_1), .clk(and_4_out));  // open: en, clr
  and and_4 (and_4_out, comparator_1_eq, data, transistor_2_out);
  Register #(.width(16)) register_3 (.D(controlled_buffer_2_out), .Q(WHITE_2), .clk(and_5_out));  // open: en, clr
  and and_5 (and_5_out, pull_resistor_7_node, data, transistor_2_out);
  Register #(.width(16)) register_4 (.D(controlled_buffer_2_out), .Q(WHITE_3), .clk(and_6_out));  // open: en, clr
  and and_6 (and_6_out, comparator_3_eq, data, transistor_2_out);
  Register #(.width(16)) register_5 (.D(controlled_buffer_2_out), .Q(WHITE_4), .clk(and_7_out));  // open: en, clr
  and and_7 (and_7_out, comparator_4_eq, data, transistor_2_out);
  Register #(.width(16)) register_6 (.D(controlled_buffer_2_out), .Q(WHITE_5), .clk(and_8_out));  // open: en, clr
  and and_8 (and_8_out, pull_resistor_10_node, data, transistor_2_out);
  Register #(.width(16)) register_7 (.D(controlled_buffer_2_out), .Q(WHITE_6), .clk(and_9_out));  // open: en, clr
  and and_9 (and_9_out, comparator_6_eq, data, transistor_2_out);
  Transistor #(.width(16)) transistor_7 (.in(rom_1_p4), .out(controlled_buffer_2_out), .gate(write_t));
  Transistor #(.\type ("n"), .width(16)) transistor_8 (.in(val), .out(controlled_buffer_2_out), .gate(write_t));
  Pull_Resistor pull_resistor_13 (.node(pull_resistor_13_node));
  Comparator #(.width(16)) comparator_7 (.a(transistor_3_out), .b(16'he0), .eq(pull_resistor_13_node));  // open: gt, lt
  Pull_Resistor pull_resistor_14 (.node(pull_resistor_14_node));
  Comparator #(.width(16)) comparator_8 (.a(transistor_3_out), .b(16'h8c), .eq(pull_resistor_14_node));  // open: gt, lt
  Pull_Resistor pull_resistor_15 (.node(pull_resistor_15_node));
  Comparator #(.width(16)) comparator_9 (.a(transistor_3_out), .b(16'h8e), .eq(pull_resistor_15_node));  // open: gt, lt
  Comparator #(.width(16)) comparator_10 (.a(transistor_3_out), .b(16'h90), .eq(comparator_10_eq));  // open: gt, lt
  Pull_Resistor pull_resistor_16 (.node(comparator_10_eq));
  Comparator #(.width(16)) comparator_11 (.a(transistor_3_out), .b(16'h92), .eq(comparator_11_eq));  // open: gt, lt
  Pull_Resistor pull_resistor_17 (.node(comparator_11_eq));
  Comparator #(.width(16)) comparator_12 (.a(transistor_3_out), .b(16'h94), .eq(comparator_12_eq));  // open: gt, lt
  Pull_Resistor pull_resistor_18 (.node(comparator_12_eq));
  Comparator #(.width(16)) comparator_13 (.a(transistor_3_out), .b(16'h96), .eq(comparator_13_eq));  // open: gt, lt
  Pull_Resistor pull_resistor_19 (.node(comparator_13_eq));
  and and_10 (and_10_out, pull_resistor_13_node, data, transistor_2_out);
  Register #(.width(16)) register_8 (.D(controlled_buffer_2_out), .Q(BLACK_1), .clk(and_11_out));  // open: en, clr
  and and_11 (and_11_out, pull_resistor_14_node, data, transistor_2_out);
  Register #(.width(16)) register_9 (.D(controlled_buffer_2_out), .Q(BLACK_2), .clk(and_12_out));  // open: en, clr
  and and_12 (and_12_out, pull_resistor_15_node, data, transistor_2_out);
  Register #(.width(16)) register_10 (.D(controlled_buffer_2_out), .Q(BLACK_3), .clk(and_13_out));  // open: en, clr
  and and_13 (and_13_out, comparator_10_eq, data, transistor_2_out);
  Register #(.width(16)) register_11 (.D(controlled_buffer_2_out), .Q(BLACK_4), .clk(and_14_out));  // open: en, clr
  and and_14 (and_14_out, comparator_11_eq, data, transistor_2_out);
  Register #(.width(16)) register_12 (.D(controlled_buffer_2_out), .Q(BLACK_5), .clk(and_15_out));  // open: en, clr
  and and_15 (and_15_out, comparator_12_eq, data, transistor_2_out);
  Register #(.width(16)) register_13 (.D(controlled_buffer_2_out), .Q(BLACK_6), .clk(and_16_out));  // open: en, clr
  and and_16 (and_16_out, comparator_13_eq, data, transistor_2_out);
  Register #(.width(16)) register_14 (
    .D(controlled_buffer_2_out), .Q(register_14_q), .clk(and_10_out));  // open: en, clr
  Bit_Extender #(.in_width(16), .out_width(1)) bit_extender_1 (.in(register_14_q), .out(FLAG));

  // Notes on the sheet:
  //   hold приостанавливает процессор
  //   write как hold но даёт возможность писать в ОЗУ
endmodule

module wrtr (
  input  go,
  input  [5:0] white1,
  input  [5:0] black1,
  input  [5:0] white2,
  input  [5:0] black2,
  input  [5:0] white3,
  input  [5:0] black3,
  input  [5:0] white4,
  input  [5:0] black4,
  input  [5:0] white5,
  input  [5:0] black5,
  input  [5:0] white6,
  input  [5:0] black6,
  output flag_bot_finish,
  output [5:0] white_out_1,
  output [5:0] black_out_1,
  output [5:0] white_out_2,
  output [5:0] black_out_2,
  output [5:0] white_out_3,
  output [5:0] black_out_3,
  output [5:0] white_out_4,
  output [5:0] black_out_4,
  output [5:0] white_out_5,
  output [5:0] black_out_5,
  output [5:0] white_out_6,
  output [5:0] black_out_6
);

  wire and_1_out, cdm16_1_flag, comparator_1_eq, comparator_1_lt, comparator_2_eq, counter_1_carry,
       not_1_out, not_2_out, not_3_out, not_4_out, pull_resistor_1_node, pull_resistor_3_node, register_3_q,
       register_4_q, tic, transistor_2_out, writing;
  wire [3:0] counter_1_q, register_1_q;
  wire [15:0] b_1, b_2, b_3, b_4, b_5, b_6, cdm16_1_black_1, cdm16_1_black_2, cdm16_1_black_3,
       cdm16_1_black_4, cdm16_1_black_5, cdm16_1_black_6, cdm16_1_white_1, cdm16_1_white_2, cdm16_1_white_3,
       cdm16_1_white_4, cdm16_1_white_5, cdm16_1_white_6, controlled_buffer_1_out, controlled_buffer_2_out,
       counter_2_q, multiplexer_1_out, multiplexer_2_out, w_1, w_2, w_3, w_4, w_5, w_6;

  Clock clock_1 (.out(tic));
  not not_1 (not_1_out, tic);
  Counter #(.width(4), .max('hf)) counter_1 (
    .Q(counter_1_q), .carry(counter_1_carry), .clk(tic), .clr(not_2_out));  // open: load, D, count
  assign w_1 = {{10{1'b0}}, white1};  // Bit_Extender bit_extender_1
  assign w_2 = {{10{1'b0}}, white2};  // Bit_Extender bit_extender_2
  assign w_3 = {{10{1'b0}}, white3};  // Bit_Extender bit_extender_3
  assign w_4 = {{10{1'b0}}, white4};  // Bit_Extender bit_extender_4
  assign w_5 = {{10{1'b0}}, white5};  // Bit_Extender bit_extender_5
  assign w_6 = {{10{1'b0}}, white6};  // Bit_Extender bit_extender_6
  Register #(.width(4)) register_1 (.D(counter_1_q), .Q(register_1_q), .clk(not_1_out), .clr(not_2_out));  // open: en
  Multiplexer #(.select(4), .width(16), .enable("false")) multiplexer_1 (
    .in0(16'h80), .in1(16'h82), .in2(16'h84), .in3(16'h86), .in4(16'h88), .in5(16'h8a), .in6(16'h8c),
    .in7(16'h8e), .in8(16'h90), .in9(16'h92), .in10(16'h94), .in11(16'h96), .in12(16'he0),
    .out(multiplexer_1_out), .sel(register_1_q));  // open: in13, in14, in15
  Multiplexer #(.select(4), .width(16), .enable("false")) multiplexer_2 (
    .in0(w_1), .in1(w_2), .in2(w_3), .in3(w_4), .in4(w_5), .in5(w_6), .in6(b_1), .in7(b_2), .in8(b_3),
    .in9(b_4), .in10(b_5), .in11(b_6), .in12(16'h1), .out(multiplexer_2_out), .sel(counter_1_q));  // open: in13, in14, in15
  assign b_1 = {{10{1'b0}}, black1};  // Bit_Extender bit_extender_7
  assign b_2 = {{10{1'b0}}, black2};  // Bit_Extender bit_extender_8
  assign b_3 = {{10{1'b0}}, black3};  // Bit_Extender bit_extender_9
  assign b_4 = {{10{1'b0}}, black4};  // Bit_Extender bit_extender_10
  assign b_5 = {{10{1'b0}}, black5};  // Bit_Extender bit_extender_11
  assign b_6 = {{10{1'b0}}, black6};  // Bit_Extender bit_extender_12
  assign controlled_buffer_1_out = writing ? multiplexer_1_out : 16'bz;  // Controlled_Buffer controlled_buffer_1
  assign controlled_buffer_2_out = writing ? multiplexer_2_out : 16'bz;  // Controlled_Buffer controlled_buffer_2
  Register #(.width(1)) register_2 (.D(go), .Q(writing), .clk(go), .clr(counter_1_carry));  // open: en
  not not_2 (not_2_out, writing);
  Pull_Resistor pull_resistor_1 (.node(pull_resistor_1_node));
  Transistor #(.\type ("n")) transistor_1 (.in(writing), .out(pull_resistor_1_node), .gate(writing));
  Comparator #(.width(16), .mode("unsigned")) comparator_1 (
    .a(controlled_buffer_1_out), .b(16'he0), .eq(comparator_1_eq), .lt(comparator_1_lt));  // open: gt
  Pull_Resistor pull_resistor_2 (.node(comparator_1_eq));
  from_16_to_6 from_16_to_6_1 (.in_1(cdm16_1_black_1), .out_2(black_out_1));
  from_16_to_6 from_16_to_6_2 (.in_1(cdm16_1_black_3), .out_2(black_out_3));
  from_16_to_6 from_16_to_6_3 (.in_1(cdm16_1_black_4), .out_2(black_out_4));
  from_16_to_6 from_16_to_6_4 (.in_1(cdm16_1_black_2), .out_2(black_out_2));
  CDM16 cdm16_1 (
    .WHITE_1(cdm16_1_white_1), .WHITE_2(cdm16_1_white_2), .WHITE_3(cdm16_1_white_3),
    .WHITE_4(cdm16_1_white_4), .write(pull_resistor_1_node), .adr(controlled_buffer_1_out),
    .val(controlled_buffer_2_out), .hold(pull_resistor_3_node), .WHITE_5(cdm16_1_white_5),
    .WHITE_6(cdm16_1_white_6), .BLACK_1(cdm16_1_black_1), .BLACK_2(cdm16_1_black_2),
    .BLACK_3(cdm16_1_black_3), .BLACK_4(cdm16_1_black_4), .BLACK_5(cdm16_1_black_5),
    .BLACK_6(cdm16_1_black_6), .FLAG(cdm16_1_flag));
  Pull_Resistor pull_resistor_3 (.node(pull_resistor_3_node));
  from_16_to_6 from_16_to_6_5 (.in_1(cdm16_1_white_1), .out_2(white_out_1));
  from_16_to_6 from_16_to_6_6 (.in_1(cdm16_1_white_2), .out_2(white_out_2));
  from_16_to_6 from_16_to_6_7 (.in_1(cdm16_1_white_4), .out_2(white_out_4));
  from_16_to_6 from_16_to_6_8 (.in_1(cdm16_1_white_3), .out_2(white_out_3));
  Pull_Resistor pull_resistor_4 (.node(comparator_1_lt));
  from_16_to_6 from_16_to_6_9 (.in_1(cdm16_1_black_5), .out_2(black_out_5));
  from_16_to_6 from_16_to_6_10 (.in_1(cdm16_1_black_6), .out_2(black_out_6));
  from_16_to_6 from_16_to_6_11 (.in_1(cdm16_1_white_6), .out_2(white_out_6));
  from_16_to_6 from_16_to_6_12 (.in_1(cdm16_1_white_5), .out_2(white_out_5));
  not not_3 (not_3_out, cdm16_1_flag);
  Register #(.width(1)) register_3 (
    .D(comparator_1_eq), .en(comparator_1_eq), .Q(register_3_q), .clk(tic), .clr(comparator_1_lt));
  and and_1 (and_1_out, not_3_out, register_3_q);
  Counter #(.width(16), .max('hffff)) counter_2 (
    .Q(counter_2_q), .clk(transistor_2_out), .clr(register_4_q));  // open: load, D, count, carry
  Transistor #(.\type ("n")) transistor_2 (.in(tic), .out(transistor_2_out), .gate(and_1_out));
  Comparator #(.width(16), .mode("unsigned")) comparator_2 (
    .a(counter_2_q), .b(16'h100), .eq(comparator_2_eq));  // open: gt, lt
  Pull_Resistor pull_resistor_5 (.node(flag_bot_finish));
  Transistor #(.\type ("n")) transistor_3 (.in(and_1_out), .out(flag_bot_finish), .gate(comparator_2_eq));
  Register #(.width(1)) register_4 (
    .D(flag_bot_finish), .en(flag_bot_finish), .Q(register_4_q), .clk(tic), .clr(not_4_out));
  not not_4 (not_4_out, and_1_out);

  // Other names for the same wires on the sheet: b_out_1[5:0] = black_out_1; b_out_2[5:0] = black_out_2;
  //   b_out_3[5:0] = black_out_3; b_out_4[5:0] = black_out_4; b_out_5[5:0] = black_out_5; b_out_6[5:0] = black_out_6;
  //   w_out_1[5:0] = white_out_1; w_out_2[5:0] = white_out_2; w_out_3[5:0] = white_out_3; w_out_4[5:0] = white_out_4;
  //   w_out_5[5:0] = white_out_5; w_out_6[5:0] = white_out_6
endmodule

module from_16_to_6 (
  input  [15:0] in_1,
  output [5:0] out_2
);

  Bit_Extender #(.in_width(16), .out_width(6)) bit_extender_1 (.in(in_1), .out(out_2));
endmodule
