// Logisim project reversi.circ as structural Verilog
module main (
);

  wire Bot_win__and_you_lose__if_you_don_t_understand, button_1_out, button_2_out, button_3_out,
       button_4_out, button_5_out, button_6_out, button_7_out, button_8_out, button_9_out, button_10_out,
       button_11_out, button_12_out, button_13_out, button_14_out, button_15_out, button_16_out,
       button_17_out, button_18_out, button_19_out, button_20_out, button_21_out, button_22_out,
       button_23_out, button_24_out, button_25_out, button_26_out, button_27_out, button_28_out,
       button_29_out, button_30_out, button_31_out, button_32_out, button_33_out, button_34_out,
       button_35_out, button_36_out, can, change_turn, Draw, game_over, not_1_out, reset, start,
       The_game_is_on_or_not, turn, turnnowb, turnnoww, You_win;
  wire [2:0] row;
  wire [3:0] to_counter_1_out_2, to_counter_1_out_3, to_counter_2_out_2, to_counter_2_out_3;
  wire [5:0] _0, _1, _2, _3, _4, _5, column, registers_to_matrix_1_black_count, registers_to_matrix_1_out_26,
       registers_to_matrix_1_white_count;
  wire [11:0] registers_to_matrix_1_out_7, registers_to_matrix_1_out_9, registers_to_matrix_1_out_11,
       registers_to_matrix_1_out_13, registers_to_matrix_1_out_17, registers_to_matrix_1_out_24;
  wire [12:0] registers_to_matrix_1_out_6, registers_to_matrix_1_out_8, registers_to_matrix_1_out_10,
       registers_to_matrix_1_out_12, registers_to_matrix_1_out_14, registers_to_matrix_1_out_16;
  wire [23:0] loading_Bot, loading_Bot_t;

  Button u_Start (.out(start));
  Button u_Reset (.out(reset));
  LED led_1 (.in(You_win));
  Hex_Digit_Display hex_digit_display_1 (.value(to_counter_1_out_2));  // open: dp
  to_counter to_counter_1 (
    .in_1(registers_to_matrix_1_white_count), .out_2(to_counter_1_out_2), .out_3(to_counter_1_out_3));
  DotMatrix #(.inputtype("row"), .matrixcols(12), .matrixrows(12)) dotmatrix_1 (
    .row0(registers_to_matrix_1_out_7), .row1(registers_to_matrix_1_out_7),
    .row2(registers_to_matrix_1_out_9), .row3(registers_to_matrix_1_out_9),
    .row4(registers_to_matrix_1_out_11), .row5(registers_to_matrix_1_out_11),
    .row6(registers_to_matrix_1_out_13), .row7(registers_to_matrix_1_out_13),
    .row8(registers_to_matrix_1_out_17), .row9(registers_to_matrix_1_out_17),
    .row10(registers_to_matrix_1_out_24), .row11(registers_to_matrix_1_out_24));
  DotMatrix #(.inputtype("row"), .matrixcols(13), .matrixrows(12)) dotmatrix_2 (
    .row0(registers_to_matrix_1_out_6), .row1(registers_to_matrix_1_out_6),
    .row2(registers_to_matrix_1_out_8), .row3(registers_to_matrix_1_out_8),
    .row4(registers_to_matrix_1_out_10), .row5(registers_to_matrix_1_out_10),
    .row6(registers_to_matrix_1_out_12), .row7(registers_to_matrix_1_out_12),
    .row8(registers_to_matrix_1_out_14), .row9(registers_to_matrix_1_out_14),
    .row10(registers_to_matrix_1_out_16), .row11(registers_to_matrix_1_out_16));
  grid grid_1 ();
  grid grid_2 ();
  grid grid_3 ();
  grid grid_4 ();
  grid grid_5 ();
  grid grid_6 ();
  registers_to_matrix registers_to_matrix_1 (
    .in_4(column), .out_6(registers_to_matrix_1_out_6), .out_8(registers_to_matrix_1_out_8),
    .out_10(registers_to_matrix_1_out_10), .in_5(row), .out_12(registers_to_matrix_1_out_12),
    .out_14(registers_to_matrix_1_out_14), .out_16(registers_to_matrix_1_out_16),
    .out_7(registers_to_matrix_1_out_7), .out_9(registers_to_matrix_1_out_9),
    .out_11(registers_to_matrix_1_out_11), .out_13(registers_to_matrix_1_out_13),
    .out_17(registers_to_matrix_1_out_17), .out_24(registers_to_matrix_1_out_24), .in_2(turn), .in_1(start),
    .white_count(registers_to_matrix_1_white_count), .in_3(reset), .out_15(can), .out_18(You_win),
    .out_19(Draw), .out_22(Bot_win__and_you_lose__if_you_don_t_understand), .out_23(game_over),
    .out_25(change_turn), .out_26(registers_to_matrix_1_out_26),
    .black_count(registers_to_matrix_1_black_count));
  progres_bar progres_bar_1 (.in_1(registers_to_matrix_1_out_26), .out_2(loading_Bot_t));
  Hex_Digit_Display hex_digit_display_2 (.value(to_counter_1_out_3));  // open: dp
  DotMatrix #(.inputtype("row"), .matrixcols(24), .matrixrows(1)) dotmatrix_3 (.row0(loading_Bot));
  LED led_2 (.in(Draw));
  Hex_Digit_Display hex_digit_display_3 (.value(to_counter_2_out_2));  // open: dp
  to_counter to_counter_2 (
    .in_1(registers_to_matrix_1_black_count), .out_2(to_counter_2_out_2), .out_3(to_counter_2_out_3));
  LED led_3 (.in(The_game_is_on_or_not));
  Button button_1 (.out(button_1_out));
  Button button_2 (.out(button_2_out));
  Button button_3 (.out(button_3_out));
  Button button_4 (.out(button_4_out));
  Button button_5 (.out(button_5_out));
  Button button_6 (.out(button_6_out));
  Button button_7 (.out(button_7_out));
  Button button_8 (.out(button_8_out));
  Button button_9 (.out(button_9_out));
  Button button_10 (.out(button_10_out));
  Button button_11 (.out(button_11_out));
  Button button_12 (.out(button_12_out));
  LED Your_move (.in(turnnoww));
  LED led_4 (.in(Bot_win__and_you_lose__if_you_don_t_understand));
  Hex_Digit_Display hex_digit_display_4 (.value(to_counter_2_out_3));  // open: dp
  Button button_13 (.out(button_13_out));
  Button button_14 (.out(button_14_out));
  Button button_15 (.out(button_15_out));
  buttons_row buttons_row_1 (
    .in_1(button_2_out), .in_2(button_1_out), .in_3(button_14_out), .in_4(button_16_out),
    .in_5(button_13_out), .in_6(button_15_out), .out_7(_0));
  Button button_16 (.out(button_16_out));
  Button button_17 (.out(button_17_out));
  Button button_18 (.out(button_18_out));
  buttons_row buttons_row_2 (
    .in_1(button_3_out), .in_2(button_4_out), .in_3(button_19_out), .in_4(button_17_out),
    .in_5(button_20_out), .in_6(button_18_out), .out_7(_1));
  Button button_19 (.out(button_19_out));
  Button button_20 (.out(button_20_out));
  Button button_21 (.out(button_21_out));
  Button button_22 (.out(button_22_out));
  Button button_23 (.out(button_23_out));
  Button button_24 (.out(button_24_out));
  buttons_row buttons_row_3 (
    .in_1(button_5_out), .in_2(button_6_out), .in_3(button_23_out), .in_4(button_22_out),
    .in_5(button_21_out), .in_6(button_24_out), .out_7(_2));
  Button button_25 (.out(button_25_out));
  Button button_26 (.out(button_26_out));
  buttons_row buttons_row_4 (
    .in_1(button_7_out), .in_2(button_8_out), .in_3(button_27_out), .in_4(button_28_out),
    .in_5(button_26_out), .in_6(button_25_out), .out_7(_3));
  Button button_27 (.out(button_27_out));
  Button button_28 (.out(button_28_out));
  Button button_29 (.out(button_29_out));
  Button button_30 (.out(button_30_out));
  buttons_row buttons_row_5 (
    .in_1(button_9_out), .in_2(button_10_out), .in_3(button_29_out), .in_4(button_32_out),
    .in_5(button_30_out), .in_6(button_31_out), .out_7(_4));
  Button button_31 (.out(button_31_out));
  Button button_32 (.out(button_32_out));
  buttons_row buttons_row_6 (
    .in_1(button_12_out), .in_2(button_11_out), .in_3(button_34_out), .in_4(button_36_out),
    .in_5(button_33_out), .in_6(button_35_out), .out_7(_5));
  Button button_33 (.out(button_33_out));
  Button button_34 (.out(button_34_out));
  Button button_35 (.out(button_35_out));
  Button button_36 (.out(button_36_out));
  LED The_bot_s_move (.in(turnnowb));
  and and_1 (turnnoww, not_1_out, The_game_is_on_or_not);
  not not_1 (not_1_out, turn);
  and and_2 (turnnowb, turn, The_game_is_on_or_not);
  baza baza_1 (
    .in_2(_0), .in_3(_1), .in_4(_2), .in_6(_3), .in_8(_4), .in_11(_5), .this_is_the_row_number(row),
    .this_is_the_column_number(column), .The_player_s_turn__When_zero_is_white_s_move(turn), .can(can),
    .reset(reset), .start(start), .out_13(The_game_is_on_or_not), .game_over(game_over), .in_5(change_turn));

  // Notes on the sheet:
  //   WHITE
  //   BLACK
endmodule

module baza (
  input  can,
  input  [5:0] in_2,
  input  [5:0] in_3,
  input  [5:0] in_4,
  input  in_5,
  input  [5:0] in_6,
  input  start,
  input  [5:0] in_8,
  input  game_over,
  input  reset,
  input  [5:0] in_11,
  output The_player_s_turn__When_zero_is_white_s_move,
  output out_13,
  output [2:0] this_is_the_row_number,
  output [5:0] this_is_the_column_number
);

  wire and_9_out, clock_1_out, clock_2_out, or_1_out, or_2_out, or_3_out, or_4_out, or_5_out, or_6_out,
       or_7_out, or_8_out, or_13_out, or_14_out, register_1_q;
  wire [2:0] row0, row1, row2, row3, row4, row5;
  wire [5:0] and_1_out, and_2_out, and_3_out, and_4_out, and_5_out, and_6_out, and_7_out, and_8_out,
       and_10_out, and_11_out, and_12_out, and_13_out, col0, col1, col2, col3, col4, col5;
  wire [5:5] not_1_out, not_2_out, not_3_out, not_4_out, not_5_out, not_6_out, or_9_out, or_10_out,
       or_11_out, or_12_out, or_19_out, or_20_out;

  or or_1 (or_1_out, in_2[0], in_2[1], in_2[2], in_2[3], in_2[4], in_2[5]);
  or or_2 (or_2_out, in_3[0], in_3[1], in_3[2], in_3[3], in_3[4], in_3[5]);
  or or_3 (or_3_out, in_8[0], in_8[1], in_8[2], in_8[3], in_8[4], in_8[5]);
  or or_4 (or_4_out, in_11[0], in_11[1], in_11[2], in_11[3], in_11[4], in_11[5]);
  if_3bit if_3bit_1 (.Input_0(3'b111), .sel(or_1_out), .Input_1(3'b000), .Output(row0));
  if_3bit if_3bit_2 (.Input_0(3'b111), .sel(or_2_out), .Input_1(3'b001), .Output(row1));
  if_3bit if_3bit_3 (.Input_0(3'b111), .sel(or_3_out), .Input_1(3'b100), .Output(row4));
  if_3bit if_3bit_4 (.Input_0(3'b111), .sel(or_4_out), .Input_1(3'b101), .Output(row5));
  Clock clock_1 (.out(clock_1_out));
  Register #(.width(1)) u_start (.D(start), .en(start), .Q(out_13), .clk(clock_1_out), .clr(or_5_out));
  or or_5 (or_5_out, game_over, reset);
  or or_6 (or_6_out, in_4[0], in_4[1], in_4[2], in_4[3], in_4[4], in_4[5]);
  or or_7 (or_7_out, in_6[0], in_6[1], in_6[2], in_6[3], in_6[4], in_6[5]);
  if_3bit if_3bit_5 (.Input_0(3'b111), .sel(or_6_out), .Input_1(3'b010), .Output(row2));
  if_3bit if_3bit_6 (.Input_0(3'b111), .sel(or_7_out), .Input_1(3'b011), .Output(row3));
  or or_8 (or_8_out, in_2[0], in_2[1], in_2[2], in_2[3], in_2[4], in_2[5], in_3[0], in_3[1], in_3[2], in_3[3], in_3[4], in_3[5], in_4[0], in_4[1], in_4[2], in_4[3], in_4[4], in_4[5], in_6[0], in_6[1], in_6[2], in_6[3], in_6[4], in_6[5], in_8[0], in_8[1], in_8[2], in_8[3], in_8[4], in_8[5], in_11[0], in_11[1]);
  not not_1 (not_1_out[5], or_9_out[5]);
  or or_9 (or_9_out[5], in_2[0], in_3[0], in_4[0], in_6[0], in_8[0], in_11[0]);
  not not_2 (not_2_out[5], or_10_out[5]);
  or or_10 (or_10_out[5], in_2[1], in_3[1], in_4[1], in_6[1], in_8[1], in_11[1]);
  not not_3 (not_3_out[5], or_11_out[5]);
  or or_11 (or_11_out[5], in_2[4], in_3[4], in_4[4], in_6[4], in_8[4], in_11[4]);
  not not_4 (not_4_out[5], or_12_out[5]);
  or or_12 (or_12_out[5], in_2[5], in_3[5], in_4[5], in_6[5], in_8[5], in_11[5]);
  or or_13 (or_13_out, or_8_out, in_11[2], in_11[3], in_11[4], in_11[5]);
  or or_14 (or_14_out, or_13_out, in_5);
  assign and_1_out = {6{1'b0}} & {6{not_1_out[5]}};  // AND_Gate and_1, 6 bits wide
  assign col0 = and_1_out | and_2_out;  // OR_Gate or_15, 6 bits wide
  assign and_2_out = {6{or_9_out[5]}} & 6'b000001;  // AND_Gate and_2, 6 bits wide
  assign and_3_out = {6{1'b0}} & {6{not_2_out[5]}};  // AND_Gate and_3, 6 bits wide
  assign col1 = and_3_out | and_4_out;  // OR_Gate or_16, 6 bits wide
  assign and_4_out = {6{or_10_out[5]}} & 6'b000010;  // AND_Gate and_4, 6 bits wide
  assign and_5_out = {6{1'b0}} & {6{not_3_out[5]}};  // AND_Gate and_5, 6 bits wide
  assign col4 = and_5_out | and_6_out;  // OR_Gate or_17, 6 bits wide
  assign and_6_out = {6{or_11_out[5]}} & 6'b010000;  // AND_Gate and_6, 6 bits wide
  assign and_7_out = {6{1'b0}} & {6{not_4_out[5]}};  // AND_Gate and_7, 6 bits wide
  assign col5 = and_7_out | and_8_out;  // OR_Gate or_18, 6 bits wide
  assign and_8_out = {6{or_12_out[5]}} & 6'b100000;  // AND_Gate and_8, 6 bits wide
  and and_9 (and_9_out, or_14_out, out_13);
  not not_5 (not_5_out[5], or_19_out[5]);
  or or_19 (or_19_out[5], in_2[2], in_3[2], in_4[2], in_6[2], in_8[2], in_11[2]);
  not not_6 (not_6_out[5], or_20_out[5]);
  or or_20 (or_20_out[5], in_2[3], in_3[3], in_4[3], in_6[3], in_8[3], in_11[3]);
  T_Flip_Flop t_ff_1 (
    .clk(and_9_out), .T(and_9_out), .Q(The_player_s_turn__When_zero_is_white_s_move), .reset(or_5_out));  // open: Qn, preset, en
  assign and_10_out = {6{1'b0}} & {6{not_5_out[5]}};  // AND_Gate and_10, 6 bits wide
  assign col2 = and_10_out | and_11_out;  // OR_Gate or_21, 6 bits wide
  assign and_11_out = {6{or_19_out[5]}} & 6'b000100;  // AND_Gate and_11, 6 bits wide
  assign and_12_out = {6{1'b0}} & {6{not_6_out[5]}};  // AND_Gate and_12, 6 bits wide
  assign col3 = and_12_out | and_13_out;  // OR_Gate or_22, 6 bits wide
  assign and_13_out = {6{or_20_out[5]}} & 6'b001000;  // AND_Gate and_13, 6 bits wide
  assign this_is_the_row_number = row0 & row1 & row2 & row3 & row4 & row5;  // AND_Gate and_14, 3 bits wide
  assign this_is_the_column_number = col0 | col1 | col2 | col3 | col4 | col5;  // OR_Gate or_23, 6 bits wide
  Pull_Resistor pull_resistor_1 (.node(can));
  Register #(.width(1)) register_1 (.D(can), .en(can), .Q(register_1_q), .clk(clock_2_out));  // open: clr
  Clock clock_2 (.out(clock_2_out));

  // Other names for the same wires on the sheet: game_play = out_13; _00 = in_2[0]; _10 = in_2[1]; _20 = in_2[2];
  //   _30 = in_2[3]; _40 = in_2[4]; _50 = in_2[5]; _01 = in_3[0]; _11 = in_3[1]; _21 = in_3[2]; _31 = in_3[3];
  //   _41 = in_3[4]; _51 = in_3[5]; _02 = in_4[0]; _12 = in_4[1]; _22 = in_4[2]; _32 = in_4[3]; _42 = in_4[4];
  //   _52 = in_4[5]; _03 = in_6[0]; _13 = in_6[1]; _23 = in_6[2]; _33 = in_6[3]; _43 = in_6[4]; _53 = in_6[5];
  //   _04 = in_8[0]; _14 = in_8[1]; _24 = in_8[2]; _34 = in_8[3]; _44 = in_8[4]; _54 = in_8[5]; _05 = in_11[0];
  //   _15 = in_11[1]; _25 = in_11[2]; _35 = in_11[3]; _45 = in_11[4]; _55 = in_11[5]
endmodule

module registers_to_matrix (
  input  in_1,
  input  in_2,
  input  in_3,
  input  [5:0] in_4,
  input  [2:0] in_5,
  output [12:0] out_6,
  output [11:0] out_7,
  output [12:0] out_8,
  output [11:0] out_9,
  output [12:0] out_10,
  output [11:0] out_11,
  output [12:0] out_12,
  output [11:0] out_13,
  output [12:0] out_14,
  output out_15,
  output [12:0] out_16,
  output [11:0] out_17,
  output out_18,
  output out_19,
  output [5:0] white_count,
  output [5:0] black_count,
  output out_22,
  output out_23,
  output [11:0] out_24,
  output out_25,
  output [5:0] out_26
);

  wire _1, _2, _3, _4, _5, _6, and_1_out, and_2_out, and_4_out, and_5_out, and_7_out, and_8_out, and_10_out,
       and_11_out, and_13_out, and_14_out, and_16_out, and_17_out, and_19_out, and_20_out, and_21_out,
       and_22_out, and_23_out, and_25_out, and_27_out, and_29_out, and_31_out, and_32_out, and_33_out,
       and_35_out, and_37_out, can_w1, can_w2, can_w3, can_w4, can_w5, can_w6, compare_6bit_1_out_3,
       compare_6bit_2_out_3, compare_6bit_3_out_3, compare_6bit_4_out_3, compare_6bit_5_out_3,
       compare_6bit_6_out_3, do_diag_coloring_1, do_diag_coloring_2, do_diag_coloring_3, do_diag_coloring_4,
       do_diag_coloring_5, do_diag_coloring_6, ld_diag, lu_diag, not_1_out, not_2_out, not_3_out, not_4_out,
       not_5_out, not_6_out, not_7_out, not_8_out, not_9_out, not_10_out, not_11_out, not_12_out, not_13_out,
       not_14_out, not_15_out, not_16_out, not_17_out, not_18_out, not_19_out, or_7_out, or_8_out, or_9_out,
       or_10_out, or_11_out, or_12_out, or_27_out, or_28_out, or_29_out, or_30_out, or_31_out, or_32_out,
       rd_diag, ru_diag, tic, zero_or_not_1_out_2, zero_or_not_2_out_2, zero_or_not_3_out_2,
       zero_or_not_4_out_2, zero_or_not_5_out_2, zero_or_not_6_out_2, zero_or_not_7_out_2,
       zero_or_not_8_out_2, zero_or_not_9_out_2, zero_or_not_10_out_2, zero_or_not_11_out_2,
       zero_or_not_12_out_2, zero_or_not_13_out_2, zero_or_not_14_out_2, zero_or_not_15_out_2,
       zero_or_not_16_out_2, zero_or_not_17_out_2, zero_or_not_18_out_2, zero_or_not_19_out_2,
       zero_or_not_20_out_2, zero_or_not_21_out_2, zero_or_not_22_out_2, zero_or_not_23_out_2,
       zero_or_not_24_out_2, zero_or_not_25_out_2;
  wire [5:0] after_ver_paint_b_1, after_ver_paint_b_2, after_ver_paint_b_3, after_ver_paint_b_4,
       after_ver_paint_b_5, after_ver_paint_b_6, after_ver_paint_w_1, after_ver_paint_w_2,
       after_ver_paint_w_3, after_ver_paint_w_4, after_ver_paint_w_5, after_ver_paint_w_6, and_3_out,
       and_6_out, and_9_out, and_12_out, and_15_out, and_18_out, and_24_out, and_26_out, and_28_out,
       and_30_out, and_34_out, and_36_out, black1_diag, black2_diag, black3_diag, black4_diag, black5_diag,
       black6_diag, black_col, coloring_black_hor, coloring_black_ver, coloring_white_hor,
       coloring_white_ver, do_res, down_ver1, down_ver2, down_ver3, down_ver4, down_ver5, down_ver6, ld_max,
       left_hor1, left_hor2, left_hor3, left_hor4, left_hor5, left_hor6, lu_max, now_row, or_1_out, or_2_out,
       or_3_out, or_4_out, or_5_out, or_6_out, or_14_out, or_15_out, or_16_out, or_17_out, or_18_out,
       or_19_out, or_20_out, or_21_out, or_22_out, or_23_out, or_24_out, or_25_out, or_26_out, out_b_1,
       out_b_2, out_b_3, out_b_4, out_b_5, out_b_6, out_w_1, out_w_2, out_w_3, out_w_4, out_w_5, out_w_6,
       pull_resistor_2_node, pull_resistor_3_node, pull_resistor_4_node, pull_resistor_5_node,
       pull_resistor_7_node, pull_resistor_8_node, pull_resistor_9_node, pull_resistor_17_node,
       pull_resistor_19_node, pull_resistor_20_node, pull_resistor_24_node, pull_resistor_25_node,
       pull_resistor_26_node, pull_resistor_27_node, pull_resistor_28_node, pull_resistor_29_node,
       pull_resistor_33_node, pull_resistor_35_node, pull_resistor_36_node, pull_resistor_39_node,
       pull_resistor_40_node, pull_resistor_46_node, pull_resistor_52_node, rd_max, right_hor1, right_hor2,
       right_hor3, right_hor4, right_hor5, right_hor6, ru_max, transistor_4_out, transistor_6_out,
       transistor_8_out, transistor_9_out, transistor_13_out, transistor_14_out, transistor_15_out,
       transistor_16_out, transistor_17_out, transistor_19_out, transistor_21_out, transistor_22_out,
       transistor_25_out, transistor_28_out, transistor_29_out, transistor_30_out, transistor_32_out,
       transistor_35_out, transistor_36_out, transistor_37_out, transistor_44_out, transistor_46_out,
       transistor_49_out, transistor_50_out, transistor_53_out, transistor_54_out, transistor_55_out,
       transistor_56_out, transistor_57_out, transistor_58_out, transistor_59_out, transistor_60_out,
       transistor_62_out, transistor_63_out, transistor_64_out, transistor_66_out, transistor_67_out,
       transistor_68_out, transistor_70_out, transistor_72_out, transistor_74_out, transistor_76_out,
       transistor_78_out, up_ver1, up_ver2, up_ver3, up_ver4, up_ver5, up_ver6, white1_diag, white2_diag,
       white3_diag, white4_diag, white5_diag, white6_diag, white_col;

  Clock clock_1 (.out(tic));
  Demultiplexer #(.select(3)) demultiplexer_1 (
    .out0(_1), .out1(_2), .out2(_3), .out3(_4), .out4(_5), .out5(_6), .in(1'b1), .sel(in_5));  // open: out6, out7, en
  Pull_Resistor #(.pull(1)) pull_resistor_1 (.node(do_res));
  Transistor #(.\type ("n"), .gate("br"), .width(6)) transistor_1 (.in({6{1'b0}}), .out(do_res), .gate(in_3));
  Multiplexer #(.select(3), .width(6)) multiplexer_1 (
    .in0(6'b000001), .in1(6'b000010), .in2(6'b000100), .in3(6'b001000), .in4(6'b010000), .in5(6'b100000),
    .in7({6{1'b0}}), .out(now_row), .sel(in_5));  // open: in6, en
  check_diag_lu check_diag_lu_1 (
    .in_1({out_6[11], out_6[9], out_6[7], out_6[5], out_6[3], out_6[1]}),
    .in_2({out_7[11], out_7[9], out_7[7], out_7[5], out_7[3], out_7[1]}),
    .in_3({out_8[11], out_8[9], out_8[7], out_8[5], out_8[3], out_8[1]}),
    .in_4({out_9[11], out_9[9], out_9[7], out_9[5], out_9[3], out_9[1]}),
    .in_5({out_10[11], out_10[9], out_10[7], out_10[5], out_10[3], out_10[1]}),
    .in_6({out_11[11], out_11[9], out_11[7], out_11[5], out_11[3], out_11[1]}),
    .in_7({out_12[11], out_12[9], out_12[7], out_12[5], out_12[3], out_12[1]}),
    .in_8({out_13[11], out_13[9], out_13[7], out_13[5], out_13[3], out_13[1]}),
    .in_9({out_14[11], out_14[9], out_14[7], out_14[5], out_14[3], out_14[1]}),
    .in_10({out_17[11], out_17[9], out_17[7], out_17[5], out_17[3], out_17[1]}),
    .in_11({out_16[11], out_16[9], out_16[7], out_16[5], out_16[3], out_16[1]}),
    .in_12({out_24[11], out_24[9], out_24[7], out_24[5], out_24[3], out_24[1]}), .column(in_4),
    .row(now_row), .out_15(lu_diag), .out_col(lu_max));
  check_diag_ld check_diag_ld_1 (
    .in_1({out_6[11], out_6[9], out_6[7], out_6[5], out_6[3], out_6[1]}),
    .in_2({out_7[11], out_7[9], out_7[7], out_7[5], out_7[3], out_7[1]}),
    .in_3({out_8[11], out_8[9], out_8[7], out_8[5], out_8[3], out_8[1]}),
    .in_4({out_9[11], out_9[9], out_9[7], out_9[5], out_9[3], out_9[1]}),
    .in_5({out_10[11], out_10[9], out_10[7], out_10[5], out_10[3], out_10[1]}),
    .in_6({out_11[11], out_11[9], out_11[7], out_11[5], out_11[3], out_11[1]}),
    .in_7({out_12[11], out_12[9], out_12[7], out_12[5], out_12[3], out_12[1]}),
    .in_8({out_13[11], out_13[9], out_13[7], out_13[5], out_13[3], out_13[1]}),
    .in_9({out_14[11], out_14[9], out_14[7], out_14[5], out_14[3], out_14[1]}),
    .in_10({out_17[11], out_17[9], out_17[7], out_17[5], out_17[3], out_17[1]}),
    .in_11({out_16[11], out_16[9], out_16[7], out_16[5], out_16[3], out_16[1]}),
    .in_12({out_24[11], out_24[9], out_24[7], out_24[5], out_24[3], out_24[1]}), .column(in_4),
    .row(now_row), .out_15(ld_diag), .out_col(ld_max));
  Pull_Resistor pull_resistor_2 (.node(pull_resistor_2_node));
  Transistor #(.\type ("n"), .width(6)) transistor_2 (
    .in(coloring_white_hor), .out(pull_resistor_2_node), .gate(can_w4));
  Pull_Resistor pull_resistor_3 (.node(pull_resistor_3_node));
  Transistor #(.\type ("n"), .width(6)) transistor_3 (.in(in_4), .out(pull_resistor_3_node), .gate(can_w4));
  Transistor #(.\type ("n"), .width(6)) transistor_4 (.in(coloring_white_hor), .out(transistor_4_out), .gate(can_w5));
  Pull_Resistor pull_resistor_4 (.node(pull_resistor_4_node));
  Transistor #(.\type ("n"), .width(6)) transistor_5 (.in(in_4), .out(pull_resistor_4_node), .gate(can_w5));
  Transistor #(.\type ("n"), .width(6)) transistor_6 (.in(coloring_white_hor), .out(transistor_6_out), .gate(can_w6));
  Pull_Resistor pull_resistor_5 (.node(pull_resistor_5_node));
  Transistor #(.\type ("n"), .width(6)) transistor_7 (.in(in_4), .out(pull_resistor_5_node), .gate(can_w1));
  Transistor #(.\type ("n"), .width(6)) transistor_8 (.in(coloring_white_hor), .out(transistor_8_out), .gate(can_w2));
  Transistor #(.\type ("n"), .width(6)) transistor_9 (.in(6'b001000), .out(transistor_9_out), .gate(in_1));
  Pull_Resistor pull_resistor_6 (.node(transistor_9_out));
  Pull_Resistor pull_resistor_7 (.node(pull_resistor_7_node));
  Transistor #(.\type ("n"), .width(6)) transistor_10 (.in(in_4), .out(pull_resistor_7_node), .gate(can_w3));
  Pull_Resistor pull_resistor_8 (.node(pull_resistor_8_node));
  Transistor #(.\type ("n"), .width(6)) transistor_11 (
    .in(coloring_white_hor), .out(pull_resistor_8_node), .gate(can_w3));
  Pull_Resistor pull_resistor_9 (.node(pull_resistor_9_node));
  Transistor #(.\type ("n"), .width(6)) transistor_12 (.in(6'b000100), .out(pull_resistor_9_node), .gate(in_1));
  assign or_1_out = {out_12[11], out_12[9], out_12[7], out_12[5], out_12[3], out_12[1]} | pull_resistor_9_node | white4_diag | pull_resistor_2_node | pull_resistor_3_node | after_ver_paint_w_4;  // OR_Gate or_1, 6 bits wide
  Pull_Resistor pull_resistor_10 (.node(transistor_4_out));
  assign or_2_out = {out_14[11], out_14[9], out_14[7], out_14[5], out_14[3], out_14[1]} | transistor_4_out | white5_diag | after_ver_paint_w_5 | pull_resistor_4_node;  // OR_Gate or_2, 6 bits wide
  Pull_Resistor pull_resistor_11 (.node(transistor_6_out));
  assign or_3_out = {out_16[11], out_16[9], out_16[7], out_16[5], out_16[3], out_16[1]} | transistor_6_out | white6_diag | after_ver_paint_w_6 | transistor_13_out;  // OR_Gate or_3, 6 bits wide
  Transistor #(.\type ("n"), .width(6)) transistor_13 (.in(in_4), .out(transistor_13_out), .gate(can_w6));
  Pull_Resistor pull_resistor_12 (.node(transistor_13_out));
  BitAdder #(.width(6)) bitadder_1 (
    .in0({out_6[11], out_6[9], out_6[7], out_6[5], out_6[3], out_6[1]}),
    .in1({out_8[11], out_8[9], out_8[7], out_8[5], out_8[3], out_8[1]}),
    .in2({out_10[11], out_10[9], out_10[7], out_10[5], out_10[3], out_10[1]}),
    .in3({out_12[11], out_12[9], out_12[7], out_12[5], out_12[3], out_12[1]}),
    .in4({out_14[11], out_14[9], out_14[7], out_14[5], out_14[3], out_14[1]}),
    .in5({out_16[11], out_16[9], out_16[7], out_16[5], out_16[3], out_16[1]}), .out(white_count));
  check_diag_ru check_diag_ru_1 (
    .in_1({out_6[11], out_6[9], out_6[7], out_6[5], out_6[3], out_6[1]}),
    .in_2({out_7[11], out_7[9], out_7[7], out_7[5], out_7[3], out_7[1]}),
    .in_3({out_8[11], out_8[9], out_8[7], out_8[5], out_8[3], out_8[1]}),
    .in_4({out_9[11], out_9[9], out_9[7], out_9[5], out_9[3], out_9[1]}),
    .in_5({out_10[11], out_10[9], out_10[7], out_10[5], out_10[3], out_10[1]}),
    .in_6({out_11[11], out_11[9], out_11[7], out_11[5], out_11[3], out_11[1]}),
    .in_7({out_12[11], out_12[9], out_12[7], out_12[5], out_12[3], out_12[1]}),
    .in_8({out_13[11], out_13[9], out_13[7], out_13[5], out_13[3], out_13[1]}),
    .in_9({out_14[11], out_14[9], out_14[7], out_14[5], out_14[3], out_14[1]}),
    .in_10({out_17[11], out_17[9], out_17[7], out_17[5], out_17[3], out_17[1]}),
    .in_11({out_16[11], out_16[9], out_16[7], out_16[5], out_16[3], out_16[1]}),
    .in_12({out_24[11], out_24[9], out_24[7], out_24[5], out_24[3], out_24[1]}), .column(in_4),
    .row(now_row), .out_15(ru_diag), .out_col(ru_max));
  check_diag_rd check_diag_rd_1 (
    .in_1({out_6[11], out_6[9], out_6[7], out_6[5], out_6[3], out_6[1]}),
    .in_2({out_7[11], out_7[9], out_7[7], out_7[5], out_7[3], out_7[1]}),
    .in_3({out_8[11], out_8[9], out_8[7], out_8[5], out_8[3], out_8[1]}),
    .in_4({out_9[11], out_9[9], out_9[7], out_9[5], out_9[3], out_9[1]}),
    .in_5({out_10[11], out_10[9], out_10[7], out_10[5], out_10[3], out_10[1]}),
    .in_6({out_11[11], out_11[9], out_11[7], out_11[5], out_11[3], out_11[1]}),
    .in_7({out_12[11], out_12[9], out_12[7], out_12[5], out_12[3], out_12[1]}),
    .in_8({out_13[11], out_13[9], out_13[7], out_13[5], out_13[3], out_13[1]}),
    .in_9({out_14[11], out_14[9], out_14[7], out_14[5], out_14[3], out_14[1]}),
    .in_10({out_17[11], out_17[9], out_17[7], out_17[5], out_17[3], out_17[1]}),
    .in_11({out_16[11], out_16[9], out_16[7], out_16[5], out_16[3], out_16[1]}),
    .in_12({out_24[11], out_24[9], out_24[7], out_24[5], out_24[3], out_24[1]}), .column(in_4),
    .row(now_row), .out_15(rd_diag), .out_col(rd_max));
  Transistor #(.\type ("n"), .width(6)) transistor_14 (.in(coloring_white_hor), .out(transistor_14_out), .gate(can_w1));
  Pull_Resistor pull_resistor_13 (.node(transistor_14_out));
  Pull_Resistor pull_resistor_14 (.node(transistor_8_out));
  assign or_4_out = {out_8[11], out_8[9], out_8[7], out_8[5], out_8[3], out_8[1]} | transistor_8_out | white2_diag | after_ver_paint_w_2 | transistor_15_out;  // OR_Gate or_4, 6 bits wide
  Transistor #(.\type ("n"), .width(6)) transistor_15 (.in(in_4), .out(transistor_15_out), .gate(can_w2));
  Pull_Resistor pull_resistor_15 (.node(transistor_15_out));
  assign or_5_out = {out_10[11], out_10[9], out_10[7], out_10[5], out_10[3], out_10[1]} | transistor_9_out | after_ver_paint_w_3 | white3_diag | pull_resistor_7_node | pull_resistor_8_node;  // OR_Gate or_5, 6 bits wide
  zero_or_not zero_or_not_1 (.in_1(white4_diag), .out_2(zero_or_not_1_out_2));
  zero_or_not zero_or_not_2 (.in_1(after_ver_paint_w_4), .out_2(zero_or_not_2_out_2));
  zero_or_not zero_or_not_3 (.in_1(white5_diag), .out_2(zero_or_not_3_out_2));
  zero_or_not zero_or_not_4 (.in_1(after_ver_paint_w_5), .out_2(zero_or_not_4_out_2));
  zero_or_not zero_or_not_5 (.in_1(white6_diag), .out_2(zero_or_not_5_out_2));
  and and_1 (and_1_out, zero_or_not_5_out_2, out_15);
  zero_or_not zero_or_not_6 (.in_1(after_ver_paint_w_6), .out_2(zero_or_not_6_out_2));
  and and_2 (and_2_out, zero_or_not_6_out_2, out_15);
  column_to_row column_to_row_1 (
    .in_5(in_4), .in_1({out_6[11], out_6[9], out_6[7], out_6[5], out_6[3], out_6[1]}),
    .in_2({out_8[11], out_8[9], out_8[7], out_8[5], out_8[3], out_8[1]}),
    .in_3({out_10[11], out_10[9], out_10[7], out_10[5], out_10[3], out_10[1]}),
    .in_4({out_12[11], out_12[9], out_12[7], out_12[5], out_12[3], out_12[1]}),
    .in_6({out_14[11], out_14[9], out_14[7], out_14[5], out_14[3], out_14[1]}),
    .in_7({out_16[11], out_16[9], out_16[7], out_16[5], out_16[3], out_16[1]}), .out_8(white_col));
  assign or_6_out = {out_6[11], out_6[9], out_6[7], out_6[5], out_6[3], out_6[1]} | transistor_14_out | white1_diag | after_ver_paint_w_1 | pull_resistor_5_node;  // OR_Gate or_6, 6 bits wide
  zero_or_not zero_or_not_7 (.in_1(white1_diag), .out_2(zero_or_not_7_out_2));
  zero_or_not zero_or_not_8 (.in_1(white2_diag), .out_2(zero_or_not_8_out_2));
  zero_or_not zero_or_not_9 (.in_1(white3_diag), .out_2(zero_or_not_9_out_2));
  zero_or_not zero_or_not_10 (.in_1(after_ver_paint_w_3), .out_2(zero_or_not_10_out_2));
  assign and_3_out = or_1_out & do_res;  // AND_Gate and_3, 6 bits wide
  and and_4 (and_4_out, zero_or_not_1_out_2, out_15);
  and and_5 (and_5_out, zero_or_not_2_out_2, out_15);
  assign and_6_out = or_2_out & do_res;  // AND_Gate and_6, 6 bits wide
  and and_7 (and_7_out, zero_or_not_3_out_2, out_15);
  or or_7 (or_7_out, can_w5, and_7_out, out_25, and_8_out);
  and and_8 (and_8_out, zero_or_not_4_out_2, out_15);
  assign and_9_out = or_3_out & do_res;  // AND_Gate and_9, 6 bits wide
  or or_8 (or_8_out, can_w6, and_1_out, out_25, and_2_out);
  can_put can_put_1 (
    .in_1(in_4), .in_2({out_6[11], out_6[9], out_6[7], out_6[5], out_6[3], out_6[1]}),
    .in_3({out_7[11], out_7[9], out_7[7], out_7[5], out_7[3], out_7[1]}), .in_4(black_col), .in_5(white_col),
    .in_6(lu_diag), .in_7(ru_diag), .in_8(now_row), .in_9(ld_diag), .in_10(rd_diag), .in_11(in_1),
    .in_12(in_2), .in_13(_1), .in_14(in_3), .left_hor(left_hor1), .out_16(can_w1), .rigth_hor(right_hor1),
    .down_ver(down_ver1), .up_ver(up_ver1));
  can_put can_put_2 (
    .in_1(in_4), .in_2({out_8[11], out_8[9], out_8[7], out_8[5], out_8[3], out_8[1]}),
    .in_3({out_9[11], out_9[9], out_9[7], out_9[5], out_9[3], out_9[1]}), .in_4(black_col), .in_5(white_col),
    .in_6(lu_diag), .in_7(ru_diag), .in_8(now_row), .in_9(ld_diag), .in_10(rd_diag), .in_11(in_1),
    .in_12(in_2), .in_13(_2), .in_14(in_3), .left_hor(left_hor2), .out_16(can_w2), .rigth_hor(right_hor2),
    .down_ver(down_ver2), .up_ver(up_ver2));
  and and_10 (and_10_out, zero_or_not_7_out_2, out_15);
  zero_or_not zero_or_not_11 (.in_1(after_ver_paint_w_1), .out_2(zero_or_not_11_out_2));
  and and_11 (and_11_out, zero_or_not_11_out_2, out_15);
  assign and_12_out = or_4_out & do_res;  // AND_Gate and_12, 6 bits wide
  and and_13 (and_13_out, zero_or_not_8_out_2, out_15);
  zero_or_not zero_or_not_12 (.in_1(after_ver_paint_w_2), .out_2(zero_or_not_12_out_2));
  and and_14 (and_14_out, zero_or_not_12_out_2, out_15);
  assign and_15_out = or_5_out & do_res;  // AND_Gate and_15, 6 bits wide
  and and_16 (and_16_out, zero_or_not_9_out_2, out_15);
  and and_17 (and_17_out, zero_or_not_10_out_2, out_15);
  Transistor #(.width(6)) transistor_16 (.in(and_3_out), .out(transistor_16_out), .gate(out_25));
  or or_9 (or_9_out, can_w4, and_4_out, out_25, and_5_out);
  Transistor #(.width(6)) transistor_17 (.in(and_6_out), .out(transistor_17_out), .gate(out_25));
  Transistor #(.\type ("n"), .gate("br"), .width(6)) transistor_18 (
    .in(out_w_5), .out(transistor_17_out), .gate(out_25));
  Transistor #(.width(6)) transistor_19 (.in(and_9_out), .out(transistor_19_out), .gate(out_25));
  Register #(.width(6)) register_1 (
    .D(transistor_19_out), .en(or_8_out),
    .Q({out_16[11], out_16[9], out_16[7], out_16[5], out_16[3], out_16[1]}), .clk(tic));  // open: clr
  Transistor #(.\type ("n"), .gate("br"), .width(6)) transistor_20 (
    .in(out_w_6), .out(transistor_19_out), .gate(out_25));
  column_to_row column_to_row_2 (
    .in_5(in_4), .in_1({out_7[11], out_7[9], out_7[7], out_7[5], out_7[3], out_7[1]}),
    .in_2({out_9[11], out_9[9], out_9[7], out_9[5], out_9[3], out_9[1]}),
    .in_3({out_11[11], out_11[9], out_11[7], out_11[5], out_11[3], out_11[1]}),
    .in_4({out_13[11], out_13[9], out_13[7], out_13[5], out_13[3], out_13[1]}),
    .in_6({out_17[11], out_17[9], out_17[7], out_17[5], out_17[3], out_17[1]}),
    .in_7({out_24[11], out_24[9], out_24[7], out_24[5], out_24[3], out_24[1]}), .out_8(black_col));
  BitAdder #(.width(6)) bitadder_2 (
    .in0({out_7[11], out_7[9], out_7[7], out_7[5], out_7[3], out_7[1]}),
    .in1({out_9[11], out_9[9], out_9[7], out_9[5], out_9[3], out_9[1]}),
    .in2({out_11[11], out_11[9], out_11[7], out_11[5], out_11[3], out_11[1]}),
    .in3({out_13[11], out_13[9], out_13[7], out_13[5], out_13[3], out_13[1]}),
    .in4({out_17[11], out_17[9], out_17[7], out_17[5], out_17[3], out_17[1]}),
    .in5({out_24[11], out_24[9], out_24[7], out_24[5], out_24[3], out_24[1]}), .out(black_count));
  can_put can_put_3 (
    .in_1(in_4), .in_2({out_10[11], out_10[9], out_10[7], out_10[5], out_10[3], out_10[1]}),
    .in_3({out_11[11], out_11[9], out_11[7], out_11[5], out_11[3], out_11[1]}), .in_4(black_col),
    .in_5(white_col), .in_6(lu_diag), .in_7(ru_diag), .in_8(now_row), .in_9(ld_diag), .in_10(rd_diag),
    .in_11(in_1), .in_12(in_2), .in_13(_3), .in_14(in_3), .left_hor(left_hor3), .out_16(can_w3),
    .rigth_hor(right_hor3), .down_ver(down_ver3), .up_ver(up_ver3));
  can_put can_put_4 (
    .in_1(in_4), .in_2({out_12[11], out_12[9], out_12[7], out_12[5], out_12[3], out_12[1]}),
    .in_3({out_13[11], out_13[9], out_13[7], out_13[5], out_13[3], out_13[1]}), .in_4(black_col),
    .in_5(white_col), .in_6(lu_diag), .in_7(ru_diag), .in_8(now_row), .in_9(ld_diag), .in_10(rd_diag),
    .in_11(in_1), .in_12(in_2), .in_13(_4), .in_14(in_3), .left_hor(left_hor4), .out_16(can_w4),
    .rigth_hor(right_hor4), .down_ver(down_ver4), .up_ver(up_ver4));
  assign and_18_out = or_6_out & do_res;  // AND_Gate and_18, 6 bits wide
  or or_10 (or_10_out, can_w1, and_10_out, out_25, and_11_out);
  Transistor #(.width(6)) transistor_21 (.in(and_12_out), .out(transistor_21_out), .gate(out_25));
  or or_11 (or_11_out, can_w2, and_13_out, out_25, and_14_out);
  Transistor #(.width(6)) transistor_22 (.in(and_15_out), .out(transistor_22_out), .gate(out_25));
  Transistor #(.\type ("n"), .gate("br"), .width(6)) transistor_23 (
    .in(out_w_3), .out(transistor_22_out), .gate(out_25));
  or or_12 (or_12_out, can_w3, and_16_out, out_25, and_17_out);
  Register #(.width(6)) register_2 (
    .D(transistor_16_out), .en(or_9_out),
    .Q({out_12[11], out_12[9], out_12[7], out_12[5], out_12[3], out_12[1]}), .clk(tic));  // open: clr
  Transistor #(.\type ("n"), .gate("br"), .width(6)) transistor_24 (
    .in(out_w_4), .out(transistor_16_out), .gate(out_25));
  Register #(.width(6)) register_3 (
    .D(transistor_17_out), .en(or_7_out),
    .Q({out_14[11], out_14[9], out_14[7], out_14[5], out_14[3], out_14[1]}), .clk(tic));  // open: clr
  Transistor #(.width(6)) transistor_25 (.in(and_18_out), .out(transistor_25_out), .gate(out_25));
  Transistor #(.\type ("n"), .gate("br"), .width(6)) transistor_26 (
    .in(out_w_1), .out(transistor_25_out), .gate(out_25));
  Register #(.width(6)) register_4 (
    .D(transistor_25_out), .en(or_10_out), .Q({out_6[11], out_6[9], out_6[7], out_6[5], out_6[3], out_6[1]}),
    .clk(tic));  // open: clr
  Register #(.width(6)) register_5 (
    .D(transistor_21_out), .en(or_11_out), .Q({out_8[11], out_8[9], out_8[7], out_8[5], out_8[3], out_8[1]}),
    .clk(tic));  // open: clr
  Transistor #(.\type ("n"), .gate("br"), .width(6)) transistor_27 (
    .in(out_w_2), .out(transistor_21_out), .gate(out_25));
  Register #(.width(6)) register_6 (
    .D(transistor_22_out), .en(or_12_out),
    .Q({out_10[11], out_10[9], out_10[7], out_10[5], out_10[3], out_10[1]}), .clk(tic));  // open: clr
  game_over game_over_1 (
    .in_1(white_count), .in_2(black_count), .white_win(out_18), .draw(out_19), .black_win(out_22),
    .game_over(out_23));
  can_put can_put_5 (
    .in_1(in_4), .in_2({out_14[11], out_14[9], out_14[7], out_14[5], out_14[3], out_14[1]}),
    .in_3({out_17[11], out_17[9], out_17[7], out_17[5], out_17[3], out_17[1]}), .in_4(black_col),
    .in_5(white_col), .in_6(lu_diag), .in_7(ru_diag), .in_8(now_row), .in_9(ld_diag), .in_10(rd_diag),
    .in_11(in_1), .in_12(in_2), .in_13(_5), .in_14(in_3), .left_hor(left_hor5), .out_16(can_w5),
    .rigth_hor(right_hor5), .down_ver(down_ver5), .up_ver(up_ver5));
  can_put can_put_6 (
    .in_1(in_4), .in_2({out_16[11], out_16[9], out_16[7], out_16[5], out_16[3], out_16[1]}),
    .in_3({out_24[11], out_24[9], out_24[7], out_24[5], out_24[3], out_24[1]}), .in_4(black_col),
    .in_5(white_col), .in_6(lu_diag), .in_7(ru_diag), .in_8(now_row), .in_9(ld_diag), .in_10(rd_diag),
    .in_11(in_1), .in_12(in_2), .in_13(_6), .in_14(in_3), .left_hor(left_hor6), .out_16(can_w6),
    .rigth_hor(right_hor6), .down_ver(down_ver6), .up_ver(up_ver6));
  Transistor #(.\type ("n"), .gate("br"), .width(6)) transistor_28 (.in(left_hor1), .out(transistor_28_out), .gate(_1));
  Transistor #(.\type ("n"), .gate("br"), .width(6)) transistor_29 (.in(left_hor2), .out(transistor_29_out), .gate(_2));
  Transistor #(.\type ("n"), .gate("br"), .width(6)) transistor_30 (
    .in(right_hor1), .out(transistor_30_out), .gate(_1));
  Pull_Resistor pull_resistor_16 (.node(transistor_30_out));
  Pull_Resistor pull_resistor_17 (.node(pull_resistor_17_node));
  Transistor #(.\type ("n"), .gate("br"), .width(6)) transistor_31 (
    .in(right_hor2), .out(pull_resistor_17_node), .gate(_2));
  Transistor #(.\type ("n"), .gate("br"), .width(6)) transistor_32 (
    .in(right_hor3), .out(transistor_32_out), .gate(_3));
  Pull_Resistor pull_resistor_18 (.node(transistor_32_out));
  Pull_Resistor pull_resistor_19 (.node(pull_resistor_19_node));
  Transistor #(.\type ("n"), .width(6)) transistor_33 (
    .in({out_6[11], out_6[9], out_6[7], out_6[5], out_6[3], out_6[1]}), .out(pull_resistor_19_node), .gate(_1));
  Pull_Resistor pull_resistor_20 (.node(pull_resistor_20_node));
  Transistor #(.\type ("n"), .gate("br"), .width(6)) transistor_34 (
    .in({out_7[11], out_7[9], out_7[7], out_7[5], out_7[3], out_7[1]}), .out(pull_resistor_20_node), .gate(_1));
  Transistor #(.\type ("n"), .width(6)) transistor_35 (
    .in({out_8[11], out_8[9], out_8[7], out_8[5], out_8[3], out_8[1]}), .out(transistor_35_out), .gate(_2));
  Pull_Resistor pull_resistor_21 (.node(transistor_35_out));
  Transistor #(.\type ("n"), .gate("br"), .width(6)) transistor_36 (
    .in({out_9[11], out_9[9], out_9[7], out_9[5], out_9[3], out_9[1]}), .out(transistor_36_out), .gate(_2));
  Pull_Resistor pull_resistor_22 (.node(transistor_36_out));
  Transistor #(.\type ("n"), .width(6)) transistor_37 (
    .in({out_10[11], out_10[9], out_10[7], out_10[5], out_10[3], out_10[1]}), .out(transistor_37_out),
    .gate(_3));
  Pull_Resistor pull_resistor_23 (.node(transistor_37_out));
  Pull_Resistor pull_resistor_24 (.node(pull_resistor_24_node));
  Transistor #(.\type ("n"), .gate("br"), .width(6)) transistor_38 (
    .in({out_11[11], out_11[9], out_11[7], out_11[5], out_11[3], out_11[1]}), .out(pull_resistor_24_node),
    .gate(_3));
  Pull_Resistor pull_resistor_25 (.node(pull_resistor_25_node));
  Transistor #(.\type ("n"), .width(6)) transistor_39 (
    .in({out_12[11], out_12[9], out_12[7], out_12[5], out_12[3], out_12[1]}), .out(pull_resistor_25_node),
    .gate(_4));
  Pull_Resistor pull_resistor_26 (.node(pull_resistor_26_node));
  Transistor #(.\type ("n"), .gate("br"), .width(6)) transistor_40 (
    .in({out_13[11], out_13[9], out_13[7], out_13[5], out_13[3], out_13[1]}), .out(pull_resistor_26_node),
    .gate(_4));
  Pull_Resistor pull_resistor_27 (.node(pull_resistor_27_node));
  Transistor #(.\type ("n"), .width(6)) transistor_41 (
    .in({out_14[11], out_14[9], out_14[7], out_14[5], out_14[3], out_14[1]}), .out(pull_resistor_27_node),
    .gate(_5));
  Pull_Resistor pull_resistor_28 (.node(pull_resistor_28_node));
  Transistor #(.\type ("n"), .gate("br"), .width(6)) transistor_42 (
    .in({out_17[11], out_17[9], out_17[7], out_17[5], out_17[3], out_17[1]}), .out(pull_resistor_28_node),
    .gate(_5));
  Pull_Resistor pull_resistor_29 (.node(pull_resistor_29_node));
  Transistor #(.\type ("n"), .width(6)) transistor_43 (
    .in({out_16[11], out_16[9], out_16[7], out_16[5], out_16[3], out_16[1]}), .out(pull_resistor_29_node),
    .gate(_6));
  Transistor #(.\type ("n"), .gate("br"), .width(6)) transistor_44 (
    .in({out_24[11], out_24[9], out_24[7], out_24[5], out_24[3], out_24[1]}), .out(transistor_44_out),
    .gate(_6));
  Pull_Resistor pull_resistor_30 (.node(transistor_44_out));
  or or_13 (out_15, can_w1, can_w2, can_w3, can_w4, can_w5, can_w6);
  Pull_Resistor pull_resistor_31 (.node(transistor_28_out));
  Pull_Resistor pull_resistor_32 (.node(transistor_29_out));
  Pull_Resistor pull_resistor_33 (.node(pull_resistor_33_node));
  Transistor #(.\type ("n"), .gate("br"), .width(6)) transistor_45 (
    .in(left_hor3), .out(pull_resistor_33_node), .gate(_3));
  Transistor #(.\type ("n"), .gate("br"), .width(6)) transistor_46 (.in(left_hor4), .out(transistor_46_out), .gate(_4));
  Pull_Resistor pull_resistor_34 (.node(transistor_46_out));
  Pull_Resistor pull_resistor_35 (.node(pull_resistor_35_node));
  Transistor #(.\type ("n"), .gate("br"), .width(6)) transistor_47 (
    .in(left_hor5), .out(pull_resistor_35_node), .gate(_5));
  Pull_Resistor pull_resistor_36 (.node(pull_resistor_36_node));
  Transistor #(.\type ("n"), .gate("br"), .width(6)) transistor_48 (
    .in(left_hor6), .out(pull_resistor_36_node), .gate(_6));
  Transistor #(.\type ("n"), .gate("br"), .width(6)) transistor_49 (
    .in(right_hor4), .out(transistor_49_out), .gate(_4));
  Pull_Resistor pull_resistor_37 (.node(transistor_49_out));
  Transistor #(.\type ("n"), .gate("br"), .width(6)) transistor_50 (
    .in(right_hor5), .out(transistor_50_out), .gate(_5));
  Pull_Resistor pull_resistor_38 (.node(transistor_50_out));
  Pull_Resistor pull_resistor_39 (.node(pull_resistor_39_node));
  Transistor #(.\type ("n"), .gate("br"), .width(6)) transistor_51 (
    .in(right_hor6), .out(pull_resistor_39_node), .gate(_6));
  assign or_14_out = left_hor3 | right_hor3;  // OR_Gate or_14, 6 bits wide
  assign or_15_out = transistor_28_out | transistor_29_out | pull_resistor_33_node | transistor_46_out | pull_resistor_35_node | pull_resistor_36_node;  // OR_Gate or_15, 6 bits wide
  assign or_16_out = transistor_30_out | pull_resistor_17_node | transistor_32_out | transistor_49_out | transistor_50_out | pull_resistor_39_node;  // OR_Gate or_16, 6 bits wide
  Pull_Resistor pull_resistor_40 (.node(pull_resistor_40_node));
  Transistor #(.\type ("n"), .width(6)) transistor_52 (.in(in_4), .out(pull_resistor_40_node), .gate(out_15));
  assign or_17_out = pull_resistor_19_node | transistor_35_out | transistor_37_out | pull_resistor_25_node | pull_resistor_27_node | pull_resistor_29_node;  // OR_Gate or_17, 6 bits wide
  assign or_18_out = pull_resistor_20_node | transistor_36_out | pull_resistor_24_node | pull_resistor_26_node | pull_resistor_28_node | transistor_44_out;  // OR_Gate or_18, 6 bits wide
  assign or_19_out = left_hor1 | right_hor1;  // OR_Gate or_19, 6 bits wide
  not not_1 (not_1_out, in_1);
  zero_or_not zero_or_not_13 (.in_1(or_19_out), .out_2(zero_or_not_13_out_2));
  and and_19 (and_19_out, can_w1, zero_or_not_13_out_2, not_1_out);
  Transistor #(.\type ("n"), .width(6)) transistor_53 (
    .in(coloring_black_hor), .out(transistor_53_out), .gate(and_19_out));
  Transistor #(.\type ("n"), .width(6)) transistor_54 (
    .in(black1_diag), .out(transistor_54_out), .gate(do_diag_coloring_1));
  assign or_20_out = left_hor2 | right_hor2;  // OR_Gate or_20, 6 bits wide
  not not_2 (not_2_out, in_1);
  zero_or_not zero_or_not_14 (.in_1(or_20_out), .out_2(zero_or_not_14_out_2));
  and and_20 (and_20_out, can_w2, zero_or_not_14_out_2, not_2_out);
  Transistor #(.\type ("n"), .width(6)) transistor_55 (
    .in(coloring_black_hor), .out(transistor_55_out), .gate(and_20_out));
  Transistor #(.\type ("n"), .width(6)) transistor_56 (
    .in(black2_diag), .out(transistor_56_out), .gate(do_diag_coloring_2));
  zero_or_not zero_or_not_15 (.in_1(or_14_out), .out_2(zero_or_not_15_out_2));
  not not_3 (not_3_out, in_1);
  and and_21 (and_21_out, can_w3, zero_or_not_15_out_2, not_3_out);
  Transistor #(.\type ("n"), .width(6)) transistor_57 (
    .in(coloring_black_hor), .out(transistor_57_out), .gate(and_21_out));
  Transistor #(.\type ("n"), .width(6)) transistor_58 (
    .in(black3_diag), .out(transistor_58_out), .gate(do_diag_coloring_3));
  Pull_Resistor #(.pull(1)) pull_resistor_41 (.node(transistor_58_out));
  coloring_hor coloring_hor_1 (
    .min_left(or_15_out), .max_right(or_16_out), .column(pull_resistor_40_node), .now_white(or_17_out),
    .now_black(or_18_out), .out_6(coloring_white_hor), .out_7(coloring_black_hor));
  Pull_Resistor #(.pull(1)) pull_resistor_42 (.node(transistor_53_out));
  Pull_Resistor #(.pull(1)) pull_resistor_43 (.node(transistor_54_out));
  Pull_Resistor #(.pull(1)) pull_resistor_44 (.node(transistor_56_out));
  Transistor #(.\type ("n"), .width(6)) transistor_59 (.in(6'b000100), .out(transistor_59_out), .gate(in_1));
  Pull_Resistor pull_resistor_45 (.node(transistor_59_out));
  assign or_21_out = left_hor4 | right_hor4;  // OR_Gate or_21, 6 bits wide
  not not_4 (not_4_out, in_1);
  zero_or_not zero_or_not_16 (.in_1(or_21_out), .out_2(zero_or_not_16_out_2));
  and and_22 (and_22_out, can_w4, zero_or_not_16_out_2, not_4_out);
  Transistor #(.\type ("n"), .width(6)) transistor_60 (
    .in(coloring_black_hor), .out(transistor_60_out), .gate(and_22_out));
  Pull_Resistor #(.pull(1)) pull_resistor_46 (.node(pull_resistor_46_node));
  Transistor #(.\type ("n"), .width(6)) transistor_61 (
    .in(black4_diag), .out(pull_resistor_46_node), .gate(do_diag_coloring_4));
  Pull_Resistor #(.pull(1)) pull_resistor_47 (.node(transistor_55_out));
  assign or_22_out = {out_11[11], out_11[9], out_11[7], out_11[5], out_11[3], out_11[1]} | transistor_59_out;  // OR_Gate or_22, 6 bits wide
  Pull_Resistor #(.pull(1)) pull_resistor_48 (.node(transistor_57_out));
  Transistor #(.\type ("n"), .width(6)) transistor_62 (.in(6'b001000), .out(transistor_62_out), .gate(in_1));
  Pull_Resistor pull_resistor_49 (.node(transistor_62_out));
  Pull_Resistor #(.pull(1)) pull_resistor_50 (.node(transistor_60_out));
  assign or_23_out = left_hor5 | right_hor5;  // OR_Gate or_23, 6 bits wide
  and and_23 (and_23_out, in_2, out_15);
  not not_5 (not_5_out, and_23_out);
  CDM16 cdm16_1 (
    .go(not_5_out), .white1({out_6[11], out_6[9], out_6[7], out_6[5], out_6[3], out_6[1]}),
    .black1({out_7[11], out_7[9], out_7[7], out_7[5], out_7[3], out_7[1]}),
    .white2({out_8[11], out_8[9], out_8[7], out_8[5], out_8[3], out_8[1]}),
    .black2({out_9[11], out_9[9], out_9[7], out_9[5], out_9[3], out_9[1]}),
    .white3({out_10[11], out_10[9], out_10[7], out_10[5], out_10[3], out_10[1]}),
    .black3({out_11[11], out_11[9], out_11[7], out_11[5], out_11[3], out_11[1]}),
    .white4({out_12[11], out_12[9], out_12[7], out_12[5], out_12[3], out_12[1]}),
    .black4({out_13[11], out_13[9], out_13[7], out_13[5], out_13[3], out_13[1]}),
    .white5({out_14[11], out_14[9], out_14[7], out_14[5], out_14[3], out_14[1]}),
    .black5({out_17[11], out_17[9], out_17[7], out_17[5], out_17[3], out_17[1]}),
    .white6({out_16[11], out_16[9], out_16[7], out_16[5], out_16[3], out_16[1]}),
    .black6({out_24[11], out_24[9], out_24[7], out_24[5], out_24[3], out_24[1]}), .white_out_1(out_w_1),
    .white_out_2(out_w_2), .white_out_3(out_w_3), .white_out_4(out_w_4), .white_out_5(out_w_5),
    .white_out_6(out_w_6), .black_out_1(out_b_1), .black_out_2(out_b_2), .black_out_3(out_b_3),
    .black_out_4(out_b_4), .black_out_5(out_b_5), .black_out_6(out_b_6), .flag_bot_finish(out_25),
    .out_29(out_26), .in_14(in_4), .in_15(now_row));
  assign or_24_out = up_ver1 | down_ver2;  // OR_Gate or_24, 6 bits wide
  zero_or_not zero_or_not_17 (.in_1(or_24_out), .out_2(zero_or_not_17_out_2));
  Transistor #(.\type ("n"), .width(6)) transistor_63 (
    .in(now_row), .out(transistor_63_out), .gate(zero_or_not_17_out_2));
  Pull_Resistor pull_resistor_51 (.node(transistor_63_out));
  assign and_24_out = transistor_53_out & transistor_54_out & {out_7[11], out_7[9], out_7[7], out_7[5], out_7[3], out_7[1]} & do_res & after_ver_paint_b_1;  // AND_Gate and_24, 6 bits wide
  zero_or_not zero_or_not_18 (.in_1(after_ver_paint_w_1), .out_2(zero_or_not_18_out_2));
  and and_25 (and_25_out, zero_or_not_18_out_2, out_15);
  assign and_26_out = transistor_55_out & transistor_56_out & {out_9[11], out_9[9], out_9[7], out_9[5], out_9[3], out_9[1]} & do_res & after_ver_paint_b_2;  // AND_Gate and_26, 6 bits wide
  zero_or_not zero_or_not_19 (.in_1(after_ver_paint_w_2), .out_2(zero_or_not_19_out_2));
  and and_27 (and_27_out, zero_or_not_19_out_2, out_15);
  assign and_28_out = or_22_out & transistor_57_out & transistor_58_out & do_res & after_ver_paint_b_3;  // AND_Gate and_28, 6 bits wide
  zero_or_not zero_or_not_20 (.in_1(after_ver_paint_w_3), .out_2(zero_or_not_20_out_2));
  and and_29 (and_29_out, zero_or_not_20_out_2, out_15);
  assign or_25_out = {out_13[11], out_13[9], out_13[7], out_13[5], out_13[3], out_13[1]} | transistor_62_out;  // OR_Gate or_25, 6 bits wide
  assign and_30_out = or_25_out & transistor_60_out & pull_resistor_46_node & do_res & after_ver_paint_b_4;  // AND_Gate and_30, 6 bits wide
  zero_or_not zero_or_not_21 (.in_1(after_ver_paint_w_4), .out_2(zero_or_not_21_out_2));
  and and_31 (and_31_out, zero_or_not_21_out_2, out_15);
  not not_6 (not_6_out, in_1);
  zero_or_not zero_or_not_22 (.in_1(or_23_out), .out_2(zero_or_not_22_out_2));
  and and_32 (and_32_out, can_w5, zero_or_not_22_out_2, not_6_out);
  Transistor #(.\type ("n"), .width(6)) transistor_64 (
    .in(coloring_black_hor), .out(transistor_64_out), .gate(and_32_out));
  Pull_Resistor #(.pull(1)) pull_resistor_52 (.node(pull_resistor_52_node));
  Transistor #(.\type ("n"), .width(6)) transistor_65 (
    .in(black5_diag), .out(pull_resistor_52_node), .gate(do_diag_coloring_5));
  assign or_26_out = left_hor6 | right_hor6;  // OR_Gate or_26, 6 bits wide
  zero_or_not zero_or_not_23 (.in_1(or_26_out), .out_2(zero_or_not_23_out_2));
  not not_7 (not_7_out, in_1);
  and and_33 (and_33_out, can_w6, zero_or_not_23_out_2, not_7_out);
  Transistor #(.\type ("n"), .width(6)) transistor_66 (
    .in(coloring_black_hor), .out(transistor_66_out), .gate(and_33_out));
  Transistor #(.\type ("n"), .width(6)) transistor_67 (
    .in(black6_diag), .out(transistor_67_out), .gate(do_diag_coloring_6));
  coloring_hor coloring_hor_2 (
    .min_left(down_ver2), .max_right(up_ver1), .column(transistor_63_out), .now_white(white_col),
    .now_black(black_col), .out_6(coloring_white_ver), .out_7(coloring_black_ver));
  Transistor #(.width(6)) transistor_68 (.in(and_24_out), .out(transistor_68_out), .gate(out_25));
  Transistor #(.\type ("n"), .gate("br"), .width(6)) transistor_69 (
    .in(out_b_1), .out(transistor_68_out), .gate(out_25));
  or or_27 (or_27_out, can_w1, do_diag_coloring_1, out_25, and_25_out);
  Transistor #(.width(6)) transistor_70 (.in(and_26_out), .out(transistor_70_out), .gate(out_25));
  Transistor #(.\type ("n"), .gate("br"), .width(6)) transistor_71 (
    .in(out_b_2), .out(transistor_70_out), .gate(out_25));
  or or_28 (or_28_out, can_w2, do_diag_coloring_2, out_25, and_27_out);
  Transistor #(.width(6)) transistor_72 (.in(and_28_out), .out(transistor_72_out), .gate(out_25));
  Transistor #(.\type ("n"), .gate("br"), .width(6)) transistor_73 (
    .in(out_b_3), .out(transistor_72_out), .gate(out_25));
  or or_29 (or_29_out, can_w3, do_diag_coloring_3, out_25, and_29_out);
  Transistor #(.width(6)) transistor_74 (.in(and_30_out), .out(transistor_74_out), .gate(out_25));
  Transistor #(.\type ("n"), .gate("br"), .width(6)) transistor_75 (
    .in(out_b_4), .out(transistor_74_out), .gate(out_25));
  or or_30 (or_30_out, can_w4, do_diag_coloring_4, out_25, and_31_out);
  Pull_Resistor #(.pull(1)) pull_resistor_53 (.node(transistor_64_out));
  Pull_Resistor #(.pull(1)) pull_resistor_54 (.node(transistor_66_out));
  Pull_Resistor #(.pull(1)) pull_resistor_55 (.node(transistor_67_out));
  Register #(.width(6)) register_7 (
    .D(transistor_68_out), .en(or_27_out), .Q({out_7[11], out_7[9], out_7[7], out_7[5], out_7[3], out_7[1]}),
    .clk(tic));  // open: clr
  Register #(.width(6)) register_8 (
    .D(transistor_70_out), .en(or_28_out), .Q({out_9[11], out_9[9], out_9[7], out_9[5], out_9[3], out_9[1]}),
    .clk(tic));  // open: clr
  Register #(.width(6)) register_9 (
    .D(transistor_72_out), .en(or_29_out),
    .Q({out_11[11], out_11[9], out_11[7], out_11[5], out_11[3], out_11[1]}), .clk(tic));  // open: clr
  Register #(.width(6)) register_10 (
    .D(transistor_74_out), .en(or_30_out),
    .Q({out_13[11], out_13[9], out_13[7], out_13[5], out_13[3], out_13[1]}), .clk(tic));  // open: clr
  assign and_34_out = transistor_64_out & pull_resistor_52_node & {out_17[11], out_17[9], out_17[7], out_17[5], out_17[3], out_17[1]} & do_res & after_ver_paint_b_5;  // AND_Gate and_34, 6 bits wide
  zero_or_not zero_or_not_24 (.in_1(after_ver_paint_w_5), .out_2(zero_or_not_24_out_2));
  and and_35 (and_35_out, zero_or_not_24_out_2, out_15);
  assign and_36_out = transistor_66_out & transistor_67_out & {out_24[11], out_24[9], out_24[7], out_24[5], out_24[3], out_24[1]} & do_res & after_ver_paint_b_6;  // AND_Gate and_36, 6 bits wide
  zero_or_not zero_or_not_25 (.in_1(after_ver_paint_w_6), .out_2(zero_or_not_25_out_2));
  and and_37 (and_37_out, zero_or_not_25_out_2, out_15);
  Transistor #(.width(6)) transistor_76 (.in(and_34_out), .out(transistor_76_out), .gate(out_25));
  Transistor #(.\type ("n"), .gate("br"), .width(6)) transistor_77 (
    .in(out_b_5), .out(transistor_76_out), .gate(out_25));
  or or_31 (or_31_out, can_w5, do_diag_coloring_5, out_25, and_35_out);
  Transistor #(.width(6)) transistor_78 (.in(and_36_out), .out(transistor_78_out), .gate(out_25));
  Transistor #(.\type ("n"), .gate("br"), .width(6)) transistor_79 (
    .in(out_b_6), .out(transistor_78_out), .gate(out_25));
  compare_6bit compare_6bit_1 (
    .in_1({out_7[11], out_7[9], out_7[7], out_7[5], out_7[3], out_7[1]}), .in_2(black1_diag),
    .out_3(compare_6bit_1_out_3));
  and and_38 (do_diag_coloring_1, out_15, compare_6bit_1_out_3, not_8_out, not_9_out);
  compare_6bit compare_6bit_2 (
    .in_1({out_9[11], out_9[9], out_9[7], out_9[5], out_9[3], out_9[1]}), .in_2(black2_diag),
    .out_3(compare_6bit_2_out_3));
  and and_39 (do_diag_coloring_2, out_15, compare_6bit_2_out_3, not_10_out, not_11_out);
  compare_6bit compare_6bit_3 (
    .in_1({out_11[11], out_11[9], out_11[7], out_11[5], out_11[3], out_11[1]}), .in_2(black3_diag),
    .out_3(compare_6bit_3_out_3));
  compare_6bit compare_6bit_4 (
    .in_1({out_13[11], out_13[9], out_13[7], out_13[5], out_13[3], out_13[1]}), .in_2(black4_diag),
    .out_3(compare_6bit_4_out_3));
  and and_40 (do_diag_coloring_4, out_15, compare_6bit_4_out_3, not_14_out, not_15_out);
  Register #(.width(6)) register_11 (
    .D(transistor_76_out), .en(or_31_out),
    .Q({out_17[11], out_17[9], out_17[7], out_17[5], out_17[3], out_17[1]}), .clk(tic));  // open: clr
  Register #(.width(6)) register_12 (
    .D(transistor_78_out), .en(or_32_out),
    .Q({out_24[11], out_24[9], out_24[7], out_24[5], out_24[3], out_24[1]}), .clk(tic));  // open: clr
  or or_32 (or_32_out, can_w6, do_diag_coloring_6, out_25, and_37_out);
  coloring_diag coloring_diag_1 (
    .max_column_ru(ru_max), .in_2({out_6[11], out_6[9], out_6[7], out_6[5], out_6[3], out_6[1]}),
    .in_3({out_7[11], out_7[9], out_7[7], out_7[5], out_7[3], out_7[1]}),
    .in_4({out_8[11], out_8[9], out_8[7], out_8[5], out_8[3], out_8[1]}),
    .in_5({out_9[11], out_9[9], out_9[7], out_9[5], out_9[3], out_9[1]}), .max_column_lu(lu_max),
    .in_7({out_10[11], out_10[9], out_10[7], out_10[5], out_10[3], out_10[1]}),
    .in_8({out_11[11], out_11[9], out_11[7], out_11[5], out_11[3], out_11[1]}),
    .in_9({out_12[11], out_12[9], out_12[7], out_12[5], out_12[3], out_12[1]}),
    .in_10({out_13[11], out_13[9], out_13[7], out_13[5], out_13[3], out_13[1]}), .max_column_rd(rd_max),
    .in_12({out_14[11], out_14[9], out_14[7], out_14[5], out_14[3], out_14[1]}),
    .in_13({out_17[11], out_17[9], out_17[7], out_17[5], out_17[3], out_17[1]}),
    .in_14({out_16[11], out_16[9], out_16[7], out_16[5], out_16[3], out_16[1]}),
    .in_15({out_24[11], out_24[9], out_24[7], out_24[5], out_24[3], out_24[1]}), .max_column_ld(ld_max),
    .now_column(in_4), .now_row(now_row), .out_19(white1_diag), .out_20(black1_diag), .out_21(white2_diag),
    .out_22(black2_diag), .out_23(white3_diag), .out_24(black3_diag), .out_25(white4_diag),
    .out_26(black4_diag), .out_27(white5_diag), .out_28(black5_diag), .out_29(white6_diag),
    .out_30(black6_diag));
  not not_8 (not_8_out, in_1);
  not not_9 (not_9_out, _1);
  not not_10 (not_10_out, in_1);
  not not_11 (not_11_out, _2);
  not not_12 (not_12_out, in_1);
  not not_13 (not_13_out, _3);
  and and_41 (do_diag_coloring_3, out_15, compare_6bit_3_out_3, not_12_out, not_13_out);
  not not_14 (not_14_out, in_1);
  not not_15 (not_15_out, _4);
  compare_6bit compare_6bit_5 (
    .in_1({out_17[11], out_17[9], out_17[7], out_17[5], out_17[3], out_17[1]}), .in_2(black5_diag),
    .out_3(compare_6bit_5_out_3));
  and and_42 (do_diag_coloring_5, out_15, compare_6bit_5_out_3, not_16_out, not_17_out);
  compare_6bit compare_6bit_6 (
    .in_1({out_24[11], out_24[9], out_24[7], out_24[5], out_24[3], out_24[1]}), .in_2(black6_diag),
    .out_3(compare_6bit_6_out_3));
  and and_43 (do_diag_coloring_6, out_15, compare_6bit_6_out_3, not_18_out, not_19_out);
  row_to_column_for_black row_to_column_for_black_1 (
    .column_black(coloring_black_ver), .column_num(in_4), .out_3(after_ver_paint_b_1),
    .out_4(after_ver_paint_b_2), .out_5(after_ver_paint_b_3), .out_6(after_ver_paint_b_4),
    .out_7(after_ver_paint_b_5), .out_8(after_ver_paint_b_6));
  row_to_column_for_white row_to_column_for_white_1 (
    .column_white(coloring_white_ver), .column_num(in_4), .out_3(after_ver_paint_w_1),
    .out_4(after_ver_paint_w_2), .out_5(after_ver_paint_w_3), .out_6(after_ver_paint_w_4),
    .out_7(after_ver_paint_w_5), .out_8(after_ver_paint_w_6));
  not not_16 (not_16_out, in_1);
  not not_17 (not_17_out, _5);
  not not_18 (not_18_out, in_1);
  not not_19 (not_19_out, _6);

  assign {out_6[12], out_6[10], out_6[8], out_6[6], out_6[4], out_6[2], out_6[0]} = {1'b0, out_6[11], out_6[9], out_6[7], out_6[5], out_6[3], out_6[1]};
  assign {out_7[10], out_7[8], out_7[6], out_7[4], out_7[2], out_7[0]} = {out_7[11], out_7[9], out_7[7], out_7[5], out_7[3], out_7[1]};
  assign {out_8[12], out_8[10], out_8[8], out_8[6], out_8[4], out_8[2], out_8[0]} = {1'b0, out_8[11], out_8[9], out_8[7], out_8[5], out_8[3], out_8[1]};
  assign {out_9[10], out_9[8], out_9[6], out_9[4], out_9[2], out_9[0]} = {out_9[11], out_9[9], out_9[7], out_9[5], out_9[3], out_9[1]};
  assign {out_10[12], out_10[10], out_10[8], out_10[6], out_10[4], out_10[2], out_10[0]} = {1'b0, out_10[11], out_10[9], out_10[7], out_10[5], out_10[3], out_10[1]};
  assign {out_11[10], out_11[8], out_11[6], out_11[4], out_11[2], out_11[0]} = {out_11[11], out_11[9], out_11[7], out_11[5], out_11[3], out_11[1]};
  assign {out_12[12], out_12[10], out_12[8], out_12[6], out_12[4], out_12[2], out_12[0]} = {1'b0, out_12[11], out_12[9], out_12[7], out_12[5], out_12[3], out_12[1]};
  assign {out_13[10], out_13[8], out_13[6], out_13[4], out_13[2], out_13[0]} = {out_13[11], out_13[9], out_13[7], out_13[5], out_13[3], out_13[1]};
  assign {out_14[12], out_14[10], out_14[8], out_14[6], out_14[4], out_14[2], out_14[0]} = {1'b0, out_14[11], out_14[9], out_14[7], out_14[5], out_14[3], out_14[1]};
  assign {out_16[12], out_16[10], out_16[8], out_16[6], out_16[4], out_16[2], out_16[0]} = {1'b0, out_16[11], out_16[9], out_16[7], out_16[5], out_16[3], out_16[1]};
  assign {out_17[10], out_17[8], out_17[6], out_17[4], out_17[2], out_17[0]} = {out_17[11], out_17[9], out_17[7], out_17[5], out_17[3], out_17[1]};
  assign {out_24[10], out_24[8], out_24[6], out_24[4], out_24[2], out_24[0]} = {out_24[11], out_24[9], out_24[7], out_24[5], out_24[3], out_24[1]};

  // Other names for the same wires on the sheet: black3[5:0] = {out_11[11], out_11[9], out_11[7], out_11[5], out_11[3], out_11[1]};
  //   bot_finish = out_25; can_put = out_15; column[5:0] = in_4; count_b[5:0] = black_count;
  //   count_w[5:0] = white_count; black1[5:0] = {out_7[11], out_7[9], out_7[7], out_7[5], out_7[3], out_7[1]};
  //   white2[5:0] = {out_8[11], out_8[9], out_8[7], out_8[5], out_8[3], out_8[1]};
  //   black2[5:0] = {out_9[11], out_9[9], out_9[7], out_9[5], out_9[3], out_9[1]};
  //   white3[5:0] = {out_10[11], out_10[9], out_10[7], out_10[5], out_10[3], out_10[1]};
  //   white4[5:0] = {out_12[11], out_12[9], out_12[7], out_12[5], out_12[3], out_12[1]};
  //   black4[5:0] = {out_13[11], out_13[9], out_13[7], out_13[5], out_13[3], out_13[1]};
  //   white5[5:0] = {out_14[11], out_14[9], out_14[7], out_14[5], out_14[3], out_14[1]};
  //   black5[5:0] = {out_17[11], out_17[9], out_17[7], out_17[5], out_17[3], out_17[1]};
  //   black6[5:0] = {out_24[11], out_24[9], out_24[7], out_24[5], out_24[3], out_24[1]}; reset = in_3;
  //   row[2:0] = in_5; start = in_1; turn = in_2;
  //   white1[5:0] = {out_6[11], out_6[9], out_6[7], out_6[5], out_6[3], out_6[1]};
  //   white6[5:0] = {out_16[11], out_16[9], out_16[7], out_16[5], out_16[3], out_16[1]}
endmodule

module buttons_row (
  input  in_1,
  input  in_2,
  input  in_3,
  input  in_4,
  input  in_5,
  input  in_6,
  output [5:0] out_7
);


  assign out_7 = {in_1, in_2, in_3, in_4, in_5, in_6};

  // Other names for the same wires on the sheet: _0 = in_6; _1 = in_5; _2 = in_4; _3 = in_3; _4 = in_2; _5 = in_1
endmodule

module if_3bit (
  input  [2:0] Input_0,
  input  sel,
  input  [2:0] Input_1,
  output [2:0] Output
);

  wire [2:0] and_1_out, and_2_out;
  wire [2:2] not_1_out;

  not not_1 (not_1_out[2], sel);
  assign and_1_out = Input_0 & {3{not_1_out[2]}};  // AND_Gate and_1, 3 bits wide
  assign and_2_out = {3{sel}} & Input_1;  // AND_Gate and_2, 3 bits wide
  assign Output = and_1_out | and_2_out;  // OR_Gate or_1, 3 bits wide
endmodule

module compare_6bit (
  input  [5:0] in_1,
  input  [5:0] in_2,
  output out_3
);

  wire comparator_1_eq;

  Comparator #(.width(6)) comparator_1 (.a(in_1), .b(in_2), .eq(comparator_1_eq));  // open: gt, lt
  not not_1 (out_3, comparator_1_eq);

  // Notes on the sheet:
  //   0 if the inputs are equal
endmodule

module column_to_row (
  input  [5:0] in_1,
  input  [5:0] in_2,
  input  [5:0] in_3,
  input  [5:0] in_4,
  input  [5:0] in_5,
  input  [5:0] in_6,
  input  [5:0] in_7,
  output [5:0] out_8
);

  wire [2:0] and_1_out, and_2_out, and_3_out, and_4_out, and_5_out, and_6_out, and_7_out, and_8_out,
       and_9_out, and_10_out, and_11_out, and_12_out, column, or_1_out, or_2_out, or_3_out, or_4_out,
       or_5_out, or_6_out;
  wire [2:2] not_1_out, not_2_out, not_3_out, not_4_out, not_5_out, not_6_out;

  Multiplexer #(.select(3)) multiplexer_1 (
    .in0(in_1[0]), .in1(in_1[1]), .in2(in_1[2]), .in3(in_1[3]), .in4(in_1[4]), .in5(in_1[5]), .out(out_8[0]),
    .sel(column));  // open: in6, in7, en
  Multiplexer #(.select(3)) multiplexer_2 (
    .in0(in_2[0]), .in1(in_2[1]), .in2(in_2[2]), .in3(in_2[3]), .in4(in_2[4]), .in5(in_2[5]), .out(out_8[1]),
    .sel(column));  // open: in6, in7, en
  Multiplexer #(.select(3)) multiplexer_3 (
    .in0(in_3[0]), .in1(in_3[1]), .in2(in_3[2]), .in3(in_3[3]), .in4(in_3[4]), .in5(in_3[5]), .out(out_8[2]),
    .sel(column));  // open: in6, in7, en
  Multiplexer #(.select(3)) multiplexer_4 (
    .in0(in_4[0]), .in1(in_4[1]), .in2(in_4[2]), .in3(in_4[3]), .in4(in_4[4]), .in5(in_4[5]), .out(out_8[3]),
    .sel(column));  // open: in6, in7, en
  Multiplexer #(.select(3)) multiplexer_5 (
    .in0(in_6[0]), .in1(in_6[1]), .in2(in_6[2]), .in3(in_6[3]), .in4(in_6[4]), .in5(in_6[5]), .out(out_8[4]),
    .sel(column));  // open: in6, in7, en
  Multiplexer #(.select(3)) multiplexer_6 (
    .in0(in_7[0]), .in1(in_7[1]), .in2(in_7[2]), .in3(in_7[3]), .in4(in_7[4]), .in5(in_7[5]), .out(out_8[5]),
    .sel(column));  // open: in6, in7, en
  assign and_1_out = 3'b000 & {3{not_1_out[2]}};  // AND_Gate and_1, 3 bits wide
  not not_1 (not_1_out[2], in_5[0]);
  assign and_2_out = {3{in_5[0]}} & 3'b000;  // AND_Gate and_2, 3 bits wide
  assign and_3_out = 3'b000 & {3{not_2_out[2]}};  // AND_Gate and_3, 3 bits wide
  not not_2 (not_2_out[2], in_5[1]);
  assign and_4_out = {3{in_5[1]}} & 3'b001;  // AND_Gate and_4, 3 bits wide
  assign and_5_out = 3'b000 & {3{not_3_out[2]}};  // AND_Gate and_5, 3 bits wide
  not not_3 (not_3_out[2], in_5[2]);
  assign and_6_out = {3{in_5[2]}} & 3'b010;  // AND_Gate and_6, 3 bits wide
  assign and_7_out = 3'b000 & {3{not_4_out[2]}};  // AND_Gate and_7, 3 bits wide
  not not_4 (not_4_out[2], in_5[3]);
  assign and_8_out = {3{in_5[3]}} & 3'b011;  // AND_Gate and_8, 3 bits wide
  assign and_9_out = 3'b000 & {3{not_5_out[2]}};  // AND_Gate and_9, 3 bits wide
  not not_5 (not_5_out[2], in_5[4]);
  assign and_10_out = {3{in_5[4]}} & 3'b100;  // AND_Gate and_10, 3 bits wide
  assign and_11_out = 3'b000 & {3{not_6_out[2]}};  // AND_Gate and_11, 3 bits wide
  not not_6 (not_6_out[2], in_5[5]);
  assign and_12_out = {3{in_5[5]}} & 3'b101;  // AND_Gate and_12, 3 bits wide
  assign or_1_out = and_1_out | and_2_out;  // OR_Gate or_1, 3 bits wide
  assign or_2_out = and_3_out | and_4_out;  // OR_Gate or_2, 3 bits wide
  assign or_3_out = and_5_out | and_6_out;  // OR_Gate or_3, 3 bits wide
  assign or_4_out = and_7_out | and_8_out;  // OR_Gate or_4, 3 bits wide
  assign or_5_out = and_9_out | and_10_out;  // OR_Gate or_5, 3 bits wide
  assign or_6_out = and_11_out | and_12_out;  // OR_Gate or_6, 3 bits wide
  assign column = or_1_out | or_2_out | or_3_out | or_4_out | or_5_out | or_6_out;  // OR_Gate or_7, 3 bits wide
endmodule

module check_right (
  input  [5:0] corrent,
  input  [5:0] white,
  input  [5:0] black,
  output [5:0] out_4,
  output out_5
);

  wire _1break, _2break, _3break, _4break, _5break, _6break, and_1_out, and_2_out, and_3_out, and_4_out,
       and_6_out, and_7_out, and_10_out, and_13_out, and_16_out, answer, compare_6bit_1_out_3,
       compare_6bit_2_out_3, compare_6bit_3_out_3, compare_6bit_4_out_3, compare_6bit_5_out_3, not_1_out,
       not_2_out, not_4_out, not_5_out, not_6_out, not_7_out, not_8_out, not_9_out, not_10_out, not_11_out,
       not_12_out, not_13_out, not_14_out, not_15_out, not_16_out, or_2_out, zero_or_not_1_out_2,
       zero_or_not_2_out_2, zero_or_not_3_out_2, zero_or_not_4_out_2, zero_or_not_5_out_2,
       zero_or_not_6_out_2, zero_or_not_7_out_2, zero_or_not_8_out_2;
  wire [2:0] bit_extender_1_out, bit_extender_2_out, bit_extender_3_out, bit_extender_4_out,
       bit_extender_5_out;
  wire [5:0] and_5_out, and_8_out, and_9_out, and_11_out, and_12_out, and_14_out, and_15_out, and_17_out,
       and_18_out, col2, col3, col4, col5, col6, or_1_out, shifter_2_out, transistor_1_out, transistor_2_out,
       transistor_3_out, transistor_4_out, transistor_5_out, transistor_6_out;

  compare_6bit compare_6bit_1 (.in_1(6'b000001), .in_2(corrent), .out_3(compare_6bit_1_out_3));
  not not_1 (not_1_out, _4break);
  not not_2 (not_2_out, _5break);
  assign bit_extender_1_out = {{2{1'b0}}, compare_6bit_1_out_3};  // Bit_Extender bit_extender_1
  not not_3 (_1break, compare_6bit_1_out_3);
  not not_4 (not_4_out, _2break);
  not not_5 (not_5_out, _1break);
  and and_1 (and_1_out, _3break, not_4_out, not_5_out);
  not not_6 (not_6_out, _1break);
  not not_7 (not_7_out, _3break);
  not not_8 (not_8_out, _2break);
  and and_2 (and_2_out, _4break, not_7_out, not_8_out, not_6_out);
  Transistor #(.\type ("n"), .width(6)) transistor_1 (.in(col4), .out(transistor_1_out), .gate(and_2_out));
  not not_9 (not_9_out, _3break);
  not not_10 (not_10_out, _1break);
  not not_11 (not_11_out, _2break);
  and and_3 (and_3_out, not_1_out, not_9_out, _5break, not_11_out, not_10_out);
  Transistor #(.\type ("n"), .width(6)) transistor_2 (.in(col5), .out(transistor_2_out), .gate(and_3_out));
  not not_12 (not_12_out, _4break);
  not not_13 (not_13_out, _3break);
  and and_4 (and_4_out, _6break, not_2_out, not_12_out, not_13_out, not_14_out, not_15_out);
  Transistor #(.\type ("n"), .width(6)) transistor_3 (.in(col6), .out(transistor_3_out), .gate(and_4_out));
  Shifter #(.width(6), .shift("lr")) shifter_1 (.in(corrent), .\dist (bit_extender_1_out), .out(col2));
  Transistor #(.\type ("n"), .width(6)) transistor_4 (.in(col3), .out(transistor_4_out), .gate(and_1_out));
  not not_14 (not_14_out, _2break);
  not not_15 (not_15_out, _1break);
  compare_6bit compare_6bit_2 (.in_1(6'b000001), .in_2(col2), .out_3(compare_6bit_2_out_3));
  assign and_5_out = col2 & black;  // AND_Gate and_5, 6 bits wide
  zero_or_not zero_or_not_1 (.in_1(and_5_out), .out_2(zero_or_not_1_out_2));
  not not_16 (not_16_out, _1break);
  and and_6 (and_6_out, _2break, not_16_out);
  Transistor #(.\type ("n"), .width(6)) transistor_5 (.in(col2), .out(transistor_5_out), .gate(and_6_out));
  and and_7 (and_7_out, compare_6bit_2_out_3, zero_or_not_1_out_2);
  not not_17 (_2break, and_7_out);
  Transistor #(.\type ("n"), .width(6)) transistor_6 (.in(corrent), .out(transistor_6_out), .gate(_1break));
  Pull_Resistor pull_resistor_1 (.node(transistor_2_out));
  Shifter #(.width(6), .shift("lr")) shifter_2 (.in(col2), .\dist (bit_extender_2_out), .out(shifter_2_out));
  assign bit_extender_2_out = {{2{1'b0}}, and_7_out};  // Bit_Extender bit_extender_2
  Pull_Resistor pull_resistor_2 (.node(transistor_6_out));
  Pull_Resistor pull_resistor_3 (.node(transistor_5_out));
  Pull_Resistor pull_resistor_4 (.node(transistor_4_out));
  Pull_Resistor pull_resistor_5 (.node(transistor_1_out));
  Transistor #(.width(6)) transistor_7 (.in(shifter_2_out), .out(col3), .gate(_2break));
  Pull_Resistor pull_resistor_6 (.node(col3));
  assign or_1_out = transistor_6_out | transistor_5_out | transistor_4_out | transistor_1_out | transistor_2_out | transistor_3_out;  // OR_Gate or_1, 6 bits wide
  Pull_Resistor pull_resistor_7 (.node(transistor_3_out));
  compare_6bit compare_6bit_3 (.in_1(6'b000001), .in_2(col3), .out_3(compare_6bit_3_out_3));
  assign and_8_out = col3 & black;  // AND_Gate and_8, 6 bits wide
  zero_or_not zero_or_not_2 (.in_1(and_8_out), .out_2(zero_or_not_2_out_2));
  Pull_Resistor pull_resistor_8 (.node(zero_or_not_2_out_2));
  zero_or_not zero_or_not_3 (.in_1(and_9_out), .out_2(zero_or_not_3_out_2));
  assign and_9_out = col3 & white;  // AND_Gate and_9, 6 bits wide
  Pull_Resistor pull_resistor_9 (.node(out_4));
  Transistor #(.\type ("n"), .width(6)) transistor_8 (.in(or_1_out), .out(out_4), .gate(answer));
  and and_10 (and_10_out, compare_6bit_3_out_3, zero_or_not_2_out_2);
  not not_18 (_3break, and_10_out);
  Transistor transistor_9 (.in(zero_or_not_3_out_2), .out(answer), .gate(zero_or_not_2_out_2));
  Shifter #(.width(6), .shift("lr")) shifter_3 (.in(col3), .\dist (bit_extender_3_out), .out(col4));
  assign bit_extender_3_out = {{2{1'b0}}, and_10_out};  // Bit_Extender bit_extender_3
  assign and_11_out = col4 & black;  // AND_Gate and_11, 6 bits wide
  zero_or_not zero_or_not_4 (.in_1(and_11_out), .out_2(zero_or_not_4_out_2));
  assign and_12_out = col4 & white;  // AND_Gate and_12, 6 bits wide
  zero_or_not zero_or_not_5 (.in_1(and_12_out), .out_2(zero_or_not_5_out_2));
  or or_2 (or_2_out, _1break, _2break, _4break, _3break, _5break, _6break);
  Transistor #(.\type ("n")) transistor_10 (.in(answer), .out(out_5), .gate(or_2_out));
  Pull_Resistor pull_resistor_10 (.node(out_5));
  compare_6bit compare_6bit_4 (.in_1(6'b000001), .in_2(col4), .out_3(compare_6bit_4_out_3));
  and and_13 (and_13_out, compare_6bit_4_out_3, zero_or_not_4_out_2);
  not not_19 (_4break, and_13_out);
  Pull_Resistor pull_resistor_11 (.node(zero_or_not_4_out_2));
  Transistor transistor_11 (.in(zero_or_not_5_out_2), .out(answer), .gate(zero_or_not_4_out_2));
  assign bit_extender_4_out = {{2{1'b0}}, and_13_out};  // Bit_Extender bit_extender_4
  Shifter #(.width(6), .shift("lr")) shifter_4 (.in(col4), .\dist (bit_extender_4_out), .out(col5));
  assign and_14_out = col5 & black;  // AND_Gate and_14, 6 bits wide
  assign and_15_out = col5 & white;  // AND_Gate and_15, 6 bits wide
  compare_6bit compare_6bit_5 (.in_1(6'b000001), .in_2(col5), .out_3(compare_6bit_5_out_3));
  and and_16 (and_16_out, compare_6bit_5_out_3, zero_or_not_6_out_2);
  zero_or_not zero_or_not_6 (.in_1(and_14_out), .out_2(zero_or_not_6_out_2));
  not not_20 (_5break, and_16_out);
  Pull_Resistor pull_resistor_12 (.node(zero_or_not_6_out_2));
  Transistor transistor_12 (.in(zero_or_not_7_out_2), .out(answer), .gate(zero_or_not_6_out_2));
  zero_or_not zero_or_not_7 (.in_1(and_15_out), .out_2(zero_or_not_7_out_2));
  assign bit_extender_5_out = {{2{1'b0}}, and_16_out};  // Bit_Extender bit_extender_5
  Shifter #(.width(6), .shift("lr")) shifter_5 (.in(col5), .\dist (bit_extender_5_out), .out(col6));
  zero_or_not zero_or_not_8 (.in_1(and_17_out), .out_2(zero_or_not_8_out_2));
  assign and_17_out = col6 & black;  // AND_Gate and_17, 6 bits wide
  not not_21 (_6break, zero_or_not_8_out_2);
  zero_or_not zero_or_not_9 (.in_1(and_18_out), .out_2(answer));
  assign and_18_out = col6 & white;  // AND_Gate and_18, 6 bits wide

  // Other names for the same wires on the sheet: col1[5:0] = corrent
endmodule

module check_left (
  input  [5:0] corrent,
  input  [5:0] white,
  input  [5:0] black,
  output out_4,
  output [5:0] out_5
);

  wire _1break, _2break, _3break, _4break, _5break, _6break, and_1_out, and_2_out, and_3_out, and_4_out,
       and_6_out, and_7_out, and_10_out, and_13_out, and_16_out, answer, compare_6bit_1_out_3,
       compare_6bit_2_out_3, compare_6bit_3_out_3, compare_6bit_4_out_3, compare_6bit_5_out_3, not_2_out,
       not_3_out, not_4_out, not_5_out, not_6_out, not_7_out, not_8_out, not_9_out, not_10_out, not_11_out,
       not_12_out, not_13_out, not_14_out, not_15_out, not_17_out, or_1_out, zero_or_not_1_out_2,
       zero_or_not_2_out_2, zero_or_not_3_out_2, zero_or_not_4_out_2, zero_or_not_5_out_2,
       zero_or_not_6_out_2, zero_or_not_7_out_2, zero_or_not_8_out_2;
  wire [2:0] bit_extender_1_out, bit_extender_2_out, bit_extender_3_out, bit_extender_4_out,
       bit_extender_5_out;
  wire [5:0] and_5_out, and_8_out, and_9_out, and_11_out, and_12_out, and_14_out, and_15_out, and_17_out,
       and_18_out, col2, col3, col4, col5, col6, or_2_out, shifter_2_out, transistor_1_out, transistor_2_out,
       transistor_3_out, transistor_4_out, transistor_5_out, transistor_7_out;

  compare_6bit compare_6bit_1 (.in_1(6'b100000), .in_2(corrent), .out_3(compare_6bit_1_out_3));
  assign bit_extender_1_out = {{2{1'b0}}, compare_6bit_1_out_3};  // Bit_Extender bit_extender_1
  not not_1 (_1break, compare_6bit_1_out_3);
  not not_2 (not_2_out, _4break);
  Shifter #(.width(6)) shifter_1 (.in(corrent), .\dist (bit_extender_1_out), .out(col2));
  not not_3 (not_3_out, _2break);
  and and_1 (and_1_out, _3break, not_3_out, not_13_out);
  not not_4 (not_4_out, _1break);
  not not_5 (not_5_out, _2break);
  not not_6 (not_6_out, _3break);
  and and_2 (and_2_out, _4break, not_6_out, not_5_out, not_4_out);
  Transistor #(.\type ("n"), .width(6)) transistor_1 (.in(col4), .out(transistor_1_out), .gate(and_2_out));
  not not_7 (not_7_out, _2break);
  not not_8 (not_8_out, _1break);
  not not_9 (not_9_out, _3break);
  and and_3 (and_3_out, not_2_out, not_9_out, _5break, not_7_out, not_8_out);
  Transistor #(.\type ("n"), .width(6)) transistor_2 (.in(col5), .out(transistor_2_out), .gate(and_3_out));
  not not_10 (not_10_out, _3break);
  not not_11 (not_11_out, _5break);
  not not_12 (not_12_out, _4break);
  and and_4 (and_4_out, _6break, not_11_out, not_12_out, not_10_out, not_15_out, not_14_out);
  Transistor #(.\type ("n"), .width(6)) transistor_3 (.in(col6), .out(transistor_3_out), .gate(and_4_out));
  compare_6bit compare_6bit_2 (.in_1(6'b100000), .in_2(col2), .out_3(compare_6bit_2_out_3));
  zero_or_not zero_or_not_1 (.in_1(and_5_out), .out_2(zero_or_not_1_out_2));
  assign and_5_out = col2 & black;  // AND_Gate and_5, 6 bits wide
  not not_13 (not_13_out, _1break);
  Transistor #(.\type ("n"), .width(6)) transistor_4 (.in(col3), .out(transistor_4_out), .gate(and_1_out));
  not not_14 (not_14_out, _1break);
  not not_15 (not_15_out, _2break);
  and and_6 (and_6_out, compare_6bit_2_out_3, zero_or_not_1_out_2);
  not not_16 (_2break, and_6_out);
  or or_1 (or_1_out, _1break, _2break, _4break, _3break, _5break, _6break);
  Pull_Resistor pull_resistor_1 (.node(answer));
  not not_17 (not_17_out, _1break);
  and and_7 (and_7_out, _2break, not_17_out);
  Transistor #(.\type ("n"), .width(6)) transistor_5 (.in(col2), .out(transistor_5_out), .gate(and_7_out));
  Shifter #(.width(6)) shifter_2 (.in(col2), .\dist (bit_extender_2_out), .out(shifter_2_out));
  assign bit_extender_2_out = {{2{1'b0}}, and_6_out};  // Bit_Extender bit_extender_2
  Transistor #(.\type ("n")) transistor_6 (.in(answer), .out(out_4), .gate(or_1_out));
  Pull_Resistor pull_resistor_2 (.node(out_4));
  Transistor #(.\type ("n"), .width(6)) transistor_7 (.in(corrent), .out(transistor_7_out), .gate(_1break));
  Pull_Resistor pull_resistor_3 (.node(transistor_2_out));
  Transistor #(.width(6)) transistor_8 (.in(shifter_2_out), .out(col3), .gate(_2break));
  Pull_Resistor pull_resistor_4 (.node(col3));
  Pull_Resistor pull_resistor_5 (.node(transistor_5_out));
  Pull_Resistor pull_resistor_6 (.node(transistor_4_out));
  Pull_Resistor pull_resistor_7 (.node(transistor_1_out));
  compare_6bit compare_6bit_3 (.in_1(6'b100000), .in_2(col3), .out_3(compare_6bit_3_out_3));
  assign and_8_out = col3 & black;  // AND_Gate and_8, 6 bits wide
  zero_or_not zero_or_not_2 (.in_1(and_8_out), .out_2(zero_or_not_2_out_2));
  Pull_Resistor pull_resistor_8 (.node(zero_or_not_2_out_2));
  assign and_9_out = col3 & white;  // AND_Gate and_9, 6 bits wide
  zero_or_not zero_or_not_3 (.in_1(and_9_out), .out_2(zero_or_not_3_out_2));
  Pull_Resistor pull_resistor_9 (.node(transistor_7_out));
  assign or_2_out = transistor_7_out | transistor_5_out | transistor_4_out | transistor_1_out | transistor_2_out | transistor_3_out;  // OR_Gate or_2, 6 bits wide
  Pull_Resistor pull_resistor_10 (.node(transistor_3_out));
  and and_10 (and_10_out, compare_6bit_3_out_3, zero_or_not_2_out_2);
  not not_18 (_3break, and_10_out);
  Transistor transistor_9 (.in(zero_or_not_3_out_2), .out(answer), .gate(zero_or_not_2_out_2));
  Pull_Resistor pull_resistor_11 (.node(out_5));
  Transistor #(.\type ("n"), .width(6)) transistor_10 (.in(or_2_out), .out(out_5), .gate(answer));
  Shifter #(.width(6)) shifter_3 (.in(col3), .\dist (bit_extender_3_out), .out(col4));
  assign bit_extender_3_out = {{2{1'b0}}, and_10_out};  // Bit_Extender bit_extender_3
  zero_or_not zero_or_not_4 (.in_1(and_11_out), .out_2(zero_or_not_4_out_2));
  assign and_11_out = col4 & black;  // AND_Gate and_11, 6 bits wide
  zero_or_not zero_or_not_5 (.in_1(and_12_out), .out_2(zero_or_not_5_out_2));
  assign and_12_out = col4 & white;  // AND_Gate and_12, 6 bits wide
  compare_6bit compare_6bit_4 (.in_1(6'b100000), .in_2(col4), .out_3(compare_6bit_4_out_3));
  and and_13 (and_13_out, compare_6bit_4_out_3, zero_or_not_4_out_2);
  not not_19 (_4break, and_13_out);
  Pull_Resistor pull_resistor_12 (.node(zero_or_not_4_out_2));
  Transistor transistor_11 (.in(zero_or_not_5_out_2), .out(answer), .gate(zero_or_not_4_out_2));
  assign bit_extender_4_out = {{2{1'b0}}, and_13_out};  // Bit_Extender bit_extender_4
  Shifter #(.width(6)) shifter_4 (.in(col4), .\dist (bit_extender_4_out), .out(col5));
  assign and_14_out = col5 & black;  // AND_Gate and_14, 6 bits wide
  assign and_15_out = col5 & white;  // AND_Gate and_15, 6 bits wide
  compare_6bit compare_6bit_5 (.in_1(6'b100000), .in_2(col5), .out_3(compare_6bit_5_out_3));
  and and_16 (and_16_out, compare_6bit_5_out_3, zero_or_not_6_out_2);
  not not_20 (_5break, and_16_out);
  zero_or_not zero_or_not_6 (.in_1(and_14_out), .out_2(zero_or_not_6_out_2));
  Pull_Resistor pull_resistor_13 (.node(zero_or_not_6_out_2));
  Transistor transistor_12 (.in(zero_or_not_7_out_2), .out(answer), .gate(zero_or_not_6_out_2));
  zero_or_not zero_or_not_7 (.in_1(and_15_out), .out_2(zero_or_not_7_out_2));
  assign bit_extender_5_out = {{2{1'b0}}, and_16_out};  // Bit_Extender bit_extender_5
  Shifter #(.width(6)) shifter_5 (.in(col5), .\dist (bit_extender_5_out), .out(col6));
  not not_21 (_6break, zero_or_not_8_out_2);
  zero_or_not zero_or_not_8 (.in_1(and_17_out), .out_2(zero_or_not_8_out_2));
  assign and_17_out = col6 & black;  // AND_Gate and_17, 6 bits wide
  zero_or_not zero_or_not_9 (.in_1(and_18_out), .out_2(answer));
  assign and_18_out = col6 & white;  // AND_Gate and_18, 6 bits wide

  // Other names for the same wires on the sheet: col1[5:0] = corrent
endmodule

module check_diag_ru (
  input  [5:0] in_1,
  input  [5:0] in_2,
  input  [5:0] in_3,
  input  [5:0] in_4,
  input  [5:0] in_5,
  input  [5:0] in_6,
  input  [5:0] in_7,
  input  [5:0] in_8,
  input  [5:0] in_9,
  input  [5:0] in_10,
  input  [5:0] in_11,
  input  [5:0] in_12,
  input  [5:0] column,
  input  [5:0] row,
  output out_15,
  output [5:0] out_col
);

  wire _0break_c, _0break_r, _1break_c, _1break_r, _2break_c, _2break_r, _3break_c, _3break_r, _4break_c,
       _4break_r, _5break_c, _5break_r, and_1_out, and_2_out, and_3_out, and_5_out, and_6_out, and_7_out,
       and_10_out, and_13_out, answer2, answer3, answer4, answer5, compare_6bit_1_out_3,
       compare_6bit_2_out_3, compare_6bit_3_out_3, compare_6bit_4_out_3, compare_6bit_5_out_3,
       compare_6bit_6_out_3, compare_6bit_7_out_3, compare_6bit_8_out_3, compare_6bit_9_out_3,
       compare_6bit_10_out_3, compare_6bit_11_out_3, not_1_out, not_2_out, not_5_out, not_6_out, not_7_out,
       not_8_out, not_9_out, not_10_out, not_12_out, not_13_out, not_15_out, not_16_out, not_17_out,
       not_19_out, or_1_out, or_2_out, or_3_out, or_4_out, or_5_out, or_6_out, or_7_out, or_8_out, or_9_out,
       or_10_out, or_11_out, or_12_out, or_14_out, or_15_out, or_16_out, or_17_out, or_18_out, or_19_out,
       or_20_out, or_21_out, or_22_out, or_23_out, or_24_out, or_26_out, or_27_out, or_28_out,
       pull_resistor_5_node, zero_or_not_1_out_2, zero_or_not_2_out_2, zero_or_not_3_out_2,
       zero_or_not_4_out_2, zero_or_not_5_out_2, zero_or_not_6_out_2, zero_or_not_7_out_2,
       zero_or_not_8_out_2;
  wire [2:0] bit_extender_1_out, bit_extender_2_out, bit_extender_3_out, bit_extender_4_out,
       bit_extender_5_out, bit_extender_6_out, bit_extender_7_out, bit_extender_8_out, bit_extender_9_out,
       bit_extender_10_out, n6numrow_to_3numrow_1_out_2, n6numrow_to_3numrow_2_out_2,
       n6numrow_to_3numrow_3_out_2, n6numrow_to_3numrow_4_out_2, n6numrow_to_3numrow_5_out_2,
       n6numrow_to_3numrow_6_out_2, n6numrow_to_3numrow_7_out_2, n6numrow_to_3numrow_8_out_2,
       n6numrow_to_3numrow_9_out_2;
  wire [5:0] and_16_out, and_17_out, black1, black2, black3, black4, black5, column1, column2, column3,
       column4, column5, multiplexer_1_out, multiplexer_2_out, multiplexer_3_out, multiplexer_4_out,
       multiplexer_5_out, multiplexer_6_out, multiplexer_7_out, multiplexer_8_out, multiplexer_9_out,
       or_25_out, pull_resistor_11_node, shifter_1_out, shifter_2_out, shifter_3_out, shifter_4_out,
       shifter_5_out, shifter_6_out, shifter_7_out, shifter_8_out, shifter_9_out, shifter_10_out,
       transistor_1_out, transistor_3_out, transistor_4_out, transistor_6_out, transistor_8_out, white2,
       white3, white4, white5;

  or or_1 (or_1_out, _0break_r, _0break_c);
  not not_1 (not_1_out, or_1_out);
  or or_2 (or_2_out, _1break_r, _1break_c);
  not not_2 (not_2_out, or_2_out);
  compare_6bit compare_6bit_1 (.in_1(6'b000001), .in_2(column), .out_3(compare_6bit_1_out_3));
  not not_3 (_0break_c, compare_6bit_1_out_3);
  compare_6bit compare_6bit_2 (.in_1(6'b000001), .in_2(row), .out_3(compare_6bit_2_out_3));
  not not_4 (_0break_r, compare_6bit_2_out_3);
  or or_3 (or_3_out, _3break_r, _3break_c);
  not not_5 (not_5_out, or_3_out);
  or or_4 (or_4_out, _4break_r, _4break_c);
  or or_5 (or_5_out, _2break_r, _2break_c);
  not not_6 (not_6_out, or_5_out);
  not not_7 (not_7_out, or_4_out);
  and and_1 (and_1_out, not_1_out, not_2_out, not_7_out, not_6_out, not_5_out, or_6_out);
  Transistor #(.\type ("n"), .width(6)) transistor_1 (.in(column5), .out(transistor_1_out), .gate(and_1_out));
  assign bit_extender_1_out = {{2{1'b0}}, compare_6bit_1_out_3};  // Bit_Extender bit_extender_1
  assign bit_extender_2_out = {{2{1'b0}}, compare_6bit_2_out_3};  // Bit_Extender bit_extender_2
  or or_6 (or_6_out, _5break_r, _5break_c);
  Pull_Resistor pull_resistor_1 (.node(transistor_1_out));
  or or_7 (or_7_out, _0break_r, _0break_c);
  Shifter #(.width(6), .shift("lr")) shifter_1 (.in(column), .\dist (bit_extender_1_out), .out(shifter_1_out));
  or or_8 (or_8_out, _0break_r, _0break_c);
  Shifter #(.width(6), .shift("lr")) shifter_2 (.in(row), .\dist (bit_extender_2_out), .out(shifter_2_out));
  or or_9 (or_9_out, _1break_r, _1break_c);
  not not_8 (not_8_out, or_9_out);
  or or_10 (or_10_out, _0break_r, _0break_c);
  not not_9 (not_9_out, or_10_out);
  Pull_Resistor pull_resistor_2 (.node(column1));
  Transistor #(.width(6)) transistor_2 (.in(shifter_1_out), .out(column1), .gate(or_7_out));
  Transistor #(.width(6)) transistor_3 (.in(shifter_2_out), .out(transistor_3_out), .gate(or_8_out));
  Pull_Resistor pull_resistor_3 (.node(transistor_3_out));
  _6numRow_to_3numRow u_6numrow_to_3numrow_1 (.in_1(transistor_3_out), .out_2(n6numrow_to_3numrow_1_out_2));
  or or_11 (or_11_out, _4break_r, _4break_c);
  or or_12 (or_12_out, _2break_r, _2break_c);
  not not_10 (not_10_out, or_12_out);
  and and_2 (and_2_out, not_9_out, not_8_out, or_11_out, not_10_out, not_13_out);
  Transistor #(.\type ("n"), .width(6)) transistor_4 (.in(column4), .out(transistor_4_out), .gate(and_2_out));
  Pull_Resistor pull_resistor_4 (.node(transistor_4_out));
  Pull_Resistor pull_resistor_5 (.node(pull_resistor_5_node));
  or or_13 (pull_resistor_5_node, answer2, answer3, answer4, answer5);
  compare_6bit compare_6bit_3 (.in_1(6'b000001), .in_2(column1), .out_3(compare_6bit_3_out_3));
  not not_11 (_1break_c, compare_6bit_3_out_3);
  compare_6bit compare_6bit_4 (.in_1(6'b000001), .in_2(transistor_3_out), .out_3(compare_6bit_4_out_3));
  zero_or_not zero_or_not_1 (.in_1(black1), .out_2(zero_or_not_1_out_2));
  Multiplexer #(.select(3), .width(6)) multiplexer_1 (
    .in0(in_2), .in1(in_4), .in2(in_6), .in3(in_8), .in4(in_10), .in5(in_12), .out(multiplexer_1_out),
    .sel(n6numrow_to_3numrow_1_out_2));  // open: in6, in7, en
  Pull_Resistor pull_resistor_6 (.node(column1));
  or or_14 (or_14_out, _0break_r, _0break_c);
  not not_12 (not_12_out, or_14_out);
  or or_15 (or_15_out, _3break_r, _3break_c);
  not not_13 (not_13_out, or_15_out);
  or or_16 (or_16_out, _0break_c, _0break_r, _1break_c, _1break_r, _2break_c, _2break_r, _3break_c, _3break_r, _4break_c, _4break_r, _5break_c, _5break_r);
  Transistor #(.\type ("n")) transistor_5 (.in(pull_resistor_5_node), .out(out_15), .gate(or_16_out));
  Pull_Resistor pull_resistor_7 (.node(out_15));
  assign bit_extender_3_out = {{2{1'b0}}, compare_6bit_3_out_3};  // Bit_Extender bit_extender_3
  and and_3 (and_3_out, compare_6bit_4_out_3, zero_or_not_1_out_2);
  not not_14 (_1break_r, and_3_out);
  assign black1 = multiplexer_1_out & column1;  // AND_Gate and_4, 6 bits wide
  or or_17 (or_17_out, _1break_r, _1break_c);
  not not_15 (not_15_out, or_17_out);
  or or_18 (or_18_out, _1break_r, _1break_c);
  Shifter #(.width(6), .shift("lr")) shifter_3 (.in(column1), .\dist (bit_extender_3_out), .out(shifter_3_out));
  Shifter #(.width(6), .shift("lr")) shifter_4 (
    .in(transistor_3_out), .\dist (bit_extender_4_out), .out(shifter_4_out));
  assign bit_extender_4_out = {{2{1'b0}}, and_3_out};  // Bit_Extender bit_extender_4
  or or_19 (or_19_out, _2break_r, _2break_c);
  not not_16 (not_16_out, or_19_out);
  or or_20 (or_20_out, _3break_r, _3break_c);
  and and_5 (and_5_out, not_12_out, not_15_out, not_16_out, or_20_out);
  Transistor #(.\type ("n"), .width(6)) transistor_6 (.in(column3), .out(transistor_6_out), .gate(and_5_out));
  Pull_Resistor pull_resistor_8 (.node(transistor_6_out));
  Pull_Resistor pull_resistor_9 (.node(column2));
  Transistor #(.width(6)) transistor_7 (.in(shifter_3_out), .out(column2), .gate(or_18_out));
  or or_21 (or_21_out, _1break_r, _1break_c);
  Transistor #(.width(6)) transistor_8 (.in(shifter_4_out), .out(transistor_8_out), .gate(or_21_out));
  Pull_Resistor pull_resistor_10 (.node(transistor_8_out));
  or or_22 (or_22_out, _0break_r, _0break_c);
  not not_17 (not_17_out, or_22_out);
  compare_6bit compare_6bit_5 (.in_1(6'b000001), .in_2(column2), .out_3(compare_6bit_5_out_3));
  not not_18 (_2break_c, compare_6bit_5_out_3);
  _6numRow_to_3numRow u_6numrow_to_3numrow_2 (.in_1(transistor_8_out), .out_2(n6numrow_to_3numrow_2_out_2));
  Multiplexer #(.select(3), .width(6)) multiplexer_2 (
    .in0(in_2), .in1(in_4), .in2(in_6), .in3(in_8), .in4(in_10), .in5(in_12), .out(multiplexer_2_out),
    .sel(n6numrow_to_3numrow_2_out_2));  // open: in6, in7, en
  _6numRow_to_3numRow u_6numrow_to_3numrow_3 (.in_1(transistor_8_out), .out_2(n6numrow_to_3numrow_3_out_2));
  Multiplexer #(.select(3), .width(6)) multiplexer_3 (
    .in0(in_1), .in1(in_3), .in2(in_5), .in3(in_7), .in4(in_9), .in5(in_11), .out(multiplexer_3_out),
    .sel(n6numrow_to_3numrow_3_out_2));  // open: in6, in7, en
  or or_23 (or_23_out, _1break_r, _1break_c);
  not not_19 (not_19_out, or_23_out);
  or or_24 (or_24_out, _2break_r, _2break_c);
  and and_6 (and_6_out, not_17_out, not_19_out, or_24_out);
  Pull_Resistor pull_resistor_11 (.node(pull_resistor_11_node));
  Transistor #(.\type ("n"), .width(6)) transistor_9 (.in(column2), .out(pull_resistor_11_node), .gate(and_6_out));
  assign bit_extender_5_out = {{2{1'b0}}, compare_6bit_5_out_3};  // Bit_Extender bit_extender_5
  compare_6bit compare_6bit_6 (.in_1(6'b000001), .in_2(transistor_8_out), .out_3(compare_6bit_6_out_3));
  and and_7 (and_7_out, compare_6bit_6_out_3, zero_or_not_2_out_2);
  not not_20 (_2break_r, and_7_out);
  zero_or_not zero_or_not_2 (.in_1(black2), .out_2(zero_or_not_2_out_2));
  Pull_Resistor pull_resistor_12 (.node(zero_or_not_2_out_2));
  zero_or_not zero_or_not_3 (.in_1(white2), .out_2(zero_or_not_3_out_2));
  Transistor transistor_10 (.in(zero_or_not_3_out_2), .out(answer2), .gate(zero_or_not_2_out_2));
  Pull_Resistor pull_resistor_13 (.node(answer2));
  assign black2 = multiplexer_2_out & column2;  // AND_Gate and_8, 6 bits wide
  Pull_Resistor pull_resistor_14 (.node(column2));
  assign white2 = multiplexer_3_out & column2;  // AND_Gate and_9, 6 bits wide
  Pull_Resistor pull_resistor_15 (.node(column2));
  assign or_25_out = pull_resistor_11_node | transistor_6_out | transistor_4_out | transistor_1_out;  // OR_Gate or_25, 6 bits wide
  Shifter #(.width(6), .shift("lr")) shifter_5 (.in(column2), .\dist (bit_extender_5_out), .out(shifter_5_out));
  assign bit_extender_6_out = {{2{1'b0}}, and_7_out};  // Bit_Extender bit_extender_6
  Pull_Resistor pull_resistor_16 (.node(out_col));
  Transistor #(.\type ("n"), .width(6)) transistor_11 (.in(or_25_out), .out(out_col), .gate(out_15));
  or or_26 (or_26_out, _2break_r, _2break_c);
  Transistor #(.width(6)) transistor_12 (.in(shifter_5_out), .out(column3), .gate(or_26_out));
  Pull_Resistor pull_resistor_17 (.node(column3));
  Shifter #(.width(6), .shift("lr")) shifter_6 (
    .in(transistor_8_out), .\dist (bit_extender_6_out), .out(shifter_6_out));
  compare_6bit compare_6bit_7 (.in_1(6'b000001), .in_2(column3), .out_3(compare_6bit_7_out_3));
  not not_21 (_3break_c, compare_6bit_7_out_3);
  _6numRow_to_3numRow u_6numrow_to_3numrow_4 (.in_1(shifter_6_out), .out_2(n6numrow_to_3numrow_4_out_2));
  _6numRow_to_3numRow u_6numrow_to_3numrow_5 (.in_1(shifter_6_out), .out_2(n6numrow_to_3numrow_5_out_2));
  assign bit_extender_7_out = {{2{1'b0}}, compare_6bit_7_out_3};  // Bit_Extender bit_extender_7
  compare_6bit compare_6bit_8 (.in_1(6'b000001), .in_2(shifter_6_out), .out_3(compare_6bit_8_out_3));
  zero_or_not zero_or_not_4 (.in_1(black3), .out_2(zero_or_not_4_out_2));
  Pull_Resistor pull_resistor_18 (.node(zero_or_not_4_out_2));
  zero_or_not zero_or_not_5 (.in_1(white3), .out_2(zero_or_not_5_out_2));
  Multiplexer #(.select(3), .width(6)) multiplexer_4 (
    .in0(in_2), .in1(in_4), .in2(in_6), .in3(in_8), .in4(in_10), .in5(in_12), .out(multiplexer_4_out),
    .sel(n6numrow_to_3numrow_4_out_2));  // open: in6, in7, en
  Pull_Resistor pull_resistor_19 (.node(column3));
  Multiplexer #(.select(3), .width(6)) multiplexer_5 (
    .in0(in_1), .in1(in_3), .in2(in_5), .in3(in_7), .in4(in_9), .in5(in_11), .out(multiplexer_5_out),
    .sel(n6numrow_to_3numrow_5_out_2));  // open: in6, in7, en
  Pull_Resistor pull_resistor_20 (.node(column3));
  Shifter #(.width(6), .shift("lr")) shifter_7 (.in(column3), .\dist (bit_extender_7_out), .out(shifter_7_out));
  and and_10 (and_10_out, compare_6bit_8_out_3, zero_or_not_4_out_2);
  not not_22 (_3break_r, and_10_out);
  Pull_Resistor pull_resistor_21 (.node(answer3));
  Transistor transistor_13 (.in(zero_or_not_5_out_2), .out(answer3), .gate(zero_or_not_4_out_2));
  assign black3 = multiplexer_4_out & column3;  // AND_Gate and_11, 6 bits wide
  assign white3 = multiplexer_5_out & column3;  // AND_Gate and_12, 6 bits wide
  or or_27 (or_27_out, _3break_r, _3break_c);
  Pull_Resistor pull_resistor_22 (.node(column4));
  Transistor #(.width(6)) transistor_14 (.in(shifter_7_out), .out(column4), .gate(or_27_out));
  Shifter #(.width(6), .shift("lr")) shifter_8 (.in(shifter_6_out), .\dist (bit_extender_8_out), .out(shifter_8_out));
  assign bit_extender_8_out = {{2{1'b0}}, and_10_out};  // Bit_Extender bit_extender_8
  compare_6bit compare_6bit_9 (.in_1(6'b000001), .in_2(column4), .out_3(compare_6bit_9_out_3));
  not not_23 (_4break_c, compare_6bit_9_out_3);
  assign bit_extender_9_out = {{2{1'b0}}, compare_6bit_9_out_3};  // Bit_Extender bit_extender_9
  _6numRow_to_3numRow u_6numrow_to_3numrow_6 (.in_1(shifter_8_out), .out_2(n6numrow_to_3numrow_6_out_2));
  Multiplexer #(.select(3), .width(6)) multiplexer_6 (
    .in0(in_2), .in1(in_4), .in2(in_6), .in3(in_8), .in4(in_10), .in5(in_12), .out(multiplexer_6_out),
    .sel(n6numrow_to_3numrow_6_out_2));  // open: in6, in7, en
  _6numRow_to_3numRow u_6numrow_to_3numrow_7 (.in_1(shifter_8_out), .out_2(n6numrow_to_3numrow_7_out_2));
  Multiplexer #(.select(3), .width(6)) multiplexer_7 (
    .in0(in_1), .in1(in_3), .in2(in_5), .in3(in_7), .in4(in_9), .in5(in_11), .out(multiplexer_7_out),
    .sel(n6numrow_to_3numrow_7_out_2));  // open: in6, in7, en
  Shifter #(.width(6), .shift("lr")) shifter_9 (.in(column4), .\dist (bit_extender_9_out), .out(shifter_9_out));
  compare_6bit compare_6bit_10 (.in_1(6'b000001), .in_2(shifter_8_out), .out_3(compare_6bit_10_out_3));
  and and_13 (and_13_out, compare_6bit_10_out_3, zero_or_not_6_out_2);
  zero_or_not zero_or_not_6 (.in_1(black4), .out_2(zero_or_not_6_out_2));
  not not_24 (_4break_r, and_13_out);
  Pull_Resistor pull_resistor_23 (.node(zero_or_not_6_out_2));
  Pull_Resistor pull_resistor_24 (.node(answer4));
  zero_or_not zero_or_not_7 (.in_1(white4), .out_2(zero_or_not_7_out_2));
  Transistor transistor_15 (.in(zero_or_not_7_out_2), .out(answer4), .gate(zero_or_not_6_out_2));
  assign black4 = multiplexer_6_out & column4;  // AND_Gate and_14, 6 bits wide
  Pull_Resistor pull_resistor_25 (.node(column4));
  assign white4 = multiplexer_7_out & column4;  // AND_Gate and_15, 6 bits wide
  Pull_Resistor pull_resistor_26 (.node(column4));
  or or_28 (or_28_out, _4break_r, _4break_c);
  Transistor #(.width(6)) transistor_16 (.in(shifter_9_out), .out(column5), .gate(or_28_out));
  Pull_Resistor pull_resistor_27 (.node(column5));
  assign bit_extender_10_out = {{2{1'b0}}, and_13_out};  // Bit_Extender bit_extender_10
  compare_6bit compare_6bit_11 (.in_1(6'b000001), .in_2(column5), .out_3(compare_6bit_11_out_3));
  Shifter #(.width(6), .shift("lr")) shifter_10 (
    .in(shifter_8_out), .\dist (bit_extender_10_out), .out(shifter_10_out));
  _6numRow_to_3numRow u_6numrow_to_3numrow_8 (.in_1(shifter_10_out), .out_2(n6numrow_to_3numrow_8_out_2));
  _6numRow_to_3numRow u_6numrow_to_3numrow_9 (.in_1(shifter_10_out), .out_2(n6numrow_to_3numrow_9_out_2));
  not not_25 (_5break_c, compare_6bit_11_out_3);
  zero_or_not zero_or_not_8 (.in_1(and_16_out), .out_2(zero_or_not_8_out_2));
  assign and_16_out = shifter_10_out & black5;  // AND_Gate and_16, 6 bits wide
  zero_or_not zero_or_not_9 (.in_1(and_17_out), .out_2(answer5));
  assign and_17_out = shifter_10_out & white5;  // AND_Gate and_17, 6 bits wide
  Multiplexer #(.select(3), .width(6)) multiplexer_8 (
    .in0(in_2), .in1(in_4), .in2(in_6), .in3(in_8), .in4(in_10), .in5(in_12), .out(multiplexer_8_out),
    .sel(n6numrow_to_3numrow_8_out_2));  // open: in6, in7, en
  Pull_Resistor pull_resistor_28 (.node(column5));
  Multiplexer #(.select(3), .width(6)) multiplexer_9 (
    .in0(in_1), .in1(in_3), .in2(in_5), .in3(in_7), .in4(in_9), .in5(in_11), .out(multiplexer_9_out),
    .sel(n6numrow_to_3numrow_9_out_2));  // open: in6, in7, en
  Pull_Resistor pull_resistor_29 (.node(column5));
  not not_26 (_5break_r, zero_or_not_8_out_2);
  assign black5 = multiplexer_8_out & column5;  // AND_Gate and_18, 6 bits wide
  assign white5 = multiplexer_9_out & column5;  // AND_Gate and_19, 6 bits wide

  // Other names for the same wires on the sheet: _0b[5:0] = in_2; _0w[5:0] = in_1; _1b[5:0] = in_4; _1w[5:0] = in_3;
  //   _2b[5:0] = in_6; _2w[5:0] = in_5; _3b[5:0] = in_8; _3w[5:0] = in_7; _4b[5:0] = in_10; _4w[5:0] = in_9;
  //   _5b[5:0] = in_12; _5w[5:0] = in_11; fin_answer = out_15
endmodule
module check_diag_rd (
  input  [5:0] in_1,
  input  [5:0] in_2,
  input  [5:0] in_3,
  input  [5:0] in_4,
  input  [5:0] in_5,
  input  [5:0] in_6,
  input  [5:0] in_7,
  input  [5:0] in_8,
  input  [5:0] in_9,
  input  [5:0] in_10,
  input  [5:0] in_11,
  input  [5:0] in_12,
  input  [5:0] column,
  input  [5:0] row,
  output out_15,
  output [5:0] out_col
);

  wire _0break_c, _0break_r, _1break_c, _1break_r, _2break_c, _2break_r, _3break_c, _3break_r, _4break_c,
       _4break_r, _5break_c, _5break_r, and_1_out, and_2_out, and_3_out, and_5_out, and_6_out, and_7_out,
       and_10_out, and_13_out, answer2, answer3, answer4, answer5, compare_6bit_1_out_3,
       compare_6bit_2_out_3, compare_6bit_3_out_3, compare_6bit_4_out_3, compare_6bit_5_out_3,
       compare_6bit_6_out_3, compare_6bit_7_out_3, compare_6bit_8_out_3, compare_6bit_9_out_3,
       compare_6bit_10_out_3, compare_6bit_11_out_3, not_1_out, not_2_out, not_5_out, not_6_out, not_7_out,
       not_8_out, not_9_out, not_10_out, not_12_out, not_13_out, not_15_out, not_16_out, not_17_out,
       not_19_out, or_1_out, or_2_out, or_3_out, or_4_out, or_5_out, or_6_out, or_7_out, or_8_out, or_9_out,
       or_10_out, or_11_out, or_12_out, or_13_out, or_14_out, or_15_out, or_16_out, or_17_out, or_18_out,
       or_19_out, or_20_out, or_21_out, or_22_out, or_23_out, or_24_out, or_26_out, or_27_out, or_28_out,
       zero_or_not_1_out_2, zero_or_not_2_out_2, zero_or_not_3_out_2, zero_or_not_4_out_2,
       zero_or_not_5_out_2, zero_or_not_6_out_2, zero_or_not_7_out_2, zero_or_not_8_out_2;
  wire [2:0] bit_extender_1_out, bit_extender_2_out, bit_extender_3_out, bit_extender_4_out,
       bit_extender_5_out, bit_extender_6_out, bit_extender_7_out, bit_extender_8_out, bit_extender_9_out,
       bit_extender_10_out, n6numrow_to_3numrow_1_out_2, n6numrow_to_3numrow_2_out_2,
       n6numrow_to_3numrow_3_out_2, n6numrow_to_3numrow_4_out_2, n6numrow_to_3numrow_5_out_2,
       n6numrow_to_3numrow_6_out_2, n6numrow_to_3numrow_7_out_2, n6numrow_to_3numrow_8_out_2,
       n6numrow_to_3numrow_9_out_2;
  wire [5:0] and_16_out, and_17_out, black1, black2, black3, black4, black5, column1, column2, column3,
       column4, column5, multiplexer_1_out, multiplexer_2_out, multiplexer_3_out, multiplexer_4_out,
       multiplexer_5_out, multiplexer_6_out, multiplexer_7_out, multiplexer_8_out, multiplexer_9_out,
       or_25_out, pull_resistor_4_node, pull_resistor_11_node, shifter_1_out, shifter_2_out, shifter_3_out,
       shifter_4_out, shifter_5_out, shifter_6_out, shifter_7_out, shifter_8_out, shifter_9_out,
       shifter_10_out, transistor_1_out, transistor_3_out, transistor_6_out, transistor_8_out, white2,
       white3, white4, white5;

  or or_1 (or_1_out, _0break_r, _0break_c);
  not not_1 (not_1_out, or_1_out);
  or or_2 (or_2_out, _1break_r, _1break_c);
  not not_2 (not_2_out, or_2_out);
  compare_6bit compare_6bit_1 (.in_1(6'b000001), .in_2(column), .out_3(compare_6bit_1_out_3));
  not not_3 (_0break_c, compare_6bit_1_out_3);
  compare_6bit compare_6bit_2 (.in_1(6'b100000), .in_2(row), .out_3(compare_6bit_2_out_3));
  not not_4 (_0break_r, compare_6bit_2_out_3);
  or or_3 (or_3_out, _3break_r, _3break_c);
  not not_5 (not_5_out, or_3_out);
  or or_4 (or_4_out, _4break_r, _4break_c);
  or or_5 (or_5_out, _2break_r, _2break_c);
  not not_6 (not_6_out, or_5_out);
  not not_7 (not_7_out, or_4_out);
  and and_1 (and_1_out, not_1_out, not_2_out, not_7_out, not_6_out, not_5_out, or_6_out);
  Transistor #(.\type ("n"), .width(6)) transistor_1 (.in(column5), .out(transistor_1_out), .gate(and_1_out));
  assign bit_extender_1_out = {{2{1'b0}}, compare_6bit_1_out_3};  // Bit_Extender bit_extender_1
  assign bit_extender_2_out = {{2{1'b0}}, compare_6bit_2_out_3};  // Bit_Extender bit_extender_2
  or or_6 (or_6_out, _5break_r, _5break_c);
  Pull_Resistor pull_resistor_1 (.node(transistor_1_out));
  or or_7 (or_7_out, _0break_r, _0break_c);
  Shifter #(.width(6), .shift("lr")) shifter_1 (.in(column), .\dist (bit_extender_1_out), .out(shifter_1_out));
  or or_8 (or_8_out, _0break_r, _0break_c);
  Shifter #(.width(6)) shifter_2 (.in(row), .\dist (bit_extender_2_out), .out(shifter_2_out));
  or or_9 (or_9_out, _1break_r, _1break_c);
  not not_8 (not_8_out, or_9_out);
  or or_10 (or_10_out, _0break_r, _0break_c);
  not not_9 (not_9_out, or_10_out);
  Pull_Resistor pull_resistor_2 (.node(column1));
  Transistor #(.width(6)) transistor_2 (.in(shifter_1_out), .out(column1), .gate(or_7_out));
  Transistor #(.width(6)) transistor_3 (.in(shifter_2_out), .out(transistor_3_out), .gate(or_8_out));
  Pull_Resistor pull_resistor_3 (.node(transistor_3_out));
  _6numRow_to_3numRow u_6numrow_to_3numrow_1 (.in_1(transistor_3_out), .out_2(n6numrow_to_3numrow_1_out_2));
  or or_11 (or_11_out, _4break_r, _4break_c);
  or or_12 (or_12_out, _2break_r, _2break_c);
  not not_10 (not_10_out, or_12_out);
  and and_2 (and_2_out, not_9_out, not_8_out, or_11_out, not_10_out, not_13_out);
  Pull_Resistor pull_resistor_4 (.node(pull_resistor_4_node));
  Transistor #(.\type ("n"), .width(6)) transistor_4 (.in(column4), .out(pull_resistor_4_node), .gate(and_2_out));
  or or_13 (or_13_out, answer2, answer3, answer4, answer5);
  Pull_Resistor pull_resistor_5 (.node(or_13_out));
  compare_6bit compare_6bit_3 (.in_1(6'b000001), .in_2(column1), .out_3(compare_6bit_3_out_3));
  not not_11 (_1break_c, compare_6bit_3_out_3);
  compare_6bit compare_6bit_4 (.in_1(6'b100000), .in_2(transistor_3_out), .out_3(compare_6bit_4_out_3));
  zero_or_not zero_or_not_1 (.in_1(black1), .out_2(zero_or_not_1_out_2));
  Multiplexer #(.select(3), .width(6)) multiplexer_1 (
    .in0(in_2), .in1(in_4), .in2(in_6), .in3(in_8), .in4(in_10), .in5(in_12), .out(multiplexer_1_out),
    .sel(n6numrow_to_3numrow_1_out_2));  // open: in6, in7, en
  Pull_Resistor pull_resistor_6 (.node(column1));
  or or_14 (or_14_out, _0break_r, _0break_c);
  or or_15 (or_15_out, _3break_r, _3break_c);
  not not_12 (not_12_out, or_14_out);
  not not_13 (not_13_out, or_15_out);
  or or_16 (or_16_out, _0break_c, _0break_r, _1break_c, _1break_r, _2break_c, _2break_r, _3break_c, _3break_r, _4break_c, _4break_r, _5break_c, _5break_r);
  Transistor #(.\type ("n")) transistor_5 (.in(or_13_out), .out(out_15), .gate(or_16_out));
  Pull_Resistor pull_resistor_7 (.node(out_15));
  assign bit_extender_3_out = {{2{1'b0}}, compare_6bit_3_out_3};  // Bit_Extender bit_extender_3
  and and_3 (and_3_out, compare_6bit_4_out_3, zero_or_not_1_out_2);
  not not_14 (_1break_r, and_3_out);
  assign black1 = multiplexer_1_out & column1;  // AND_Gate and_4, 6 bits wide
  or or_17 (or_17_out, _1break_r, _1break_c);
  not not_15 (not_15_out, or_17_out);
  or or_18 (or_18_out, _1break_r, _1break_c);
  Shifter #(.width(6), .shift("lr")) shifter_3 (.in(column1), .\dist (bit_extender_3_out), .out(shifter_3_out));
  Shifter #(.width(6)) shifter_4 (.in(transistor_3_out), .\dist (bit_extender_4_out), .out(shifter_4_out));
  assign bit_extender_4_out = {{2{1'b0}}, and_3_out};  // Bit_Extender bit_extender_4
  or or_19 (or_19_out, _2break_r, _2break_c);
  not not_16 (not_16_out, or_19_out);
  or or_20 (or_20_out, _3break_r, _3break_c);
  and and_5 (and_5_out, not_12_out, not_15_out, not_16_out, or_20_out);
  Transistor #(.\type ("n"), .width(6)) transistor_6 (.in(column3), .out(transistor_6_out), .gate(and_5_out));
  Pull_Resistor pull_resistor_8 (.node(transistor_6_out));
  Transistor #(.width(6)) transistor_7 (.in(shifter_3_out), .out(column2), .gate(or_18_out));
  Pull_Resistor pull_resistor_9 (.node(column2));
  or or_21 (or_21_out, _1break_r, _1break_c);
  Transistor #(.width(6)) transistor_8 (.in(shifter_4_out), .out(transistor_8_out), .gate(or_21_out));
  Pull_Resistor pull_resistor_10 (.node(transistor_8_out));
  or or_22 (or_22_out, _0break_r, _0break_c);
  not not_17 (not_17_out, or_22_out);
  compare_6bit compare_6bit_5 (.in_1(6'b000001), .in_2(column2), .out_3(compare_6bit_5_out_3));
  not not_18 (_2break_c, compare_6bit_5_out_3);
  _6numRow_to_3numRow u_6numrow_to_3numrow_2 (.in_1(transistor_8_out), .out_2(n6numrow_to_3numrow_2_out_2));
  Multiplexer #(.select(3), .width(6)) multiplexer_2 (
    .in0(in_2), .in1(in_4), .in2(in_6), .in3(in_8), .in4(in_10), .in5(in_12), .out(multiplexer_2_out),
    .sel(n6numrow_to_3numrow_2_out_2));  // open: in6, in7, en
  _6numRow_to_3numRow u_6numrow_to_3numrow_3 (.in_1(transistor_8_out), .out_2(n6numrow_to_3numrow_3_out_2));
  Multiplexer #(.select(3), .width(6)) multiplexer_3 (
    .in0(in_1), .in1(in_3), .in2(in_5), .in3(in_7), .in4(in_9), .in5(in_11), .out(multiplexer_3_out),
    .sel(n6numrow_to_3numrow_3_out_2));  // open: in6, in7, en
  or or_23 (or_23_out, _1break_r, _1break_c);
  or or_24 (or_24_out, _2break_r, _2break_c);
  not not_19 (not_19_out, or_23_out);
  and and_6 (and_6_out, not_17_out, not_19_out, or_24_out);
  Pull_Resistor pull_resistor_11 (.node(pull_resistor_11_node));
  Transistor #(.\type ("n"), .width(6)) transistor_9 (.in(column2), .out(pull_resistor_11_node), .gate(and_6_out));
  assign bit_extender_5_out = {{2{1'b0}}, compare_6bit_5_out_3};  // Bit_Extender bit_extender_5
  compare_6bit compare_6bit_6 (.in_1(6'b100000), .in_2(transistor_8_out), .out_3(compare_6bit_6_out_3));
  and and_7 (and_7_out, compare_6bit_6_out_3, zero_or_not_2_out_2);
  zero_or_not zero_or_not_2 (.in_1(black2), .out_2(zero_or_not_2_out_2));
  not not_20 (_2break_r, and_7_out);
  Pull_Resistor pull_resistor_12 (.node(zero_or_not_2_out_2));
  Pull_Resistor pull_resistor_13 (.node(answer2));
  Transistor transistor_10 (.in(zero_or_not_3_out_2), .out(answer2), .gate(zero_or_not_2_out_2));
  zero_or_not zero_or_not_3 (.in_1(white2), .out_2(zero_or_not_3_out_2));
  assign black2 = multiplexer_2_out & column2;  // AND_Gate and_8, 6 bits wide
  Pull_Resistor pull_resistor_14 (.node(column2));
  assign white2 = multiplexer_3_out & column2;  // AND_Gate and_9, 6 bits wide
  Pull_Resistor pull_resistor_15 (.node(column2));
  assign or_25_out = pull_resistor_11_node | transistor_6_out | pull_resistor_4_node | transistor_1_out;  // OR_Gate or_25, 6 bits wide
  Shifter #(.width(6), .shift("lr")) shifter_5 (.in(column2), .\dist (bit_extender_5_out), .out(shifter_5_out));
  assign bit_extender_6_out = {{2{1'b0}}, and_7_out};  // Bit_Extender bit_extender_6
  Pull_Resistor pull_resistor_16 (.node(out_col));
  Transistor #(.\type ("n"), .width(6)) transistor_11 (.in(or_25_out), .out(out_col), .gate(out_15));
  or or_26 (or_26_out, _2break_r, _2break_c);
  Transistor #(.width(6)) transistor_12 (.in(shifter_5_out), .out(column3), .gate(or_26_out));
  Pull_Resistor pull_resistor_17 (.node(column3));
  Shifter #(.width(6)) shifter_6 (.in(transistor_8_out), .\dist (bit_extender_6_out), .out(shifter_6_out));
  compare_6bit compare_6bit_7 (.in_1(6'b000001), .in_2(column3), .out_3(compare_6bit_7_out_3));
  not not_21 (_3break_c, compare_6bit_7_out_3);
  _6numRow_to_3numRow u_6numrow_to_3numrow_4 (.in_1(shifter_6_out), .out_2(n6numrow_to_3numrow_4_out_2));
  _6numRow_to_3numRow u_6numrow_to_3numrow_5 (.in_1(shifter_6_out), .out_2(n6numrow_to_3numrow_5_out_2));
  assign bit_extender_7_out = {{2{1'b0}}, compare_6bit_7_out_3};  // Bit_Extender bit_extender_7
  compare_6bit compare_6bit_8 (.in_1(6'b100000), .in_2(shifter_6_out), .out_3(compare_6bit_8_out_3));
  zero_or_not zero_or_not_4 (.in_1(black3), .out_2(zero_or_not_4_out_2));
  Pull_Resistor pull_resistor_18 (.node(zero_or_not_4_out_2));
  zero_or_not zero_or_not_5 (.in_1(white3), .out_2(zero_or_not_5_out_2));
  Multiplexer #(.select(3), .width(6)) multiplexer_4 (
    .in0(in_2), .in1(in_4), .in2(in_6), .in3(in_8), .in4(in_10), .in5(in_12), .out(multiplexer_4_out),
    .sel(n6numrow_to_3numrow_4_out_2));  // open: in6, in7, en
  Pull_Resistor pull_resistor_19 (.node(column3));
  Multiplexer #(.select(3), .width(6)) multiplexer_5 (
    .in0(in_1), .in1(in_3), .in2(in_5), .in3(in_7), .in4(in_9), .in5(in_11), .out(multiplexer_5_out),
    .sel(n6numrow_to_3numrow_5_out_2));  // open: in6, in7, en
  Pull_Resistor pull_resistor_20 (.node(column3));
  Shifter #(.width(6), .shift("lr")) shifter_7 (.in(column3), .\dist (bit_extender_7_out), .out(shifter_7_out));
  and and_10 (and_10_out, compare_6bit_8_out_3, zero_or_not_4_out_2);
  not not_22 (_3break_r, and_10_out);
  Transistor transistor_13 (.in(zero_or_not_5_out_2), .out(answer3), .gate(zero_or_not_4_out_2));
  Pull_Resistor pull_resistor_21 (.node(answer3));
  assign black3 = multiplexer_4_out & column3;  // AND_Gate and_11, 6 bits wide
  assign white3 = multiplexer_5_out & column3;  // AND_Gate and_12, 6 bits wide
  or or_27 (or_27_out, _3break_r, _3break_c);
  Transistor #(.width(6)) transistor_14 (.in(shifter_7_out), .out(column4), .gate(or_27_out));
  Pull_Resistor pull_resistor_22 (.node(column4));
  Shifter #(.width(6)) shifter_8 (.in(shifter_6_out), .\dist (bit_extender_8_out), .out(shifter_8_out));
  assign bit_extender_8_out = {{2{1'b0}}, and_10_out};  // Bit_Extender bit_extender_8
  compare_6bit compare_6bit_9 (.in_1(6'b000001), .in_2(column4), .out_3(compare_6bit_9_out_3));
  not not_23 (_4break_c, compare_6bit_9_out_3);
  assign bit_extender_9_out = {{2{1'b0}}, compare_6bit_9_out_3};  // Bit_Extender bit_extender_9
  _6numRow_to_3numRow u_6numrow_to_3numrow_6 (.in_1(shifter_8_out), .out_2(n6numrow_to_3numrow_6_out_2));
  Multiplexer #(.select(3), .width(6)) multiplexer_6 (
    .in0(in_2), .in1(in_4), .in2(in_6), .in3(in_8), .in4(in_10), .in5(in_12), .out(multiplexer_6_out),
    .sel(n6numrow_to_3numrow_6_out_2));  // open: in6, in7, en
  _6numRow_to_3numRow u_6numrow_to_3numrow_7 (.in_1(shifter_8_out), .out_2(n6numrow_to_3numrow_7_out_2));
  Multiplexer #(.select(3), .width(6)) multiplexer_7 (
    .in0(in_1), .in1(in_3), .in2(in_5), .in3(in_7), .in4(in_9), .in5(in_11), .out(multiplexer_7_out),
    .sel(n6numrow_to_3numrow_7_out_2));  // open: in6, in7, en
  Shifter #(.width(6), .shift("lr")) shifter_9 (.in(column4), .\dist (bit_extender_9_out), .out(shifter_9_out));
  compare_6bit compare_6bit_10 (.in_1(6'b100000), .in_2(shifter_8_out), .out_3(compare_6bit_10_out_3));
  and and_13 (and_13_out, compare_6bit_10_out_3, zero_or_not_6_out_2);
  zero_or_not zero_or_not_6 (.in_1(black4), .out_2(zero_or_not_6_out_2));
  not not_24 (_4break_r, and_13_out);
  Pull_Resistor pull_resistor_23 (.node(zero_or_not_6_out_2));
  Transistor transistor_15 (.in(zero_or_not_7_out_2), .out(answer4), .gate(zero_or_not_6_out_2));
  zero_or_not zero_or_not_7 (.in_1(white4), .out_2(zero_or_not_7_out_2));
  Pull_Resistor pull_resistor_24 (.node(answer4));
  assign black4 = multiplexer_6_out & column4;  // AND_Gate and_14, 6 bits wide
  Pull_Resistor pull_resistor_25 (.node(column4));
  assign white4 = multiplexer_7_out & column4;  // AND_Gate and_15, 6 bits wide
  Pull_Resistor pull_resistor_26 (.node(column4));
  or or_28 (or_28_out, _4break_r, _4break_c);
  Pull_Resistor pull_resistor_27 (.node(column5));
  Transistor #(.width(6)) transistor_16 (.in(shifter_9_out), .out(column5), .gate(or_28_out));
  assign bit_extender_10_out = {{2{1'b0}}, and_13_out};  // Bit_Extender bit_extender_10
  compare_6bit compare_6bit_11 (.in_1(6'b000001), .in_2(column5), .out_3(compare_6bit_11_out_3));
  Shifter #(.width(6)) shifter_10 (.in(shifter_8_out), .\dist (bit_extender_10_out), .out(shifter_10_out));
  _6numRow_to_3numRow u_6numrow_to_3numrow_8 (.in_1(shifter_10_out), .out_2(n6numrow_to_3numrow_8_out_2));
  _6numRow_to_3numRow u_6numrow_to_3numrow_9 (.in_1(shifter_10_out), .out_2(n6numrow_to_3numrow_9_out_2));
  not not_25 (_5break_c, compare_6bit_11_out_3);
  zero_or_not zero_or_not_8 (.in_1(and_16_out), .out_2(zero_or_not_8_out_2));
  assign and_16_out = shifter_10_out & black5;  // AND_Gate and_16, 6 bits wide
  zero_or_not zero_or_not_9 (.in_1(and_17_out), .out_2(answer5));
  assign and_17_out = shifter_10_out & white5;  // AND_Gate and_17, 6 bits wide
  Multiplexer #(.select(3), .width(6)) multiplexer_8 (
    .in0(in_2), .in1(in_4), .in2(in_6), .in3(in_8), .in4(in_10), .in5(in_12), .out(multiplexer_8_out),
    .sel(n6numrow_to_3numrow_8_out_2));  // open: in6, in7, en
  Pull_Resistor pull_resistor_28 (.node(column5));
  Multiplexer #(.select(3), .width(6)) multiplexer_9 (
    .in0(in_1), .in1(in_3), .in2(in_5), .in3(in_7), .in4(in_9), .in5(in_11), .out(multiplexer_9_out),
    .sel(n6numrow_to_3numrow_9_out_2));  // open: in6, in7, en
  Pull_Resistor pull_resistor_29 (.node(column5));
  not not_26 (_5break_r, zero_or_not_8_out_2);
  assign black5 = multiplexer_8_out & column5;  // AND_Gate and_18, 6 bits wide
  assign white5 = multiplexer_9_out & column5;  // AND_Gate and_19, 6 bits wide

  // Other names for the same wires on the sheet: _0b[5:0] = in_2; _0w[5:0] = in_1; _1b[5:0] = in_4; _1w[5:0] = in_3;
  //   _2b[5:0] = in_6; _2w[5:0] = in_5; _3b[5:0] = in_8; _3w[5:0] = in_7; _4b[5:0] = in_10; _4w[5:0] = in_9;
  //   _5b[5:0] = in_12; _5w[5:0] = in_11; fin_answer = out_15
endmodule

module check_diag_lu (
  input  [5:0] in_1,
  input  [5:0] in_2,
  input  [5:0] in_3,
  input  [5:0] in_4,
  input  [5:0] in_5,
  input  [5:0] in_6,
  input  [5:0] in_7,
  input  [5:0] in_8,
  input  [5:0] in_9,
  input  [5:0] in_10,
  input  [5:0] in_11,
  input  [5:0] in_12,
  input  [5:0] column,
  input  [5:0] row,
  output out_15,
  output [5:0] out_col
);

  wire _0break_c, _0break_r, _1break_c, _1break_r, _2break_c, _2break_r, _3break_c, _3break_r, _4break_c,
       _4break_r, _5break_c, _5break_r, and_1_out, and_2_out, and_3_out, and_5_out, and_6_out, and_7_out,
       and_10_out, and_13_out, answer2, answer3, answer4, answer5, compare_6bit_3_out_3,
       compare_6bit_4_out_3, compare_6bit_5_out_3, compare_6bit_6_out_3, compare_6bit_7_out_3,
       compare_6bit_8_out_3, compare_6bit_9_out_3, compare_6bit_10_out_3, compare_6bit_11_out_3, not_1_out,
       not_2_out, not_5_out, not_6_out, not_7_out, not_8_out, not_9_out, not_10_out, not_12_out, not_13_out,
       not_15_out, not_16_out, not_17_out, not_19_out, or_1_out, or_2_out, or_3_out, or_4_out, or_5_out,
       or_6_out, or_9_out, or_10_out, or_11_out, or_12_out, or_14_out, or_15_out, or_16_out, or_17_out,
       or_19_out, or_20_out, or_22_out, or_23_out, or_24_out, or_26_out, or_27_out, or_28_out,
       pull_resistor_1_node, pull_resistor_2_node, pull_resistor_4_node, pull_resistor_5_node,
       pull_resistor_9_node, pull_resistor_12_node, pull_resistor_15_node, zero_or_not_1_out_2,
       zero_or_not_2_out_2, zero_or_not_3_out_2, zero_or_not_4_out_2, zero_or_not_5_out_2,
       zero_or_not_6_out_2, zero_or_not_7_out_2, zero_or_not_8_out_2;
  wire [2:0] bit_extender_1_out, bit_extender_2_out, bit_extender_3_out, bit_extender_4_out,
       bit_extender_5_out, bit_extender_6_out, bit_extender_7_out, bit_extender_8_out, bit_extender_9_out,
       bit_extender_10_out, n6numrow_to_3numrow_1_out_2, n6numrow_to_3numrow_2_out_2,
       n6numrow_to_3numrow_3_out_2, n6numrow_to_3numrow_4_out_2, n6numrow_to_3numrow_5_out_2,
       n6numrow_to_3numrow_6_out_2, n6numrow_to_3numrow_7_out_2, n6numrow_to_3numrow_8_out_2,
       n6numrow_to_3numrow_9_out_2;
  wire [5:0] and_16_out, and_17_out, black1, black2, black3, black4, black5, column1, column2, column3,
       column4, column5, multiplexer_1_out, multiplexer_2_out, multiplexer_3_out, multiplexer_4_out,
       multiplexer_5_out, multiplexer_6_out, multiplexer_7_out, multiplexer_8_out, multiplexer_9_out,
       or_25_out, pull_resistor_13_node, pull_resistor_17_node, shifter_1_out, shifter_2_out, shifter_3_out,
       shifter_4_out, shifter_5_out, shifter_6_out, shifter_7_out, shifter_8_out, shifter_9_out,
       shifter_10_out, transistor_1_out, transistor_3_out, transistor_4_out, transistor_8_out, white2,
       white3, white4, white5;

  or or_1 (or_1_out, _0break_r, _0break_c);
  not not_1 (not_1_out, or_1_out);
  or or_2 (or_2_out, _1break_r, _1break_c);
  not not_2 (not_2_out, or_2_out);
  Pull_Resistor #(.pull(1)) pull_resistor_1 (.node(pull_resistor_1_node));
  compare_6bit compare_6bit_1 (.in_1(6'b100000), .in_2(column), .out_3(pull_resistor_1_node));
  not not_3 (_0break_c, pull_resistor_1_node);
  Pull_Resistor #(.pull(1)) pull_resistor_2 (.node(pull_resistor_2_node));
  compare_6bit compare_6bit_2 (.in_1(6'b000001), .in_2(row), .out_3(pull_resistor_2_node));
  not not_4 (_0break_r, pull_resistor_2_node);
  or or_3 (or_3_out, _3break_r, _3break_c);
  not not_5 (not_5_out, or_3_out);
  or or_4 (or_4_out, _4break_r, _4break_c);
  or or_5 (or_5_out, _2break_r, _2break_c);
  not not_6 (not_6_out, or_5_out);
  not not_7 (not_7_out, or_4_out);
  and and_1 (and_1_out, not_1_out, not_2_out, not_7_out, not_6_out, not_5_out, or_6_out);
  Transistor #(.\type ("n"), .width(6)) transistor_1 (.in(column5), .out(transistor_1_out), .gate(and_1_out));
  assign bit_extender_1_out = {{2{1'b0}}, pull_resistor_1_node};  // Bit_Extender bit_extender_1
  assign bit_extender_2_out = {{2{1'b0}}, pull_resistor_2_node};  // Bit_Extender bit_extender_2
  or or_6 (or_6_out, _5break_r, _5break_c);
  Pull_Resistor pull_resistor_3 (.node(transistor_1_out));
  Pull_Resistor #(.pull(1)) pull_resistor_4 (.node(pull_resistor_4_node));
  or or_7 (pull_resistor_4_node, _0break_r, _0break_c);
  Shifter #(.width(6)) shifter_1 (.in(column), .\dist (bit_extender_1_out), .out(shifter_1_out));
  Pull_Resistor #(.pull(1)) pull_resistor_5 (.node(pull_resistor_5_node));
  or or_8 (pull_resistor_5_node, _0break_r, _0break_c);
  Shifter #(.width(6), .shift("lr")) shifter_2 (.in(row), .\dist (bit_extender_2_out), .out(shifter_2_out));
  or or_9 (or_9_out, _1break_r, _1break_c);
  not not_8 (not_8_out, or_9_out);
  or or_10 (or_10_out, _0break_r, _0break_c);
  not not_9 (not_9_out, or_10_out);
  Transistor #(.width(6)) transistor_2 (.in(shifter_1_out), .out(column1), .gate(pull_resistor_4_node));
  Pull_Resistor pull_resistor_6 (.node(column1));
  Transistor #(.width(6)) transistor_3 (.in(shifter_2_out), .out(transistor_3_out), .gate(pull_resistor_5_node));
  Pull_Resistor pull_resistor_7 (.node(transistor_3_out));
  _6numRow_to_3numRow u_6numrow_to_3numrow_1 (.in_1(transistor_3_out), .out_2(n6numrow_to_3numrow_1_out_2));
  or or_11 (or_11_out, _4break_r, _4break_c);
  or or_12 (or_12_out, _2break_r, _2break_c);
  not not_10 (not_10_out, or_12_out);
  and and_2 (and_2_out, not_9_out, not_8_out, or_11_out, not_10_out, not_13_out);
  Transistor #(.\type ("n"), .width(6)) transistor_4 (.in(column4), .out(transistor_4_out), .gate(and_2_out));
  Pull_Resistor pull_resistor_8 (.node(transistor_4_out));
  Pull_Resistor pull_resistor_9 (.node(pull_resistor_9_node));
  or or_13 (pull_resistor_9_node, answer2, answer3, answer4, answer5);
  compare_6bit compare_6bit_3 (.in_1(6'b100000), .in_2(column1), .out_3(compare_6bit_3_out_3));
  not not_11 (_1break_c, compare_6bit_3_out_3);
  compare_6bit compare_6bit_4 (.in_1(6'b000001), .in_2(transistor_3_out), .out_3(compare_6bit_4_out_3));
  zero_or_not zero_or_not_1 (.in_1(black1), .out_2(zero_or_not_1_out_2));
  Multiplexer #(.select(3), .width(6)) multiplexer_1 (
    .in0(in_2), .in1(in_4), .in2(in_6), .in3(in_8), .in4(in_10), .in5(in_12), .out(multiplexer_1_out),
    .sel(n6numrow_to_3numrow_1_out_2));  // open: in6, in7, en
  Pull_Resistor pull_resistor_10 (.node(column1));
  or or_14 (or_14_out, _0break_r, _0break_c);
  not not_12 (not_12_out, or_14_out);
  or or_15 (or_15_out, _3break_r, _3break_c);
  not not_13 (not_13_out, or_15_out);
  or or_16 (or_16_out, _0break_c, _0break_r, _1break_c, _1break_r, _2break_c, _2break_r, _3break_c, _3break_r, _4break_c, _4break_r, _5break_c, _5break_r);
  Transistor #(.\type ("n")) transistor_5 (.in(pull_resistor_9_node), .out(out_15), .gate(or_16_out));
  Pull_Resistor pull_resistor_11 (.node(out_15));
  assign bit_extender_3_out = {{2{1'b0}}, compare_6bit_3_out_3};  // Bit_Extender bit_extender_3
  and and_3 (and_3_out, compare_6bit_4_out_3, zero_or_not_1_out_2);
  not not_14 (_1break_r, and_3_out);
  assign black1 = multiplexer_1_out & column1;  // AND_Gate and_4, 6 bits wide
  or or_17 (or_17_out, _1break_r, _1break_c);
  not not_15 (not_15_out, or_17_out);
  Pull_Resistor #(.pull(1)) pull_resistor_12 (.node(pull_resistor_12_node));
  or or_18 (pull_resistor_12_node, _1break_r, _1break_c);
  Shifter #(.width(6)) shifter_3 (.in(column1), .\dist (bit_extender_3_out), .out(shifter_3_out));
  Shifter #(.width(6), .shift("lr")) shifter_4 (
    .in(transistor_3_out), .\dist (bit_extender_4_out), .out(shifter_4_out));
  assign bit_extender_4_out = {{2{1'b0}}, and_3_out};  // Bit_Extender bit_extender_4
  or or_19 (or_19_out, _2break_r, _2break_c);
  not not_16 (not_16_out, or_19_out);
  or or_20 (or_20_out, _3break_r, _3break_c);
  and and_5 (and_5_out, not_12_out, not_15_out, not_16_out, or_20_out);
  Pull_Resistor pull_resistor_13 (.node(pull_resistor_13_node));
  Transistor #(.\type ("n"), .width(6)) transistor_6 (.in(column3), .out(pull_resistor_13_node), .gate(and_5_out));
  Pull_Resistor pull_resistor_14 (.node(column2));
  Transistor #(.width(6)) transistor_7 (.in(shifter_3_out), .out(column2), .gate(pull_resistor_12_node));
  Pull_Resistor #(.pull(1)) pull_resistor_15 (.node(pull_resistor_15_node));
  or or_21 (pull_resistor_15_node, _1break_r, _1break_c);
  Transistor #(.width(6)) transistor_8 (.in(shifter_4_out), .out(transistor_8_out), .gate(pull_resistor_15_node));
  Pull_Resistor pull_resistor_16 (.node(transistor_8_out));
  or or_22 (or_22_out, _0break_r, _0break_c);
  not not_17 (not_17_out, or_22_out);
  compare_6bit compare_6bit_5 (.in_1(6'b100000), .in_2(column2), .out_3(compare_6bit_5_out_3));
  not not_18 (_2break_c, compare_6bit_5_out_3);
  _6numRow_to_3numRow u_6numrow_to_3numrow_2 (.in_1(transistor_8_out), .out_2(n6numrow_to_3numrow_2_out_2));
  Multiplexer #(.select(3), .width(6)) multiplexer_2 (
    .in0(in_2), .in1(in_4), .in2(in_6), .in3(in_8), .in4(in_10), .in5(in_12), .out(multiplexer_2_out),
    .sel(n6numrow_to_3numrow_2_out_2));  // open: in6, in7, en
  _6numRow_to_3numRow u_6numrow_to_3numrow_3 (.in_1(transistor_8_out), .out_2(n6numrow_to_3numrow_3_out_2));
  Multiplexer #(.select(3), .width(6)) multiplexer_3 (
    .in0(in_1), .in1(in_3), .in2(in_5), .in3(in_7), .in4(in_9), .in5(in_11), .out(multiplexer_3_out),
    .sel(n6numrow_to_3numrow_3_out_2));  // open: in6, in7, en
  or or_23 (or_23_out, _1break_r, _1break_c);
  or or_24 (or_24_out, _2break_r, _2break_c);
  not not_19 (not_19_out, or_23_out);
  and and_6 (and_6_out, not_17_out, not_19_out, or_24_out);
  Pull_Resistor pull_resistor_17 (.node(pull_resistor_17_node));
  Transistor #(.\type ("n"), .width(6)) transistor_9 (.in(column2), .out(pull_resistor_17_node), .gate(and_6_out));
  assign bit_extender_5_out = {{2{1'b0}}, compare_6bit_5_out_3};  // Bit_Extender bit_extender_5
  compare_6bit compare_6bit_6 (.in_1(6'b000001), .in_2(transistor_8_out), .out_3(compare_6bit_6_out_3));
  and and_7 (and_7_out, compare_6bit_6_out_3, zero_or_not_2_out_2);
  zero_or_not zero_or_not_2 (.in_1(black2), .out_2(zero_or_not_2_out_2));
  not not_20 (_2break_r, and_7_out);
  Pull_Resistor pull_resistor_18 (.node(zero_or_not_2_out_2));
  Transistor transistor_10 (.in(zero_or_not_3_out_2), .out(answer2), .gate(zero_or_not_2_out_2));
  zero_or_not zero_or_not_3 (.in_1(white2), .out_2(zero_or_not_3_out_2));
  Pull_Resistor pull_resistor_19 (.node(answer2));
  assign black2 = multiplexer_2_out & column2;  // AND_Gate and_8, 6 bits wide
  Pull_Resistor pull_resistor_20 (.node(column2));
  assign white2 = multiplexer_3_out & column2;  // AND_Gate and_9, 6 bits wide
  Pull_Resistor pull_resistor_21 (.node(column2));
  assign or_25_out = pull_resistor_17_node | pull_resistor_13_node | transistor_4_out | transistor_1_out;  // OR_Gate or_25, 6 bits wide
  Shifter #(.width(6)) shifter_5 (.in(column2), .\dist (bit_extender_5_out), .out(shifter_5_out));
  assign bit_extender_6_out = {{2{1'b0}}, and_7_out};  // Bit_Extender bit_extender_6
  Pull_Resistor pull_resistor_22 (.node(out_col));
  Transistor #(.\type ("n"), .width(6)) transistor_11 (.in(or_25_out), .out(out_col), .gate(out_15));
  or or_26 (or_26_out, _2break_r, _2break_c);
  Pull_Resistor #(.pull(1)) pull_resistor_23 (.node(or_26_out));
  Pull_Resistor pull_resistor_24 (.node(column3));
  Transistor #(.width(6)) transistor_12 (.in(shifter_5_out), .out(column3), .gate(or_26_out));
  Shifter #(.width(6), .shift("lr")) shifter_6 (
    .in(transistor_8_out), .\dist (bit_extender_6_out), .out(shifter_6_out));
  compare_6bit compare_6bit_7 (.in_1(6'b100000), .in_2(column3), .out_3(compare_6bit_7_out_3));
  not not_21 (_3break_c, compare_6bit_7_out_3);
  _6numRow_to_3numRow u_6numrow_to_3numrow_4 (.in_1(shifter_6_out), .out_2(n6numrow_to_3numrow_4_out_2));
  _6numRow_to_3numRow u_6numrow_to_3numrow_5 (.in_1(shifter_6_out), .out_2(n6numrow_to_3numrow_5_out_2));
  assign bit_extender_7_out = {{2{1'b0}}, compare_6bit_7_out_3};  // Bit_Extender bit_extender_7
  compare_6bit compare_6bit_8 (.in_1(6'b000001), .in_2(shifter_6_out), .out_3(compare_6bit_8_out_3));
  zero_or_not zero_or_not_4 (.in_1(black3), .out_2(zero_or_not_4_out_2));
  Pull_Resistor pull_resistor_25 (.node(zero_or_not_4_out_2));
  zero_or_not zero_or_not_5 (.in_1(white3), .out_2(zero_or_not_5_out_2));
  Multiplexer #(.select(3), .width(6)) multiplexer_4 (
    .in0(in_2), .in1(in_4), .in2(in_6), .in3(in_8), .in4(in_10), .in5(in_12), .out(multiplexer_4_out),
    .sel(n6numrow_to_3numrow_4_out_2));  // open: in6, in7, en
  Pull_Resistor pull_resistor_26 (.node(column3));
  Multiplexer #(.select(3), .width(6)) multiplexer_5 (
    .in0(in_1), .in1(in_3), .in2(in_5), .in3(in_7), .in4(in_9), .in5(in_11), .out(multiplexer_5_out),
    .sel(n6numrow_to_3numrow_5_out_2));  // open: in6, in7, en
  Pull_Resistor pull_resistor_27 (.node(column3));
  Shifter #(.width(6)) shifter_7 (.in(column3), .\dist (bit_extender_7_out), .out(shifter_7_out));
  and and_10 (and_10_out, compare_6bit_8_out_3, zero_or_not_4_out_2);
  not not_22 (_3break_r, and_10_out);
  Transistor transistor_13 (.in(zero_or_not_5_out_2), .out(answer3), .gate(zero_or_not_4_out_2));
  Pull_Resistor pull_resistor_28 (.node(answer3));
  assign black3 = multiplexer_4_out & column3;  // AND_Gate and_11, 6 bits wide
  assign white3 = multiplexer_5_out & column3;  // AND_Gate and_12, 6 bits wide
  or or_27 (or_27_out, _3break_r, _3break_c);
  Pull_Resistor #(.pull(1)) pull_resistor_29 (.node(or_27_out));
  Pull_Resistor pull_resistor_30 (.node(column4));
  Transistor #(.width(6)) transistor_14 (.in(shifter_7_out), .out(column4), .gate(or_27_out));
  Shifter #(.width(6), .shift("lr")) shifter_8 (.in(shifter_6_out), .\dist (bit_extender_8_out), .out(shifter_8_out));
  assign bit_extender_8_out = {{2{1'b0}}, and_10_out};  // Bit_Extender bit_extender_8
  compare_6bit compare_6bit_9 (.in_1(6'b100000), .in_2(column4), .out_3(compare_6bit_9_out_3));
  not not_23 (_4break_c, compare_6bit_9_out_3);
  assign bit_extender_9_out = {{2{1'b0}}, compare_6bit_9_out_3};  // Bit_Extender bit_extender_9
  _6numRow_to_3numRow u_6numrow_to_3numrow_6 (.in_1(shifter_8_out), .out_2(n6numrow_to_3numrow_6_out_2));
  Multiplexer #(.select(3), .width(6)) multiplexer_6 (
    .in0(in_2), .in1(in_4), .in2(in_6), .in3(in_8), .in4(in_10), .in5(in_12), .out(multiplexer_6_out),
    .sel(n6numrow_to_3numrow_6_out_2));  // open: in6, in7, en
  _6numRow_to_3numRow u_6numrow_to_3numrow_7 (.in_1(shifter_8_out), .out_2(n6numrow_to_3numrow_7_out_2));
  Multiplexer #(.select(3), .width(6)) multiplexer_7 (
    .in0(in_1), .in1(in_3), .in2(in_5), .in3(in_7), .in4(in_9), .in5(in_11), .out(multiplexer_7_out),
    .sel(n6numrow_to_3numrow_7_out_2));  // open: in6, in7, en
  Shifter #(.width(6)) shifter_9 (.in(column4), .\dist (bit_extender_9_out), .out(shifter_9_out));
  compare_6bit compare_6bit_10 (.in_1(6'b000001), .in_2(shifter_8_out), .out_3(compare_6bit_10_out_3));
  and and_13 (and_13_out, compare_6bit_10_out_3, zero_or_not_6_out_2);
  not not_24 (_4break_r, and_13_out);
  zero_or_not zero_or_not_6 (.in_1(black4), .out_2(zero_or_not_6_out_2));
  Pull_Resistor pull_resistor_31 (.node(zero_or_not_6_out_2));
  Transistor transistor_15 (.in(zero_or_not_7_out_2), .out(answer4), .gate(zero_or_not_6_out_2));
  Pull_Resistor pull_resistor_32 (.node(answer4));
  zero_or_not zero_or_not_7 (.in_1(white4), .out_2(zero_or_not_7_out_2));
  assign black4 = multiplexer_6_out & column4;  // AND_Gate and_14, 6 bits wide
  Pull_Resistor pull_resistor_33 (.node(column4));
  assign white4 = multiplexer_7_out & column4;  // AND_Gate and_15, 6 bits wide
  Pull_Resistor pull_resistor_34 (.node(column4));
  or or_28 (or_28_out, _4break_r, _4break_c);
  Pull_Resistor #(.pull(1)) pull_resistor_35 (.node(or_28_out));
  Pull_Resistor pull_resistor_36 (.node(column5));
  Transistor #(.width(6)) transistor_16 (.in(shifter_9_out), .out(column5), .gate(or_28_out));
  assign bit_extender_10_out = {{2{1'b0}}, and_13_out};  // Bit_Extender bit_extender_10
  compare_6bit compare_6bit_11 (.in_1(6'b100000), .in_2(column5), .out_3(compare_6bit_11_out_3));
  Shifter #(.width(6), .shift("lr")) shifter_10 (
    .in(shifter_8_out), .\dist (bit_extender_10_out), .out(shifter_10_out));
  _6numRow_to_3numRow u_6numrow_to_3numrow_8 (.in_1(shifter_10_out), .out_2(n6numrow_to_3numrow_8_out_2));
  _6numRow_to_3numRow u_6numrow_to_3numrow_9 (.in_1(shifter_10_out), .out_2(n6numrow_to_3numrow_9_out_2));
  not not_25 (_5break_c, compare_6bit_11_out_3);
  assign and_16_out = shifter_10_out & black5;  // AND_Gate and_16, 6 bits wide
  zero_or_not zero_or_not_8 (.in_1(and_16_out), .out_2(zero_or_not_8_out_2));
  zero_or_not zero_or_not_9 (.in_1(and_17_out), .out_2(answer5));
  assign and_17_out = shifter_10_out & white5;  // AND_Gate and_17, 6 bits wide
  Multiplexer #(.select(3), .width(6)) multiplexer_8 (
    .in0(in_2), .in1(in_4), .in2(in_6), .in3(in_8), .in4(in_10), .in5(in_12), .out(multiplexer_8_out),
    .sel(n6numrow_to_3numrow_8_out_2));  // open: in6, in7, en
  Pull_Resistor pull_resistor_37 (.node(column5));
  Multiplexer #(.select(3), .width(6)) multiplexer_9 (
    .in0(in_1), .in1(in_3), .in2(in_5), .in3(in_7), .in4(in_9), .in5(in_11), .out(multiplexer_9_out),
    .sel(n6numrow_to_3numrow_9_out_2));  // open: in6, in7, en
  Pull_Resistor pull_resistor_38 (.node(column5));
  not not_26 (_5break_r, zero_or_not_8_out_2);
  assign black5 = multiplexer_8_out & column5;  // AND_Gate and_18, 6 bits wide
  assign white5 = multiplexer_9_out & column5;  // AND_Gate and_19, 6 bits wide

  // Other names for the same wires on the sheet: _0b[5:0] = in_2; _0w[5:0] = in_1; _1b[5:0] = in_4; _1w[5:0] = in_3;
  //   _2b[5:0] = in_6; _2w[5:0] = in_5; _3b[5:0] = in_8; _3w[5:0] = in_7; _4b[5:0] = in_10; _4w[5:0] = in_9;
  //   _5b[5:0] = in_12; _5w[5:0] = in_11; fin_answer = out_15
endmodule

module check_diag_ld (
  input  [5:0] in_1,
  input  [5:0] in_2,
  input  [5:0] in_3,
  input  [5:0] in_4,
  input  [5:0] in_5,
  input  [5:0] in_6,
  input  [5:0] in_7,
  input  [5:0] in_8,
  input  [5:0] in_9,
  input  [5:0] in_10,
  input  [5:0] in_11,
  input  [5:0] in_12,
  input  [5:0] column,
  input  [5:0] row,
  output out_15,
  output [5:0] out_col
);

  wire _0break_c, _0break_r, _1break_c, _1break_r, _2break_c, _2break_r, _3break_c, _3break_r, _4break_c,
       _4break_r, _5break_c, _5break_r, and_1_out, and_2_out, and_3_out, and_5_out, and_6_out, and_7_out,
       and_10_out, and_13_out, answer2, answer3, answer4, answer5, compare_6bit_1_out_3,
       compare_6bit_2_out_3, compare_6bit_3_out_3, compare_6bit_4_out_3, compare_6bit_5_out_3,
       compare_6bit_6_out_3, compare_6bit_7_out_3, compare_6bit_8_out_3, compare_6bit_9_out_3,
       compare_6bit_10_out_3, compare_6bit_11_out_3, not_1_out, not_2_out, not_5_out, not_6_out, not_7_out,
       not_8_out, not_9_out, not_10_out, not_12_out, not_13_out, not_15_out, not_16_out, not_17_out,
       not_19_out, or_1_out, or_2_out, or_3_out, or_4_out, or_5_out, or_6_out, or_7_out, or_8_out, or_9_out,
       or_10_out, or_11_out, or_12_out, or_14_out, or_15_out, or_16_out, or_17_out, or_18_out, or_19_out,
       or_20_out, or_21_out, or_22_out, or_23_out, or_24_out, or_26_out, or_27_out, or_28_out,
       pull_resistor_5_node, zero_or_not_1_out_2, zero_or_not_2_out_2, zero_or_not_3_out_2,
       zero_or_not_4_out_2, zero_or_not_5_out_2, zero_or_not_6_out_2, zero_or_not_7_out_2,
       zero_or_not_8_out_2;
  wire [2:0] bit_extender_1_out, bit_extender_2_out, bit_extender_3_out, bit_extender_4_out,
       bit_extender_5_out, bit_extender_6_out, bit_extender_7_out, bit_extender_8_out, bit_extender_9_out,
       bit_extender_10_out, n6numrow_to_3numrow_1_out_2, n6numrow_to_3numrow_2_out_2,
       n6numrow_to_3numrow_3_out_2, n6numrow_to_3numrow_4_out_2, n6numrow_to_3numrow_5_out_2,
       n6numrow_to_3numrow_6_out_2, n6numrow_to_3numrow_7_out_2, n6numrow_to_3numrow_8_out_2,
       n6numrow_to_3numrow_9_out_2;
  wire [5:0] and_16_out, and_17_out, black1, black2, black3, black4, black5, column1, column2, column3,
       column4, column5, multiplexer_1_out, multiplexer_2_out, multiplexer_3_out, multiplexer_4_out,
       multiplexer_5_out, multiplexer_6_out, multiplexer_7_out, multiplexer_8_out, multiplexer_9_out,
       or_25_out, pull_resistor_3_node, pull_resistor_8_node, pull_resistor_10_node, shifter_1_out,
       shifter_2_out, shifter_3_out, shifter_4_out, shifter_5_out, shifter_6_out, shifter_7_out,
       shifter_8_out, shifter_9_out, shifter_10_out, transistor_1_out, transistor_4_out, transistor_9_out,
       white2, white3, white4, white5;

  or or_1 (or_1_out, _0break_r, _0break_c);
  not not_1 (not_1_out, or_1_out);
  or or_2 (or_2_out, _1break_r, _1break_c);
  not not_2 (not_2_out, or_2_out);
  compare_6bit compare_6bit_1 (.in_1(6'b100000), .in_2(column), .out_3(compare_6bit_1_out_3));
  not not_3 (_0break_c, compare_6bit_1_out_3);
  compare_6bit compare_6bit_2 (.in_1(6'b100000), .in_2(row), .out_3(compare_6bit_2_out_3));
  not not_4 (_0break_r, compare_6bit_2_out_3);
  or or_3 (or_3_out, _3break_r, _3break_c);
  not not_5 (not_5_out, or_3_out);
  or or_4 (or_4_out, _4break_r, _4break_c);
  or or_5 (or_5_out, _2break_r, _2break_c);
  not not_6 (not_6_out, or_5_out);
  not not_7 (not_7_out, or_4_out);
  and and_1 (and_1_out, not_1_out, not_2_out, not_7_out, not_6_out, not_5_out, or_6_out);
  Transistor #(.\type ("n"), .width(6)) transistor_1 (.in(column5), .out(transistor_1_out), .gate(and_1_out));
  assign bit_extender_1_out = {{2{1'b0}}, compare_6bit_1_out_3};  // Bit_Extender bit_extender_1
  assign bit_extender_2_out = {{2{1'b0}}, compare_6bit_2_out_3};  // Bit_Extender bit_extender_2
  or or_6 (or_6_out, _5break_r, _5break_c);
  Pull_Resistor pull_resistor_1 (.node(transistor_1_out));
  or or_7 (or_7_out, _0break_r, _0break_c);
  Shifter #(.width(6)) shifter_1 (.in(column), .\dist (bit_extender_1_out), .out(shifter_1_out));
  or or_8 (or_8_out, _0break_r, _0break_c);
  Shifter #(.width(6)) shifter_2 (.in(row), .\dist (bit_extender_2_out), .out(shifter_2_out));
  or or_9 (or_9_out, _1break_r, _1break_c);
  or or_10 (or_10_out, _0break_r, _0break_c);
  not not_8 (not_8_out, or_9_out);
  not not_9 (not_9_out, or_10_out);
  Transistor #(.width(6)) transistor_2 (.in(shifter_1_out), .out(column1), .gate(or_7_out));
  Pull_Resistor pull_resistor_2 (.node(column1));
  Pull_Resistor pull_resistor_3 (.node(pull_resistor_3_node));
  Transistor #(.width(6)) transistor_3 (.in(shifter_2_out), .out(pull_resistor_3_node), .gate(or_8_out));
  _6numRow_to_3numRow u_6numrow_to_3numrow_1 (.in_1(pull_resistor_3_node), .out_2(n6numrow_to_3numrow_1_out_2));
  or or_11 (or_11_out, _4break_r, _4break_c);
  or or_12 (or_12_out, _2break_r, _2break_c);
  not not_10 (not_10_out, or_12_out);
  and and_2 (and_2_out, not_9_out, not_8_out, or_11_out, not_10_out, not_13_out);
  Transistor #(.\type ("n"), .width(6)) transistor_4 (.in(column4), .out(transistor_4_out), .gate(and_2_out));
  Pull_Resistor pull_resistor_4 (.node(transistor_4_out));
  Pull_Resistor pull_resistor_5 (.node(pull_resistor_5_node));
  or or_13 (pull_resistor_5_node, answer2, answer3, answer4, answer5);
  compare_6bit compare_6bit_3 (.in_1(6'b100000), .in_2(column1), .out_3(compare_6bit_3_out_3));
  not not_11 (_1break_c, compare_6bit_3_out_3);
  compare_6bit compare_6bit_4 (.in_1(6'b100000), .in_2(pull_resistor_3_node), .out_3(compare_6bit_4_out_3));
  zero_or_not zero_or_not_1 (.in_1(black1), .out_2(zero_or_not_1_out_2));
  Multiplexer #(.select(3), .width(6)) multiplexer_1 (
    .in0(in_2), .in1(in_4), .in2(in_6), .in3(in_8), .in4(in_10), .in5(in_12), .out(multiplexer_1_out),
    .sel(n6numrow_to_3numrow_1_out_2));  // open: in6, in7, en
  Pull_Resistor pull_resistor_6 (.node(column1));
  or or_14 (or_14_out, _0break_r, _0break_c);
  or or_15 (or_15_out, _3break_r, _3break_c);
  not not_12 (not_12_out, or_14_out);
  not not_13 (not_13_out, or_15_out);
  or or_16 (or_16_out, _0break_c, _0break_r, _1break_c, _1break_r, _2break_c, _2break_r, _3break_c, _3break_r, _4break_c, _4break_r, _5break_c, _5break_r);
  Transistor #(.\type ("n")) transistor_5 (.in(pull_resistor_5_node), .out(out_15), .gate(or_16_out));
  Pull_Resistor pull_resistor_7 (.node(out_15));
  assign bit_extender_3_out = {{2{1'b0}}, compare_6bit_3_out_3};  // Bit_Extender bit_extender_3
  and and_3 (and_3_out, compare_6bit_4_out_3, zero_or_not_1_out_2);
  not not_14 (_1break_r, and_3_out);
  assign black1 = multiplexer_1_out & column1;  // AND_Gate and_4, 6 bits wide
  or or_17 (or_17_out, _1break_r, _1break_c);
  not not_15 (not_15_out, or_17_out);
  or or_18 (or_18_out, _1break_r, _1break_c);
  Shifter #(.width(6)) shifter_3 (.in(column1), .\dist (bit_extender_3_out), .out(shifter_3_out));
  Shifter #(.width(6)) shifter_4 (.in(pull_resistor_3_node), .\dist (bit_extender_4_out), .out(shifter_4_out));
  assign bit_extender_4_out = {{2{1'b0}}, and_3_out};  // Bit_Extender bit_extender_4
  or or_19 (or_19_out, _2break_r, _2break_c);
  not not_16 (not_16_out, or_19_out);
  or or_20 (or_20_out, _3break_r, _3break_c);
  and and_5 (and_5_out, not_12_out, not_15_out, not_16_out, or_20_out);
  Pull_Resistor pull_resistor_8 (.node(pull_resistor_8_node));
  Transistor #(.\type ("n"), .width(6)) transistor_6 (.in(column3), .out(pull_resistor_8_node), .gate(and_5_out));
  Pull_Resistor pull_resistor_9 (.node(column2));
  Transistor #(.width(6)) transistor_7 (.in(shifter_3_out), .out(column2), .gate(or_18_out));
  or or_21 (or_21_out, _1break_r, _1break_c);
  Pull_Resistor pull_resistor_10 (.node(pull_resistor_10_node));
  Transistor #(.width(6)) transistor_8 (.in(shifter_4_out), .out(pull_resistor_10_node), .gate(or_21_out));
  or or_22 (or_22_out, _0break_r, _0break_c);
  not not_17 (not_17_out, or_22_out);
  compare_6bit compare_6bit_5 (.in_1(6'b100000), .in_2(column2), .out_3(compare_6bit_5_out_3));
  not not_18 (_2break_c, compare_6bit_5_out_3);
  _6numRow_to_3numRow u_6numrow_to_3numrow_2 (.in_1(pull_resistor_10_node), .out_2(n6numrow_to_3numrow_2_out_2));
  Multiplexer #(.select(3), .width(6)) multiplexer_2 (
    .in0(in_2), .in1(in_4), .in2(in_6), .in3(in_8), .in4(in_10), .in5(in_12), .out(multiplexer_2_out),
    .sel(n6numrow_to_3numrow_2_out_2));  // open: in6, in7, en
  _6numRow_to_3numRow u_6numrow_to_3numrow_3 (.in_1(pull_resistor_10_node), .out_2(n6numrow_to_3numrow_3_out_2));
  Multiplexer #(.select(3), .width(6)) multiplexer_3 (
    .in0(in_1), .in1(in_3), .in2(in_5), .in3(in_7), .in4(in_9), .in5(in_11), .out(multiplexer_3_out),
    .sel(n6numrow_to_3numrow_3_out_2));  // open: in6, in7, en
  or or_23 (or_23_out, _1break_r, _1break_c);
  not not_19 (not_19_out, or_23_out);
  or or_24 (or_24_out, _2break_r, _2break_c);
  and and_6 (and_6_out, not_17_out, not_19_out, or_24_out);
  Transistor #(.\type ("n"), .width(6)) transistor_9 (.in(column2), .out(transistor_9_out), .gate(and_6_out));
  Pull_Resistor pull_resistor_11 (.node(transistor_9_out));
  assign bit_extender_5_out = {{2{1'b0}}, compare_6bit_5_out_3};  // Bit_Extender bit_extender_5
  compare_6bit compare_6bit_6 (.in_1(6'b100000), .in_2(pull_resistor_10_node), .out_3(compare_6bit_6_out_3));
  and and_7 (and_7_out, compare_6bit_6_out_3, zero_or_not_2_out_2);
  not not_20 (_2break_r, and_7_out);
  zero_or_not zero_or_not_2 (.in_1(black2), .out_2(zero_or_not_2_out_2));
  Pull_Resistor pull_resistor_12 (.node(zero_or_not_2_out_2));
  Transistor transistor_10 (.in(zero_or_not_3_out_2), .out(answer2), .gate(zero_or_not_2_out_2));
  Pull_Resistor pull_resistor_13 (.node(answer2));
  zero_or_not zero_or_not_3 (.in_1(white2), .out_2(zero_or_not_3_out_2));
  assign black2 = multiplexer_2_out & column2;  // AND_Gate and_8, 6 bits wide
  Pull_Resistor pull_resistor_14 (.node(column2));
  assign white2 = multiplexer_3_out & column2;  // AND_Gate and_9, 6 bits wide
  Pull_Resistor pull_resistor_15 (.node(column2));
  assign or_25_out = transistor_9_out | pull_resistor_8_node | transistor_4_out | transistor_1_out;  // OR_Gate or_25, 6 bits wide
  Shifter #(.width(6)) shifter_5 (.in(column2), .\dist (bit_extender_5_out), .out(shifter_5_out));
  assign bit_extender_6_out = {{2{1'b0}}, and_7_out};  // Bit_Extender bit_extender_6
  Transistor #(.\type ("n"), .width(6)) transistor_11 (.in(or_25_out), .out(out_col), .gate(out_15));
  Pull_Resistor pull_resistor_16 (.node(out_col));
  or or_26 (or_26_out, _2break_r, _2break_c);
  Transistor #(.width(6)) transistor_12 (.in(shifter_5_out), .out(column3), .gate(or_26_out));
  Pull_Resistor pull_resistor_17 (.node(column3));
  Shifter #(.width(6)) shifter_6 (.in(pull_resistor_10_node), .\dist (bit_extender_6_out), .out(shifter_6_out));
  compare_6bit compare_6bit_7 (.in_1(6'b100000), .in_2(column3), .out_3(compare_6bit_7_out_3));
  not not_21 (_3break_c, compare_6bit_7_out_3);
  _6numRow_to_3numRow u_6numrow_to_3numrow_4 (.in_1(shifter_6_out), .out_2(n6numrow_to_3numrow_4_out_2));
  _6numRow_to_3numRow u_6numrow_to_3numrow_5 (.in_1(shifter_6_out), .out_2(n6numrow_to_3numrow_5_out_2));
  assign bit_extender_7_out = {{2{1'b0}}, compare_6bit_7_out_3};  // Bit_Extender bit_extender_7
  compare_6bit compare_6bit_8 (.in_1(6'b100000), .in_2(shifter_6_out), .out_3(compare_6bit_8_out_3));
  zero_or_not zero_or_not_4 (.in_1(black3), .out_2(zero_or_not_4_out_2));
  Pull_Resistor pull_resistor_18 (.node(zero_or_not_4_out_2));
  zero_or_not zero_or_not_5 (.in_1(white3), .out_2(zero_or_not_5_out_2));
  Multiplexer #(.select(3), .width(6)) multiplexer_4 (
    .in0(in_2), .in1(in_4), .in2(in_6), .in3(in_8), .in4(in_10), .in5(in_12), .out(multiplexer_4_out),
    .sel(n6numrow_to_3numrow_4_out_2));  // open: in6, in7, en
  Pull_Resistor pull_resistor_19 (.node(column3));
  Multiplexer #(.select(3), .width(6)) multiplexer_5 (
    .in0(in_1), .in1(in_3), .in2(in_5), .in3(in_7), .in4(in_9), .in5(in_11), .out(multiplexer_5_out),
    .sel(n6numrow_to_3numrow_5_out_2));  // open: in6, in7, en
  Pull_Resistor pull_resistor_20 (.node(column3));
  Shifter #(.width(6)) shifter_7 (.in(column3), .\dist (bit_extender_7_out), .out(shifter_7_out));
  and and_10 (and_10_out, compare_6bit_8_out_3, zero_or_not_4_out_2);
  not not_22 (_3break_r, and_10_out);
  Transistor transistor_13 (.in(zero_or_not_5_out_2), .out(answer3), .gate(zero_or_not_4_out_2));
  Pull_Resistor pull_resistor_21 (.node(answer3));
  assign black3 = multiplexer_4_out & column3;  // AND_Gate and_11, 6 bits wide
  assign white3 = multiplexer_5_out & column3;  // AND_Gate and_12, 6 bits wide
  or or_27 (or_27_out, _3break_r, _3break_c);
  Pull_Resistor pull_resistor_22 (.node(column4));
  Transistor #(.width(6)) transistor_14 (.in(shifter_7_out), .out(column4), .gate(or_27_out));
  Shifter #(.width(6)) shifter_8 (.in(shifter_6_out), .\dist (bit_extender_8_out), .out(shifter_8_out));
  assign bit_extender_8_out = {{2{1'b0}}, and_10_out};  // Bit_Extender bit_extender_8
  compare_6bit compare_6bit_9 (.in_1(6'b100000), .in_2(column4), .out_3(compare_6bit_9_out_3));
  not not_23 (_4break_c, compare_6bit_9_out_3);
  assign bit_extender_9_out = {{2{1'b0}}, compare_6bit_9_out_3};  // Bit_Extender bit_extender_9
  _6numRow_to_3numRow u_6numrow_to_3numrow_6 (.in_1(shifter_8_out), .out_2(n6numrow_to_3numrow_6_out_2));
  Multiplexer #(.select(3), .width(6)) multiplexer_6 (
    .in0(in_2), .in1(in_4), .in2(in_6), .in3(in_8), .in4(in_10), .in5(in_12), .out(multiplexer_6_out),
    .sel(n6numrow_to_3numrow_6_out_2));  // open: in6, in7, en
  _6numRow_to_3numRow u_6numrow_to_3numrow_7 (.in_1(shifter_8_out), .out_2(n6numrow_to_3numrow_7_out_2));
  Multiplexer #(.select(3), .width(6)) multiplexer_7 (
    .in0(in_1), .in1(in_3), .in2(in_5), .in3(in_7), .in4(in_9), .in5(in_11), .out(multiplexer_7_out),
    .sel(n6numrow_to_3numrow_7_out_2));  // open: in6, in7, en
  Shifter #(.width(6)) shifter_9 (.in(column4), .\dist (bit_extender_9_out), .out(shifter_9_out));
  compare_6bit compare_6bit_10 (.in_1(6'b100000), .in_2(shifter_8_out), .out_3(compare_6bit_10_out_3));
  and and_13 (and_13_out, compare_6bit_10_out_3, zero_or_not_6_out_2);
  zero_or_not zero_or_not_6 (.in_1(black4), .out_2(zero_or_not_6_out_2));
  not not_24 (_4break_r, and_13_out);
  Pull_Resistor pull_resistor_23 (.node(zero_or_not_6_out_2));
  zero_or_not zero_or_not_7 (.in_1(white4), .out_2(zero_or_not_7_out_2));
  Pull_Resistor pull_resistor_24 (.node(answer4));
  Transistor transistor_15 (.in(zero_or_not_7_out_2), .out(answer4), .gate(zero_or_not_6_out_2));
  assign black4 = multiplexer_6_out & column4;  // AND_Gate and_14, 6 bits wide
  Pull_Resistor pull_resistor_25 (.node(column4));
  assign white4 = multiplexer_7_out & column4;  // AND_Gate and_15, 6 bits wide
  Pull_Resistor pull_resistor_26 (.node(column4));
  or or_28 (or_28_out, _4break_r, _4break_c);
  Pull_Resistor pull_resistor_27 (.node(column5));
  Transistor #(.width(6)) transistor_16 (.in(shifter_9_out), .out(column5), .gate(or_28_out));
  assign bit_extender_10_out = {{2{1'b0}}, and_13_out};  // Bit_Extender bit_extender_10
  compare_6bit compare_6bit_11 (.in_1(6'b100000), .in_2(column5), .out_3(compare_6bit_11_out_3));
  Shifter #(.width(6)) shifter_10 (.in(shifter_8_out), .\dist (bit_extender_10_out), .out(shifter_10_out));
  _6numRow_to_3numRow u_6numrow_to_3numrow_8 (.in_1(shifter_10_out), .out_2(n6numrow_to_3numrow_8_out_2));
  _6numRow_to_3numRow u_6numrow_to_3numrow_9 (.in_1(shifter_10_out), .out_2(n6numrow_to_3numrow_9_out_2));
  not not_25 (_5break_c, compare_6bit_11_out_3);
  assign and_16_out = shifter_10_out & black5;  // AND_Gate and_16, 6 bits wide
  zero_or_not zero_or_not_8 (.in_1(and_16_out), .out_2(zero_or_not_8_out_2));
  assign and_17_out = shifter_10_out & white5;  // AND_Gate and_17, 6 bits wide
  zero_or_not zero_or_not_9 (.in_1(and_17_out), .out_2(answer5));
  Multiplexer #(.select(3), .width(6)) multiplexer_8 (
    .in0(in_2), .in1(in_4), .in2(in_6), .in3(in_8), .in4(in_10), .in5(in_12), .out(multiplexer_8_out),
    .sel(n6numrow_to_3numrow_8_out_2));  // open: in6, in7, en
  Pull_Resistor pull_resistor_28 (.node(column5));
  Multiplexer #(.select(3), .width(6)) multiplexer_9 (
    .in0(in_1), .in1(in_3), .in2(in_5), .in3(in_7), .in4(in_9), .in5(in_11), .out(multiplexer_9_out),
    .sel(n6numrow_to_3numrow_9_out_2));  // open: in6, in7, en
  Pull_Resistor pull_resistor_29 (.node(column5));
  not not_26 (_5break_r, zero_or_not_8_out_2);
  assign black5 = multiplexer_8_out & column5;  // AND_Gate and_18, 6 bits wide
  assign white5 = multiplexer_9_out & column5;  // AND_Gate and_19, 6 bits wide

  // Other names for the same wires on the sheet: _0b[5:0] = in_2; _0w[5:0] = in_1; _1b[5:0] = in_4; _1w[5:0] = in_3;
  //   _2b[5:0] = in_6; _2w[5:0] = in_5; _3b[5:0] = in_8; _3w[5:0] = in_7; _4b[5:0] = in_10; _4w[5:0] = in_9;
  //   _5b[5:0] = in_12; _5w[5:0] = in_11; fin_answer = out_15
endmodule

module can_put (
  input  [5:0] in_1,
  input  [5:0] in_2,
  input  [5:0] in_3,
  input  [5:0] in_4,
  input  [5:0] in_5,
  input  in_6,
  input  in_7,
  input  [5:0] in_8,
  input  in_9,
  input  in_10,
  input  in_11,
  input  in_12,
  input  in_13,
  input  in_14,
  output [5:0] left_hor,
  output out_16,
  output [5:0] rigth_hor,
  output [5:0] down_ver,
  output [5:0] up_ver
);

  wire and_2_out, check_left_1_out_4, check_left_2_out_4, check_right_1_out_5, check_right_2_out_5, or_1_out,
       or_2_out, or_3_out, or_4_out, replay;
  wire [5:0] and_1_out, or_5_out;

  check_left check_left_1 (.corrent(in_8), .white(in_5), .black(in_4), .out_4(check_left_1_out_4), .out_5(down_ver));
  check_right check_right_1 (.corrent(in_8), .white(in_5), .black(in_4), .out_5(check_right_1_out_5), .out_4(up_ver));
  check_left check_left_2 (.corrent(in_1), .white(in_2), .black(in_3), .out_4(check_left_2_out_4), .out_5(left_hor));
  check_right check_right_2 (
    .corrent(in_1), .white(in_2), .black(in_3), .out_5(check_right_2_out_5), .out_4(rigth_hor));
  or or_1 (or_1_out, check_left_1_out_4, check_right_1_out_5);
  or or_2 (or_2_out, check_left_2_out_4, check_right_2_out_5);
  or or_3 (or_3_out, or_2_out, or_1_out, in_6, in_7, in_9, in_10);
  not not_1 (replay, or_4_out);
  or or_4 (or_4_out, and_1_out[5], and_1_out[4], and_1_out[3], and_1_out[2], and_1_out[1], and_1_out[0]);
  assign and_1_out = in_1 & or_5_out;  // AND_Gate and_1, 6 bits wide
  assign or_5_out = in_2 | in_3;  // OR_Gate or_5, 6 bits wide
  and and_2 (and_2_out, in_13, in_12, replay, or_3_out);
  or or_6 (out_16, in_11, in_14, and_2_out);

  // Other names for the same wires on the sheet: black[5:0] = in_3; black_col[5:0] = in_4; column[5:0] = in_1;
  //   ld_diag = in_9; lu_diag = in_6; now_row[5:0] = in_8; rd_diag = in_10; reset = in_14; row = in_13;
  //   ru_diag = in_7; start = in_11; turn = in_12; white[5:0] = in_2; white_col[5:0] = in_5
endmodule

module to_counter (
  input  [5:0] in_1,
  output [3:0] out_2,
  output [3:0] out_3
);

  wire [5:0] divider_1_out, divider_1_rem;

  Divider #(.width(6)) divider_1 (.a(in_1), .b(6'b001010), .out(divider_1_out), .rem(divider_1_rem));  // open: upper
  Bit_Extender #(.in_width(6), .out_width(4)) bit_extender_1 (.in(divider_1_out), .out(out_2));
  Bit_Extender #(.in_width(6), .out_width(4)) bit_extender_2 (.in(divider_1_rem), .out(out_3));
endmodule

module zero_or_not (
  input  [5:0] in_1,
  output out_2
);

  or or_1 (out_2, in_1[0], in_1[1], in_1[2], in_1[3], in_1[4], in_1[5]);
endmodule

module _6numRow_to_3numRow (
  input  [5:0] in_1,
  output [2:0] out_2
);

  wire [2:0] and_1_out, and_2_out, and_3_out, and_4_out, and_5_out, and_6_out, and_7_out, and_8_out,
       and_9_out, and_10_out, and_11_out, and_12_out, or_1_out, or_2_out, or_3_out, or_4_out, or_5_out,
       or_6_out;
  wire [2:2] not_1_out, not_2_out, not_3_out, not_4_out, not_5_out, not_6_out;

  assign and_1_out = 3'b000 & {3{not_1_out[2]}};  // AND_Gate and_1, 3 bits wide
  not not_1 (not_1_out[2], in_1[0]);
  assign and_2_out = {3{in_1[0]}} & 3'b000;  // AND_Gate and_2, 3 bits wide
  assign and_3_out = 3'b000 & {3{not_2_out[2]}};  // AND_Gate and_3, 3 bits wide
  not not_2 (not_2_out[2], in_1[1]);
  assign and_4_out = {3{in_1[1]}} & 3'b001;  // AND_Gate and_4, 3 bits wide
  assign and_5_out = 3'b000 & {3{not_3_out[2]}};  // AND_Gate and_5, 3 bits wide
  not not_3 (not_3_out[2], in_1[2]);
  assign and_6_out = {3{in_1[2]}} & 3'b010;  // AND_Gate and_6, 3 bits wide
  assign and_7_out = 3'b000 & {3{not_4_out[2]}};  // AND_Gate and_7, 3 bits wide
  not not_4 (not_4_out[2], in_1[3]);
  assign and_8_out = {3{in_1[3]}} & 3'b011;  // AND_Gate and_8, 3 bits wide
  assign and_9_out = 3'b000 & {3{not_5_out[2]}};  // AND_Gate and_9, 3 bits wide
  not not_5 (not_5_out[2], in_1[4]);
  assign and_10_out = {3{in_1[4]}} & 3'b100;  // AND_Gate and_10, 3 bits wide
  assign and_11_out = 3'b000 & {3{not_6_out[2]}};  // AND_Gate and_11, 3 bits wide
  not not_6 (not_6_out[2], in_1[5]);
  assign and_12_out = {3{in_1[5]}} & 3'b101;  // AND_Gate and_12, 3 bits wide
  assign or_1_out = and_1_out | and_2_out;  // OR_Gate or_1, 3 bits wide
  assign or_2_out = and_3_out | and_4_out;  // OR_Gate or_2, 3 bits wide
  assign or_3_out = and_5_out | and_6_out;  // OR_Gate or_3, 3 bits wide
  assign or_4_out = and_7_out | and_8_out;  // OR_Gate or_4, 3 bits wide
  assign or_5_out = and_9_out | and_10_out;  // OR_Gate or_5, 3 bits wide
  assign or_6_out = and_11_out | and_12_out;  // OR_Gate or_6, 3 bits wide
  assign out_2 = or_1_out | or_2_out | or_3_out | or_4_out | or_5_out | or_6_out;  // OR_Gate or_7, 3 bits wide
endmodule

module coloring_hor (
  input  [5:0] min_left,
  input  [5:0] max_right,
  input  [5:0] column,
  input  [5:0] now_white,
  input  [5:0] now_black,
  output [5:0] out_6,
  output [5:0] out_7
);

  wire _1break_l, _1break_r, _2break_l, _2break_r, _3break_l, _3break_r, _4break_l, _4break_r, _5break_l,
       _5break_r, and_1_out, and_2_out, and_3_out, and_4_out, and_5_out, and_6_out, and_7_out, and_8_out,
       and_9_out, and_10_out, and_11_out, and_12_out, and_13_out, and_14_out, and_15_out, and_16_out,
       and_17_out, and_18_out, and_19_out, and_20_out, and_21_out, and_22_out, and_23_out, and_24_out,
       and_25_out, and_26_out, and_27_out, and_28_out, compare_6bit_1_out_3, compare_6bit_2_out_3,
       compare_6bit_3_out_3, compare_6bit_4_out_3, compare_6bit_6_out_3, compare_6bit_7_out_3,
       compare_6bit_9_out_3, compare_6bit_10_out_3, compare_6bit_11_out_3, compare_6bit_12_out_3, maxr_not_0,
       minl_not_0, not_1_out, not_2_out, not_3_out, not_4_out, not_5_out, not_6_out, not_7_out, not_8_out,
       not_9_out, not_10_out, not_11_out, not_12_out, not_13_out, not_14_out, not_15_out, not_16_out,
       not_17_out, not_18_out, not_19_out, not_20_out, not_21_out, not_22_out, not_23_out, not_26_out,
       not_27_out, not_28_out, not_29_out, not_30_out, not_31_out, not_32_out, not_35_out, not_36_out,
       not_37_out, not_38_out, not_39_out, not_40_out, not_41_out, not_42_out, not_43_out, not_44_out,
       not_45_out, not_46_out, not_47_out, not_48_out, not_49_out, not_50_out, not_51_out, not_52_out,
       not_53_out, not_56_out, not_57_out, not_58_out, not_59_out, not_60_out, not_61_out, not_62_out,
       not_63_out, not_64_out, not_65_out, not_68_out;
  wire [2:0] bit_extender_1_out, bit_extender_2_out, bit_extender_3_out, bit_extender_4_out,
       bit_extender_5_out, bit_extender_6_out, bit_extender_7_out, bit_extender_8_out;
  wire [5:0] _1bre_b_l, _1bre_b_r, _1bre_w_l, _1bre_w_r, _2bre_b_l, _2bre_b_r, _2bre_w_l, _2bre_w_r,
       _3bre_b_l, _3bre_b_r, _3bre_w_l, _3bre_w_r, _4bre_b_l, _4bre_b_r, _4bre_w_l, _4bre_w_r, or_1_out,
       or_3_out, or_10_out, or_11_out, pull_resistor_1_node, pull_resistor_2_node, pull_resistor_3_node,
       pull_resistor_4_node, pull_resistor_9_node, pull_resistor_18_node, shifter_1_out, shifter_2_out,
       shifter_3_out, shifter_4_out, shifter_5_out, shifter_6_out, shifter_7_out, shifter_8_out,
       transistor_5_out, transistor_6_out, transistor_7_out, transistor_8_out, transistor_9_out,
       transistor_11_out, transistor_12_out, transistor_13_out, transistor_14_out, transistor_15_out,
       transistor_16_out, transistor_17_out, transistor_18_out, transistor_20_out, transistor_21_out,
       transistor_22_out;

  not not_1 (not_1_out, _2break_l);
  and and_1 (and_1_out, not_1_out, _3break_l, not_11_out);
  not not_2 (not_2_out, _3break_l);
  not not_3 (not_3_out, _2break_l);
  not not_4 (not_4_out, _3break_l);
  not not_5 (not_5_out, _2break_l);
  not not_6 (not_6_out, _2break_r);
  and and_2 (and_2_out, not_6_out, _3break_r, not_14_out);
  not not_7 (not_7_out, _2break_r);
  not not_8 (not_8_out, _3break_r);
  and and_3 (and_3_out, not_7_out, not_8_out, not_15_out, _4break_r);
  not not_9 (not_9_out, _3break_r);
  not not_10 (not_10_out, _2break_r);
  and and_4 (and_4_out, not_10_out, not_9_out, _5break_r, not_16_out, not_17_out);
  not not_11 (not_11_out, _1break_l);
  Pull_Resistor pull_resistor_1 (.node(pull_resistor_1_node));
  Transistor #(.\type ("n"), .width(6)) transistor_1 (.in(_2bre_w_l), .out(pull_resistor_1_node), .gate(and_1_out));
  not not_12 (not_12_out, _1break_l);
  and and_5 (and_5_out, not_3_out, not_2_out, not_12_out, _4break_l);
  Pull_Resistor pull_resistor_2 (.node(pull_resistor_2_node));
  Transistor #(.\type ("n"), .width(6)) transistor_2 (.in(_3bre_w_l), .out(pull_resistor_2_node), .gate(and_5_out));
  not not_13 (not_13_out, _1break_l);
  and and_6 (and_6_out, not_5_out, not_4_out, _5break_l, not_13_out, not_19_out);
  Pull_Resistor pull_resistor_3 (.node(pull_resistor_3_node));
  Transistor #(.\type ("n"), .width(6)) transistor_3 (.in(_4bre_w_l), .out(pull_resistor_3_node), .gate(and_6_out));
  not not_14 (not_14_out, _1break_r);
  Pull_Resistor pull_resistor_4 (.node(pull_resistor_4_node));
  Transistor #(.\type ("n"), .width(6)) transistor_4 (.in(_2bre_w_r), .out(pull_resistor_4_node), .gate(and_2_out));
  not not_15 (not_15_out, _1break_r);
  Transistor #(.\type ("n"), .width(6)) transistor_5 (.in(_3bre_w_r), .out(transistor_5_out), .gate(and_3_out));
  Pull_Resistor pull_resistor_5 (.node(transistor_5_out));
  not not_16 (not_16_out, _1break_r);
  not not_17 (not_17_out, _4break_r);
  Transistor #(.\type ("n"), .width(6)) transistor_6 (.in(_4bre_w_r), .out(transistor_6_out), .gate(and_4_out));
  Pull_Resistor pull_resistor_6 (.node(transistor_6_out));
  not not_18 (not_18_out, _2break_l);
  not not_19 (not_19_out, _4break_l);
  and and_7 (and_7_out, _2break_r, not_26_out);
  not not_20 (not_20_out, _2break_r);
  not not_21 (not_21_out, _1break_l);
  and and_8 (and_8_out, _2break_l, not_21_out);
  Transistor #(.\type ("n"), .width(6)) transistor_7 (.in(_1bre_w_l), .out(transistor_7_out), .gate(and_8_out));
  Pull_Resistor pull_resistor_7 (.node(transistor_7_out));
  not not_22 (not_22_out, _5break_l);
  not not_23 (not_23_out, _3break_l);
  and and_9 (and_9_out, not_18_out, not_23_out, not_22_out, not_29_out, not_30_out);
  and and_10 (and_10_out, maxr_not_0, compare_6bit_1_out_3);
  not not_24 (_1break_r, and_10_out);
  compare_6bit compare_6bit_1 (.in_1(max_right), .in_2(column), .out_3(compare_6bit_1_out_3));
  and and_11 (and_11_out, minl_not_0, compare_6bit_2_out_3);
  not not_25 (_1break_l, and_11_out);
  compare_6bit compare_6bit_2 (.in_1(min_left), .in_2(column), .out_3(compare_6bit_2_out_3));
  not not_26 (not_26_out, _1break_r);
  Transistor #(.\type ("n"), .width(6)) transistor_8 (.in(_1bre_w_r), .out(transistor_8_out), .gate(and_7_out));
  Pull_Resistor pull_resistor_8 (.node(transistor_8_out));
  not not_27 (not_27_out, _5break_r);
  not not_28 (not_28_out, _3break_r);
  and and_12 (and_12_out, not_20_out, not_28_out, not_27_out, not_31_out, not_32_out);
  Transistor #(.\type ("n"), .width(6)) transistor_9 (.in({6{1'b1}}), .out(transistor_9_out), .gate(and_12_out));
  not not_29 (not_29_out, _1break_l);
  not not_30 (not_30_out, _4break_l);
  Pull_Resistor pull_resistor_9 (.node(pull_resistor_9_node));
  Transistor #(.\type ("n"), .width(6)) transistor_10 (.in({6{1'b1}}), .out(pull_resistor_9_node), .gate(and_9_out));
  Shifter #(.width(6), .shift("lr")) shifter_1 (.in(column), .\dist (bit_extender_1_out), .out(shifter_1_out));
  assign bit_extender_1_out = {{2{1'b0}}, and_10_out};  // Bit_Extender bit_extender_1
  Shifter #(.width(6)) shifter_2 (.in(column), .\dist (bit_extender_2_out), .out(shifter_2_out));
  assign bit_extender_2_out = {{2{1'b0}}, and_11_out};  // Bit_Extender bit_extender_2
  not not_31 (not_31_out, _1break_r);
  not not_32 (not_32_out, _4break_r);
  Pull_Resistor pull_resistor_10 (.node(transistor_9_out));
  assign or_1_out = transistor_7_out | pull_resistor_1_node | pull_resistor_9_node | pull_resistor_2_node | pull_resistor_3_node;  // OR_Gate or_1, 6 bits wide
  assign _1bre_w_r = now_white | shifter_1_out;  // OR_Gate or_2, 6 bits wide
  compare_6bit compare_6bit_3 (.in_1(max_right), .in_2(shifter_1_out), .out_3(compare_6bit_3_out_3));
  compare_6bit compare_6bit_4 (.in_1(min_left), .in_2(shifter_2_out), .out_3(compare_6bit_4_out_3));
  assign or_3_out = transistor_8_out | pull_resistor_4_node | transistor_9_out | transistor_5_out | transistor_6_out;  // OR_Gate or_3, 6 bits wide
  assign out_6 = or_3_out | now_white | or_1_out;  // OR_Gate or_4, 6 bits wide
  assign _1bre_b_r = shifter_1_out ^ now_black;  // XOR_Gate xor_1, 6 bits wide
  and and_13 (and_13_out, maxr_not_0, compare_6bit_3_out_3);
  assign bit_extender_3_out = {{2{1'b0}}, and_13_out};  // Bit_Extender bit_extender_3
  not not_33 (_2break_r, and_13_out);
  assign _1bre_w_l = now_white | shifter_2_out;  // OR_Gate or_5, 6 bits wide
  assign _1bre_b_l = shifter_2_out ^ now_black;  // XOR_Gate xor_2, 6 bits wide
  and and_14 (and_14_out, minl_not_0, compare_6bit_4_out_3);
  not not_34 (_2break_l, and_14_out);
  compare_6bit compare_6bit_5 (.in_1(min_left), .in_2({6{1'b0}}), .out_3(minl_not_0));
  not not_35 (not_35_out, _2break_l);
  not not_36 (not_36_out, _2break_l);
  not not_37 (not_37_out, _2break_l);
  not not_38 (not_38_out, _3break_l);
  not not_39 (not_39_out, _2break_l);
  Shifter #(.width(6), .shift("lr")) shifter_3 (.in(shifter_1_out), .\dist (bit_extender_3_out), .out(shifter_3_out));
  // Probe on _1bre_b_l
  Shifter #(.width(6)) shifter_4 (.in(shifter_2_out), .\dist (bit_extender_4_out), .out(shifter_4_out));
  assign bit_extender_4_out = {{2{1'b0}}, and_14_out};  // Bit_Extender bit_extender_4
  not not_40 (not_40_out, _2break_r);
  not not_41 (not_41_out, _2break_r);
  not not_42 (not_42_out, _2break_r);
  and and_15 (and_15_out, not_35_out, _3break_l, not_49_out);
  Transistor #(.\type ("n"), .width(6)) transistor_11 (.in(_2bre_b_l), .out(transistor_11_out), .gate(and_15_out));
  not not_43 (not_43_out, _3break_l);
  and and_16 (and_16_out, not_36_out, not_43_out, not_50_out, _4break_l);
  not not_44 (not_44_out, _3break_l);
  and and_17 (and_17_out, not_37_out, not_44_out, _5break_l, not_51_out, not_52_out);
  not not_45 (not_45_out, _5break_l);
  not not_46 (not_46_out, _1break_l);
  and and_18 (and_18_out, not_39_out, not_38_out, not_45_out, not_46_out, not_53_out);
  Transistor #(.\type ("n"), .width(6)) transistor_12 (.in({6{1'b0}}), .out(transistor_12_out), .gate(and_18_out));
  Pull_Resistor pull_resistor_11 (.node(transistor_12_out));
  assign _2bre_w_r = _1bre_w_r | shifter_3_out;  // OR_Gate or_6, 6 bits wide
  compare_6bit compare_6bit_6 (.in_1(max_right), .in_2(shifter_3_out), .out_3(compare_6bit_6_out_3));
  compare_6bit compare_6bit_7 (.in_1(min_left), .in_2(shifter_4_out), .out_3(compare_6bit_7_out_3));
  compare_6bit compare_6bit_8 (.in_1(max_right), .in_2({6{1'b0}}), .out_3(maxr_not_0));
  and and_19 (and_19_out, not_40_out, _3break_r, not_56_out);
  Transistor #(.\type ("n"), .width(6)) transistor_13 (.in(_2bre_b_r), .out(transistor_13_out), .gate(and_19_out));
  not not_47 (not_47_out, _3break_r);
  and and_20 (and_20_out, not_41_out, not_47_out, not_57_out, _4break_r);
  Transistor #(.\type ("n"), .width(6)) transistor_14 (.in(_3bre_b_r), .out(transistor_14_out), .gate(and_20_out));
  not not_48 (not_48_out, _3break_r);
  and and_21 (and_21_out, not_42_out, not_48_out, _5break_r, not_59_out, not_58_out);
  Transistor #(.\type ("n"), .width(6)) transistor_15 (.in(_4bre_b_r), .out(transistor_15_out), .gate(and_21_out));
  not not_49 (not_49_out, _1break_l);
  Pull_Resistor pull_resistor_12 (.node(transistor_11_out));
  not not_50 (not_50_out, _1break_l);
  Transistor #(.\type ("n"), .width(6)) transistor_16 (.in(_3bre_b_l), .out(transistor_16_out), .gate(and_16_out));
  Pull_Resistor pull_resistor_13 (.node(transistor_16_out));
  not not_51 (not_51_out, _1break_l);
  not not_52 (not_52_out, _4break_l);
  Transistor #(.\type ("n"), .width(6)) transistor_17 (.in(_4bre_b_l), .out(transistor_17_out), .gate(and_17_out));
  Pull_Resistor pull_resistor_14 (.node(transistor_17_out));
  not not_53 (not_53_out, _4break_l);
  assign _2bre_b_r = shifter_3_out ^ _1bre_b_r;  // XOR_Gate xor_3, 6 bits wide
  and and_22 (and_22_out, maxr_not_0, compare_6bit_6_out_3);
  assign bit_extender_5_out = {{2{1'b0}}, and_22_out};  // Bit_Extender bit_extender_5
  not not_54 (_3break_r, and_22_out);
  assign _2bre_w_l = _1bre_w_l | shifter_4_out;  // OR_Gate or_7, 6 bits wide
  assign _2bre_b_l = shifter_4_out ^ _1bre_b_l;  // XOR_Gate xor_4, 6 bits wide
  and and_23 (and_23_out, minl_not_0, compare_6bit_7_out_3);
  not not_55 (_3break_l, and_23_out);
  not not_56 (not_56_out, _1break_r);
  Pull_Resistor pull_resistor_15 (.node(transistor_13_out));
  // Probe on transistor_13_out
  not not_57 (not_57_out, _1break_r);
  Pull_Resistor pull_resistor_16 (.node(transistor_14_out));
  not not_58 (not_58_out, _4break_r);
  not not_59 (not_59_out, _1break_r);
  Pull_Resistor pull_resistor_17 (.node(transistor_15_out));
  not not_60 (not_60_out, _1break_l);
  and and_24 (and_24_out, _2break_l, not_60_out);
  Shifter #(.width(6), .shift("lr")) shifter_5 (.in(shifter_3_out), .\dist (bit_extender_5_out), .out(shifter_5_out));
  Shifter #(.width(6)) shifter_6 (.in(shifter_4_out), .\dist (bit_extender_6_out), .out(shifter_6_out));
  assign bit_extender_6_out = {{2{1'b0}}, and_23_out};  // Bit_Extender bit_extender_6
  not not_61 (not_61_out, _2break_r);
  not not_62 (not_62_out, _1break_r);
  and and_25 (and_25_out, _2break_r, not_62_out);
  Transistor #(.\type ("n"), .width(6)) transistor_18 (.in(_1bre_b_r), .out(transistor_18_out), .gate(and_25_out));
  Pull_Resistor pull_resistor_18 (.node(pull_resistor_18_node));
  Transistor #(.\type ("n"), .width(6)) transistor_19 (.in(_1bre_b_l), .out(pull_resistor_18_node), .gate(and_24_out));
  Transistor #(.\type ("n"), .width(6)) transistor_20 (.in(now_black), .out(transistor_20_out), .gate(_1break_l));
  assign _3bre_w_r = _2bre_w_r | shifter_5_out;  // OR_Gate or_8, 6 bits wide
  and and_26 (and_26_out, maxr_not_0, compare_6bit_9_out_3);
  compare_6bit compare_6bit_9 (.in_1(max_right), .in_2(shifter_5_out), .out_3(compare_6bit_9_out_3));
  assign _3bre_w_l = _2bre_w_l | shifter_6_out;  // OR_Gate or_9, 6 bits wide
  compare_6bit compare_6bit_10 (.in_1(min_left), .in_2(shifter_6_out), .out_3(compare_6bit_10_out_3));
  not not_63 (not_63_out, _5break_r);
  not not_64 (not_64_out, _1break_r);
  not not_65 (not_65_out, _3break_r);
  and and_27 (and_27_out, not_61_out, not_65_out, not_63_out, not_64_out, not_68_out);
  Transistor #(.\type ("n"), .width(6)) transistor_21 (.in({6{1'b0}}), .out(transistor_21_out), .gate(and_27_out));
  Pull_Resistor pull_resistor_19 (.node(transistor_18_out));
  Transistor #(.\type ("n"), .width(6)) transistor_22 (.in(now_black), .out(transistor_22_out), .gate(_1break_r));
  assign or_10_out = transistor_12_out | pull_resistor_18_node | transistor_11_out | transistor_16_out | transistor_17_out | transistor_20_out;  // OR_Gate or_10, 6 bits wide
  Pull_Resistor pull_resistor_20 (.node(transistor_20_out));
  assign _3bre_b_r = shifter_5_out ^ _2bre_b_r;  // XOR_Gate xor_5, 6 bits wide
  assign bit_extender_7_out = {{2{1'b0}}, and_26_out};  // Bit_Extender bit_extender_7
  not not_66 (_4break_r, and_26_out);
  assign _3bre_b_l = shifter_6_out ^ _2bre_b_l;  // XOR_Gate xor_6, 6 bits wide
  and and_28 (and_28_out, minl_not_0, compare_6bit_10_out_3);
  assign bit_extender_8_out = {{2{1'b0}}, and_28_out};  // Bit_Extender bit_extender_8
  not not_67 (_4break_l, and_28_out);
  not not_68 (not_68_out, _4break_r);
  Pull_Resistor pull_resistor_21 (.node(transistor_21_out));
  assign or_11_out = transistor_21_out | transistor_18_out | transistor_13_out | transistor_14_out | transistor_15_out | transistor_22_out;  // OR_Gate or_11, 6 bits wide
  Pull_Resistor pull_resistor_22 (.node(transistor_22_out));
  Shifter #(.width(6), .shift("lr")) shifter_7 (.in(shifter_5_out), .\dist (bit_extender_7_out), .out(shifter_7_out));
  Shifter #(.width(6)) shifter_8 (.in(shifter_6_out), .\dist (bit_extender_8_out), .out(shifter_8_out));
  assign out_7 = or_11_out & or_10_out;  // AND_Gate and_29, 6 bits wide
  assign _4bre_w_r = _3bre_w_r | shifter_7_out;  // OR_Gate or_12, 6 bits wide
  compare_6bit compare_6bit_11 (.in_1(max_right), .in_2(shifter_7_out), .out_3(compare_6bit_11_out_3));
  not not_69 (_5break_r, compare_6bit_11_out_3);
  assign _4bre_w_l = _3bre_w_l | shifter_8_out;  // OR_Gate or_13, 6 bits wide
  not not_70 (_5break_l, compare_6bit_12_out_3);
  compare_6bit compare_6bit_12 (.in_1(min_left), .in_2(shifter_8_out), .out_3(compare_6bit_12_out_3));
  assign _4bre_b_r = shifter_7_out ^ _3bre_b_r;  // XOR_Gate xor_7, 6 bits wide
  assign _4bre_b_l = shifter_8_out ^ _3bre_b_l;  // XOR_Gate xor_8, 6 bits wide

  // Other names for the same wires on the sheet: max_r[5:0] = max_right; min_l[5:0] = min_left; n_b[5:0] = now_black;
  //   n_w[5:0] = now_white
endmodule
module coloring_diag (
  input  [5:0] max_column_ru,
  input  [5:0] in_2,
  input  [5:0] in_3,
  input  [5:0] in_4,
  input  [5:0] in_5,
  input  [5:0] max_column_lu,
  input  [5:0] in_7,
  input  [5:0] in_8,
  input  [5:0] in_9,
  input  [5:0] in_10,
  input  [5:0] max_column_rd,
  input  [5:0] in_12,
  input  [5:0] in_13,
  input  [5:0] in_14,
  input  [5:0] in_15,
  input  [5:0] max_column_ld,
  input  [5:0] now_column,
  input  [5:0] now_row,
  output [5:0] out_19,
  output [5:0] out_20,
  output [5:0] out_21,
  output [5:0] out_22,
  output [5:0] out_23,
  output [5:0] out_24,
  output [5:0] out_25,
  output [5:0] out_26,
  output [5:0] out_27,
  output [5:0] out_28,
  output [5:0] out_29,
  output [5:0] out_30
);

  wire _1break_ld, _1break_lu, _1break_rd, _1break_ru, _2break_down, _2break_ld, _2break_lu, _2break_rd,
       _2break_ru, _2break_up, _3break_down, _3break_ld, _3break_lu, _3break_rd, _3break_ru, _3break_up,
       _4break_down, _4break_ld, _4break_lu, _4break_rd, _4break_ru, _4break_up, _5break_down, _5break_ld,
       _5break_lu, _5break_rd, _5break_ru, _5break_up, _6break_down, _6break_ld, _6break_lu, _6break_rd,
       _6break_ru, _6break_up, and_1_out, and_2_out, and_3_out, and_4_out, and_5_out, and_6_out, and_7_out,
       and_8_out, and_9_out, and_10_out, and_11_out, and_12_out, and_13_out, and_14_out, and_15_out,
       and_16_out, and_19_out, and_20_out, and_21_out, and_22_out, and_24_out, and_25_out, and_26_out,
       and_27_out, compare_6bit_2_out_3, compare_6bit_3_out_3, compare_6bit_4_out_3, compare_6bit_5_out_3,
       compare_6bit_6_out_3, compare_6bit_7_out_3, compare_6bit_9_out_3, compare_6bit_10_out_3,
       compare_6bit_12_out_3, compare_6bit_13_out_3, compare_6bit_14_out_3, compare_6bit_15_out_3,
       compare_6bit_17_out_3, compare_6bit_18_out_3, compare_6bit_19_out_3, compare_6bit_20_out_3,
       compare_6bit_21_out_3, compare_6bit_22_out_3, compare_6bit_23_out_3, compare_6bit_24_out_3,
       compare_6bit_25_out_3, compare_6bit_26_out_3, compare_6bit_27_out_3, compare_6bit_28_out_3,
       compare_6bit_29_out_3, compare_6bit_30_out_3, compare_6bit_31_out_3, compare_6bit_32_out_3,
       compare_6bit_33_out_3, compare_6bit_34_out_3, compare_6bit_35_out_3, compare_6bit_36_out_3,
       compare_6bit_37_out_3, compare_6bit_38_out_3, compare_6bit_39_out_3, compare_6bit_40_out_3,
       max_ld_not_0, max_lu_not_0, max_rd_not_0, max_ru_not_0, zero_or_not_1_out_2, zero_or_not_2_out_2,
       zero_or_not_3_out_2, zero_or_not_4_out_2, zero_or_not_5_out_2, zero_or_not_6_out_2,
       zero_or_not_7_out_2, zero_or_not_8_out_2, zero_or_not_9_out_2, zero_or_not_10_out_2,
       zero_or_not_11_out_2, zero_or_not_12_out_2, zero_or_not_13_out_2, zero_or_not_14_out_2,
       zero_or_not_15_out_2, zero_or_not_16_out_2, zero_or_not_17_out_2, zero_or_not_18_out_2,
       zero_or_not_19_out_2, zero_or_not_20_out_2;
  wire [2:0] bit_extender_1_out, bit_extender_2_out, bit_extender_3_out, bit_extender_4_out,
       bit_extender_5_out, bit_extender_6_out, bit_extender_7_out, bit_extender_8_out, bit_extender_9_out,
       bit_extender_10_out, bit_extender_11_out, bit_extender_12_out, bit_extender_13_out,
       bit_extender_14_out, bit_extender_15_out, bit_extender_16_out, bit_extender_17_out,
       bit_extender_18_out, bit_extender_19_out, bit_extender_20_out, bit_extender_21_out,
       bit_extender_22_out, bit_extender_23_out, bit_extender_24_out, bit_extender_25_out,
       bit_extender_26_out, bit_extender_27_out, bit_extender_28_out, bit_extender_29_out,
       bit_extender_30_out, row_down2, row_down3, row_down4, row_down5, row_down6, row_up2, row_up3, row_up4,
       row_up5, row_up6;
  wire [5:0] _0b_ou, _0w_ou, _1b_ou, _1w_ou, _2b_ou, _2w_ou, _3b_ou, _3w_ou, _4b_ou, _4w_ou, _5b_ou, _5w_ou,
       and_17_out, and_18_out, and_23_out, and_28_out, and_29_out, and_30_out, and_31_out, and_32_out,
       and_33_out, and_34_out, multiplexer_1_out, multiplexer_2_out, multiplexer_3_out, multiplexer_4_out,
       multiplexer_5_out, multiplexer_6_out, multiplexer_7_out, multiplexer_8_out, multiplexer_9_out,
       multiplexer_10_out, multiplexer_11_out, multiplexer_12_out, multiplexer_13_out, multiplexer_14_out,
       multiplexer_15_out, multiplexer_16_out, multiplexer_17_out, multiplexer_18_out, multiplexer_19_out,
       multiplexer_20_out, multiplexer_21_out, multiplexer_22_out, multiplexer_23_out, multiplexer_24_out,
       multiplexer_25_out, multiplexer_26_out, multiplexer_27_out, multiplexer_28_out, multiplexer_29_out,
       multiplexer_30_out, multiplexer_31_out, multiplexer_32_out, multiplexer_33_out, multiplexer_34_out,
       multiplexer_35_out, multiplexer_36_out, multiplexer_37_out, multiplexer_38_out, multiplexer_39_out,
       multiplexer_40_out, or_13_out, or_14_out, or_19_out, or_20_out, or_25_out, or_26_out, or_27_out,
       or_28_out, or_29_out, or_30_out, pull_resistor_4_node, pull_resistor_5_node, pull_resistor_6_node,
       pull_resistor_7_node, pull_resistor_10_node, pull_resistor_11_node, pull_resistor_13_node,
       pull_resistor_16_node, pull_resistor_18_node, pull_resistor_19_node, res2_b_ld, res2_b_lu, res2_b_rd,
       res2_b_ru, res2_w_ld, res2_w_lu, res2_w_rd, res2_w_ru, res3_b_ld, res3_b_lu, res3_b_rd, res3_b_ru,
       res3_w_ld, res3_w_lu, res3_w_rd, res3_w_ru, res4_b_ld, res4_b_lu, res4_b_rd, res4_b_ru, res4_w_ld,
       res4_w_lu, res4_w_rd, res4_w_ru, res5_b_ld, res5_b_lu, res5_b_rd, res5_b_ru, res5_w_ld, res5_w_lu,
       res5_w_rd, res5_w_ru, res6_b_ld, res6_b_lu, res6_b_rd, res6_b_ru, res6_w_ld, res6_w_lu, res6_w_rd,
       res6_w_ru, shifter_1_out, shifter_2_out, shifter_3_out, shifter_4_out, shifter_5_out, shifter_6_out,
       shifter_7_out, shifter_8_out, shifter_9_out, shifter_10_out, shifter_11_out, shifter_12_out,
       shifter_13_out, shifter_14_out, shifter_15_out, shifter_16_out, shifter_17_out, shifter_18_out,
       shifter_19_out, shifter_20_out, shifter_21_out, shifter_22_out, shifter_23_out, shifter_24_out,
       shifter_25_out, shifter_26_out, shifter_27_out, shifter_28_out, shifter_29_out, shifter_30_out,
       transistor_1_out, transistor_2_out, transistor_3_out, transistor_8_out, transistor_9_out,
       transistor_12_out, transistor_14_out, transistor_15_out, transistor_17_out, transistor_20_out;

  compare_6bit compare_6bit_1 (.in_1(max_column_ru), .in_2({6{1'b0}}), .out_3(max_ru_not_0));
  compare_6bit compare_6bit_2 (.in_1(max_column_ru), .in_2(now_column), .out_3(compare_6bit_2_out_3));
  compare_6bit compare_6bit_3 (.in_1(max_column_lu), .in_2(now_column), .out_3(compare_6bit_3_out_3));
  compare_6bit compare_6bit_4 (.in_1(max_column_ld), .in_2(now_column), .out_3(compare_6bit_4_out_3));
  compare_6bit compare_6bit_5 (.in_1(max_column_rd), .in_2(now_column), .out_3(compare_6bit_5_out_3));
  compare_6bit compare_6bit_6 (.in_1(6'b000001), .in_2(now_row), .out_3(compare_6bit_6_out_3));
  compare_6bit compare_6bit_7 (.in_1(6'b100000), .in_2(now_row), .out_3(compare_6bit_7_out_3));
  assign bit_extender_1_out = {{2{1'b0}}, and_1_out};  // Bit_Extender bit_extender_1
  and and_1 (and_1_out, max_ru_not_0, compare_6bit_2_out_3);
  not not_1 (_1break_ru, and_1_out);
  assign bit_extender_2_out = {{2{1'b0}}, and_2_out};  // Bit_Extender bit_extender_2
  and and_2 (and_2_out, max_lu_not_0, compare_6bit_3_out_3);
  not not_2 (_1break_lu, and_2_out);
  assign bit_extender_3_out = {{2{1'b0}}, and_3_out};  // Bit_Extender bit_extender_3
  and and_3 (and_3_out, max_ld_not_0, compare_6bit_4_out_3);
  not not_3 (_1break_ld, and_3_out);
  assign bit_extender_4_out = {{2{1'b0}}, and_4_out};  // Bit_Extender bit_extender_4
  and and_4 (and_4_out, max_rd_not_0, compare_6bit_5_out_3);
  not not_4 (_1break_rd, and_4_out);
  assign bit_extender_5_out = {{2{1'b0}}, compare_6bit_6_out_3};  // Bit_Extender bit_extender_5
  assign bit_extender_6_out = {{2{1'b0}}, compare_6bit_7_out_3};  // Bit_Extender bit_extender_6
  compare_6bit compare_6bit_8 (.in_1(max_column_lu), .in_2({6{1'b0}}), .out_3(max_lu_not_0));
  Shifter #(.width(6), .shift("lr")) shifter_1 (.in(now_column), .\dist (bit_extender_1_out), .out(shifter_1_out));
  Transistor #(.width(6)) transistor_1 (.in(shifter_1_out), .out(transistor_1_out), .gate(_1break_ru));
  Pull_Resistor pull_resistor_1 (.node(transistor_1_out));
  Shifter #(.width(6)) shifter_2 (.in(now_column), .\dist (bit_extender_2_out), .out(shifter_2_out));
  Transistor #(.width(6)) transistor_2 (.in(shifter_2_out), .out(transistor_2_out), .gate(_1break_lu));
  Pull_Resistor pull_resistor_2 (.node(transistor_2_out));
  Transistor #(.width(6)) transistor_3 (.in(shifter_3_out), .out(transistor_3_out), .gate(_1break_ld));
  Pull_Resistor pull_resistor_3 (.node(transistor_3_out));
  Shifter #(.width(6)) shifter_3 (.in(now_column), .\dist (bit_extender_3_out), .out(shifter_3_out));
  Pull_Resistor pull_resistor_4 (.node(pull_resistor_4_node));
  Transistor #(.width(6)) transistor_4 (.in(shifter_4_out), .out(pull_resistor_4_node), .gate(_1break_rd));
  Shifter #(.width(6), .shift("lr")) shifter_4 (.in(now_column), .\dist (bit_extender_4_out), .out(shifter_4_out));
  Shifter #(.width(6), .shift("lr")) shifter_5 (.in(now_row), .\dist (bit_extender_5_out), .out(shifter_5_out));
  Shifter #(.width(6)) shifter_6 (.in(now_row), .\dist (bit_extender_6_out), .out(shifter_6_out));
  Multiplexer #(.select(3), .width(6)) multiplexer_1 (
    .in0(in_3), .in1(in_5), .in2(in_8), .in3(in_10), .in4(in_13), .in5(in_15), .out(multiplexer_1_out),
    .sel(row_up2));  // open: in6, in7, en
  Multiplexer #(.select(3), .width(6)) multiplexer_2 (
    .in0(in_3), .in1(in_5), .in2(in_8), .in3(in_10), .in4(in_13), .in5(in_15), .out(multiplexer_2_out),
    .sel(row_up2));  // open: in6, in7, en
  Multiplexer #(.select(3), .width(6)) multiplexer_3 (
    .in0(in_3), .in1(in_5), .in2(in_8), .in3(in_10), .in4(in_13), .in5(in_15), .out(multiplexer_3_out),
    .sel(row_down2));  // open: in6, in7, en
  Multiplexer #(.select(3), .width(6)) multiplexer_4 (
    .in0(in_3), .in1(in_5), .in2(in_8), .in3(in_10), .in4(in_13), .in5(in_15), .out(multiplexer_4_out),
    .sel(row_down2));  // open: in6, in7, en
  _6numRow_to_3numRow u_6numrow_to_3numrow_1 (.in_1(shifter_5_out), .out_2(row_up2));
  compare_6bit compare_6bit_9 (.in_1(6'b000001), .in_2(shifter_5_out), .out_3(compare_6bit_9_out_3));
  not not_5 (_2break_up, compare_6bit_9_out_3);
  _6numRow_to_3numRow u_6numrow_to_3numrow_2 (.in_1(shifter_6_out), .out_2(row_down2));
  compare_6bit compare_6bit_10 (.in_1(6'b100000), .in_2(shifter_6_out), .out_3(compare_6bit_10_out_3));
  not not_6 (_2break_down, compare_6bit_10_out_3);
  compare_6bit compare_6bit_11 (.in_1(max_column_rd), .in_2({6{1'b0}}), .out_3(max_rd_not_0));
  Multiplexer #(.select(3), .width(6)) multiplexer_5 (
    .in0(in_2), .in1(in_4), .in2(in_7), .in3(in_9), .in4(in_12), .in5(in_14), .out(multiplexer_5_out),
    .sel(row_up2));  // open: in6, in7, en
  and and_5 (and_5_out, max_ru_not_0, zero_or_not_1_out_2, compare_6bit_12_out_3);
  zero_or_not zero_or_not_1 (.in_1(transistor_1_out), .out_2(zero_or_not_1_out_2));
  compare_6bit compare_6bit_12 (.in_1(max_column_ru), .in_2(transistor_1_out), .out_3(compare_6bit_12_out_3));
  not not_7 (_2break_ru, and_5_out);
  Multiplexer #(.select(3), .width(6)) multiplexer_6 (
    .in0(in_2), .in1(in_4), .in2(in_7), .in3(in_9), .in4(in_12), .in5(in_14), .out(multiplexer_6_out),
    .sel(row_up2));  // open: in6, in7, en
  and and_6 (and_6_out, max_lu_not_0, zero_or_not_2_out_2, compare_6bit_13_out_3);
  zero_or_not zero_or_not_2 (.in_1(transistor_2_out), .out_2(zero_or_not_2_out_2));
  compare_6bit compare_6bit_13 (.in_1(max_column_lu), .in_2(transistor_2_out), .out_3(compare_6bit_13_out_3));
  not not_8 (_2break_lu, and_6_out);
  Multiplexer #(.select(3), .width(6)) multiplexer_7 (
    .in0(in_2), .in1(in_4), .in2(in_7), .in3(in_9), .in4(in_12), .in5(in_14), .out(multiplexer_7_out),
    .sel(row_down2));  // open: in6, in7, en
  and and_7 (and_7_out, max_ld_not_0, zero_or_not_3_out_2, compare_6bit_14_out_3);
  zero_or_not zero_or_not_3 (.in_1(transistor_3_out), .out_2(zero_or_not_3_out_2));
  compare_6bit compare_6bit_14 (.in_1(max_column_ld), .in_2(transistor_3_out), .out_3(compare_6bit_14_out_3));
  not not_9 (_2break_ld, and_7_out);
  Multiplexer #(.select(3), .width(6)) multiplexer_8 (
    .in0(in_2), .in1(in_4), .in2(in_7), .in3(in_9), .in4(in_12), .in5(in_14), .out(multiplexer_8_out),
    .sel(row_down2));  // open: in6, in7, en
  and and_8 (and_8_out, max_rd_not_0, zero_or_not_4_out_2, compare_6bit_15_out_3);
  zero_or_not zero_or_not_4 (.in_1(pull_resistor_4_node), .out_2(zero_or_not_4_out_2));
  compare_6bit compare_6bit_15 (.in_1(max_column_rd), .in_2(pull_resistor_4_node), .out_3(compare_6bit_15_out_3));
  not not_10 (_2break_rd, and_8_out);
  assign bit_extender_7_out = {{2{1'b0}}, compare_6bit_10_out_3};  // Bit_Extender bit_extender_7
  assign res2_w_ru = multiplexer_5_out | transistor_1_out;  // OR_Gate or_1, 6 bits wide
  assign res2_b_ru = transistor_1_out ^ multiplexer_1_out;  // XOR_Gate xor_1, 6 bits wide
  Shifter #(.width(6), .shift("lr")) shifter_7 (
    .in(transistor_1_out), .\dist (bit_extender_8_out), .out(shifter_7_out));
  assign bit_extender_8_out = {{2{1'b0}}, and_5_out};  // Bit_Extender bit_extender_8
  assign res2_w_lu = multiplexer_6_out | transistor_2_out;  // OR_Gate or_2, 6 bits wide
  assign res2_b_lu = transistor_2_out ^ multiplexer_2_out;  // XOR_Gate xor_2, 6 bits wide
  Shifter #(.width(6)) shifter_8 (.in(transistor_2_out), .\dist (bit_extender_9_out), .out(shifter_8_out));
  assign bit_extender_9_out = {{2{1'b0}}, and_6_out};  // Bit_Extender bit_extender_9
  assign res2_w_ld = multiplexer_7_out | transistor_3_out;  // OR_Gate or_3, 6 bits wide
  assign res2_b_ld = transistor_3_out ^ multiplexer_3_out;  // XOR_Gate xor_3, 6 bits wide
  Shifter #(.width(6)) shifter_9 (.in(transistor_3_out), .\dist (bit_extender_10_out), .out(shifter_9_out));
  assign bit_extender_10_out = {{2{1'b0}}, and_7_out};  // Bit_Extender bit_extender_10
  assign res2_w_rd = multiplexer_8_out | pull_resistor_4_node;  // OR_Gate or_4, 6 bits wide
  assign res2_b_rd = pull_resistor_4_node ^ multiplexer_4_out;  // XOR_Gate xor_4, 6 bits wide
  Shifter #(.width(6), .shift("lr")) shifter_10 (
    .in(pull_resistor_4_node), .\dist (bit_extender_11_out), .out(shifter_10_out));
  assign bit_extender_11_out = {{2{1'b0}}, and_8_out};  // Bit_Extender bit_extender_11
  Shifter #(.width(6), .shift("lr")) shifter_11 (
    .in(shifter_5_out), .\dist (bit_extender_12_out), .out(shifter_11_out));
  assign bit_extender_12_out = {{2{1'b0}}, compare_6bit_9_out_3};  // Bit_Extender bit_extender_12
  Shifter #(.width(6)) shifter_12 (.in(shifter_6_out), .\dist (bit_extender_7_out), .out(shifter_12_out));
  compare_6bit compare_6bit_16 (.in_1(max_column_ld), .in_2({6{1'b0}}), .out_3(max_ld_not_0));
  E_to_one_6bit e_to_one_6bit_1 (.in_1(_0w_ou), .out_2(out_19));
  E_to_one_6bit e_to_one_6bit_2 (.in_1(_1w_ou), .out_2(out_21));
  E_to_one_6bit e_to_one_6bit_3 (.in_1(_2w_ou), .out_2(out_23));
  E_to_one_6bit e_to_one_6bit_4 (.in_1(_3w_ou), .out_2(out_25));
  E_to_one_6bit e_to_one_6bit_5 (.in_1(_4w_ou), .out_2(out_27));
  E_to_one_6bit e_to_one_6bit_6 (.in_1(_5w_ou), .out_2(out_29));
  Pull_Resistor pull_resistor_5 (.node(pull_resistor_5_node));
  Transistor #(.width(6)) transistor_5 (.in(shifter_7_out), .out(pull_resistor_5_node), .gate(_2break_ru));
  Pull_Resistor pull_resistor_6 (.node(pull_resistor_6_node));
  Transistor #(.width(6)) transistor_6 (.in(shifter_8_out), .out(pull_resistor_6_node), .gate(_2break_lu));
  Pull_Resistor pull_resistor_7 (.node(pull_resistor_7_node));
  Transistor #(.width(6)) transistor_7 (.in(shifter_9_out), .out(pull_resistor_7_node), .gate(_2break_ld));
  Transistor #(.width(6)) transistor_8 (.in(shifter_10_out), .out(transistor_8_out), .gate(_2break_rd));
  Pull_Resistor pull_resistor_8 (.node(transistor_8_out));
  _6numRow_to_3numRow u_6numrow_to_3numrow_3 (.in_1(shifter_11_out), .out_2(row_up3));
  compare_6bit compare_6bit_17 (.in_1(6'b000001), .in_2(shifter_11_out), .out_3(compare_6bit_17_out_3));
  not not_11 (_3break_up, compare_6bit_17_out_3);
  _6numRow_to_3numRow u_6numrow_to_3numrow_4 (.in_1(shifter_12_out), .out_2(row_down3));
  compare_6bit compare_6bit_18 (.in_1(6'b100000), .in_2(shifter_12_out), .out_3(compare_6bit_18_out_3));
  not not_12 (_3break_down, compare_6bit_18_out_3);
  Multiplexer #(.select(3), .width(6)) multiplexer_9 (
    .in0(in_3), .in1(in_5), .in2(in_8), .in3(in_10), .in4(in_13), .in5(in_15), .out(multiplexer_9_out),
    .sel(row_up3));  // open: in6, in7, en
  zero_or_not zero_or_not_5 (.in_1(pull_resistor_5_node), .out_2(zero_or_not_5_out_2));
  compare_6bit compare_6bit_19 (.in_1(max_column_ru), .in_2(pull_resistor_5_node), .out_3(compare_6bit_19_out_3));
  Multiplexer #(.select(3), .width(6)) multiplexer_10 (
    .in0(in_3), .in1(in_5), .in2(in_8), .in3(in_10), .in4(in_13), .in5(in_15), .out(multiplexer_10_out),
    .sel(row_up3));  // open: in6, in7, en
  zero_or_not zero_or_not_6 (.in_1(pull_resistor_6_node), .out_2(zero_or_not_6_out_2));
  compare_6bit compare_6bit_20 (.in_1(max_column_lu), .in_2(pull_resistor_6_node), .out_3(compare_6bit_20_out_3));
  Multiplexer #(.select(3), .width(6)) multiplexer_11 (
    .in0(in_3), .in1(in_5), .in2(in_8), .in3(in_10), .in4(in_13), .in5(in_15), .out(multiplexer_11_out),
    .sel(row_down3));  // open: in6, in7, en
  zero_or_not zero_or_not_7 (.in_1(pull_resistor_7_node), .out_2(zero_or_not_7_out_2));
  compare_6bit compare_6bit_21 (.in_1(max_column_ld), .in_2(pull_resistor_7_node), .out_3(compare_6bit_21_out_3));
  Multiplexer #(.select(3), .width(6)) multiplexer_12 (
    .in0(in_3), .in1(in_5), .in2(in_8), .in3(in_10), .in4(in_13), .in5(in_15), .out(multiplexer_12_out),
    .sel(row_down3));  // open: in6, in7, en
  zero_or_not zero_or_not_8 (.in_1(transistor_8_out), .out_2(zero_or_not_8_out_2));
  compare_6bit compare_6bit_22 (.in_1(max_column_rd), .in_2(transistor_8_out), .out_3(compare_6bit_22_out_3));
  assign bit_extender_13_out = {{2{1'b0}}, compare_6bit_17_out_3};  // Bit_Extender bit_extender_13
  assign bit_extender_14_out = {{2{1'b0}}, compare_6bit_18_out_3};  // Bit_Extender bit_extender_14
  Multiplexer #(.select(3), .width(6)) multiplexer_13 (
    .in0(in_2), .in1(in_4), .in2(in_7), .in3(in_9), .in4(in_12), .in5(in_14), .out(multiplexer_13_out),
    .sel(row_up3));  // open: in6, in7, en
  assign res3_w_ru = multiplexer_13_out | pull_resistor_5_node;  // OR_Gate or_5, 6 bits wide
  and and_9 (and_9_out, max_ru_not_0, zero_or_not_5_out_2, compare_6bit_19_out_3);
  assign bit_extender_15_out = {{2{1'b0}}, and_9_out};  // Bit_Extender bit_extender_15
  not not_13 (_3break_ru, and_9_out);
  Multiplexer #(.select(3), .width(6)) multiplexer_14 (
    .in0(in_2), .in1(in_4), .in2(in_7), .in3(in_9), .in4(in_12), .in5(in_14), .out(multiplexer_14_out),
    .sel(row_up3));  // open: in6, in7, en
  assign res3_w_lu = multiplexer_14_out | pull_resistor_6_node;  // OR_Gate or_6, 6 bits wide
  and and_10 (and_10_out, max_lu_not_0, zero_or_not_6_out_2, compare_6bit_20_out_3);
  assign bit_extender_16_out = {{2{1'b0}}, and_10_out};  // Bit_Extender bit_extender_16
  not not_14 (_3break_lu, and_10_out);
  Multiplexer #(.select(3), .width(6)) multiplexer_15 (
    .in0(in_2), .in1(in_4), .in2(in_7), .in3(in_9), .in4(in_12), .in5(in_14), .out(multiplexer_15_out),
    .sel(row_down3));  // open: in6, in7, en
  assign res3_w_ld = multiplexer_15_out | pull_resistor_7_node;  // OR_Gate or_7, 6 bits wide
  assign bit_extender_17_out = {{2{1'b0}}, and_11_out};  // Bit_Extender bit_extender_17
  and and_11 (and_11_out, max_ld_not_0, zero_or_not_7_out_2, compare_6bit_21_out_3);
  not not_15 (_3break_ld, and_11_out);
  Multiplexer #(.select(3), .width(6)) multiplexer_16 (
    .in0(in_2), .in1(in_4), .in2(in_7), .in3(in_9), .in4(in_12), .in5(in_14), .out(multiplexer_16_out),
    .sel(row_down3));  // open: in6, in7, en
  assign res3_w_rd = multiplexer_16_out | transistor_8_out;  // OR_Gate or_8, 6 bits wide
  assign bit_extender_18_out = {{2{1'b0}}, and_12_out};  // Bit_Extender bit_extender_18
  and and_12 (and_12_out, max_rd_not_0, zero_or_not_8_out_2, compare_6bit_22_out_3);
  not not_16 (_3break_rd, and_12_out);
  Shifter #(.width(6), .shift("lr")) shifter_13 (
    .in(shifter_11_out), .\dist (bit_extender_13_out), .out(shifter_13_out));
  Shifter #(.width(6)) shifter_14 (.in(shifter_12_out), .\dist (bit_extender_14_out), .out(shifter_14_out));
  E_to_one_6bit e_to_one_6bit_7 (.in_1(_0b_ou), .out_2(out_20));
  E_to_one_6bit e_to_one_6bit_8 (.in_1(_1b_ou), .out_2(out_22));
  E_to_one_6bit e_to_one_6bit_9 (.in_1(_2b_ou), .out_2(out_24));
  E_to_one_6bit e_to_one_6bit_10 (.in_1(_3b_ou), .out_2(out_26));
  E_to_one_6bit e_to_one_6bit_11 (.in_1(_4b_ou), .out_2(out_28));
  E_to_one_6bit e_to_one_6bit_12 (.in_1(_5b_ou), .out_2(out_30));
  assign res3_b_ru = pull_resistor_5_node ^ multiplexer_9_out;  // XOR_Gate xor_5, 6 bits wide
  Shifter #(.width(6), .shift("lr")) shifter_15 (
    .in(pull_resistor_5_node), .\dist (bit_extender_15_out), .out(shifter_15_out));
  assign res3_b_lu = pull_resistor_6_node ^ multiplexer_10_out;  // XOR_Gate xor_6, 6 bits wide
  Shifter #(.width(6)) shifter_16 (.in(pull_resistor_6_node), .\dist (bit_extender_16_out), .out(shifter_16_out));
  assign res3_b_ld = pull_resistor_7_node ^ multiplexer_11_out;  // XOR_Gate xor_7, 6 bits wide
  Shifter #(.width(6)) shifter_17 (.in(pull_resistor_7_node), .\dist (bit_extender_17_out), .out(shifter_17_out));
  assign res3_b_rd = transistor_8_out ^ multiplexer_12_out;  // XOR_Gate xor_8, 6 bits wide
  Shifter #(.width(6), .shift("lr")) shifter_18 (
    .in(transistor_8_out), .\dist (bit_extender_18_out), .out(shifter_18_out));
  _6numRow_to_3numRow u_6numrow_to_3numrow_5 (.in_1(shifter_13_out), .out_2(row_up4));
  compare_6bit compare_6bit_23 (.in_1(6'b000001), .in_2(shifter_13_out), .out_3(compare_6bit_23_out_3));
  not not_17 (_4break_up, compare_6bit_23_out_3);
  _6numRow_to_3numRow u_6numrow_to_3numrow_6 (.in_1(shifter_14_out), .out_2(row_down4));
  compare_6bit compare_6bit_24 (.in_1(6'b100000), .in_2(shifter_14_out), .out_3(compare_6bit_24_out_3));
  not not_18 (_4break_down, compare_6bit_24_out_3);
  Transistor #(.width(6)) transistor_9 (.in(shifter_15_out), .out(transistor_9_out), .gate(_3break_ru));
  Pull_Resistor pull_resistor_9 (.node(transistor_9_out));
  Pull_Resistor pull_resistor_10 (.node(pull_resistor_10_node));
  Transistor #(.width(6)) transistor_10 (.in(shifter_16_out), .out(pull_resistor_10_node), .gate(_3break_lu));
  Pull_Resistor pull_resistor_11 (.node(pull_resistor_11_node));
  Transistor #(.width(6)) transistor_11 (.in(shifter_17_out), .out(pull_resistor_11_node), .gate(_3break_ld));
  Transistor #(.width(6)) transistor_12 (.in(shifter_18_out), .out(transistor_12_out), .gate(_3break_rd));
  Pull_Resistor pull_resistor_12 (.node(transistor_12_out));
  assign bit_extender_19_out = {{2{1'b0}}, compare_6bit_23_out_3};  // Bit_Extender bit_extender_19
  Shifter #(.width(6)) shifter_19 (.in(shifter_14_out), .\dist (bit_extender_20_out), .out(shifter_19_out));
  assign bit_extender_20_out = {{2{1'b0}}, compare_6bit_24_out_3};  // Bit_Extender bit_extender_20
  Multiplexer #(.select(3), .width(6)) multiplexer_17 (
    .in0(in_2), .in1(in_4), .in2(in_7), .in3(in_9), .in4(in_12), .in5(in_14), .out(multiplexer_17_out),
    .sel(row_up4));  // open: in6, in7, en
  Multiplexer #(.select(3), .width(6)) multiplexer_18 (
    .in0(in_3), .in1(in_5), .in2(in_8), .in3(in_10), .in4(in_13), .in5(in_15), .out(multiplexer_18_out),
    .sel(row_up4));  // open: in6, in7, en
  zero_or_not zero_or_not_9 (.in_1(transistor_9_out), .out_2(zero_or_not_9_out_2));
  compare_6bit compare_6bit_25 (.in_1(max_column_ru), .in_2(transistor_9_out), .out_3(compare_6bit_25_out_3));
  Multiplexer #(.select(3), .width(6)) multiplexer_19 (
    .in0(in_2), .in1(in_4), .in2(in_7), .in3(in_9), .in4(in_12), .in5(in_14), .out(multiplexer_19_out),
    .sel(row_up4));  // open: in6, in7, en
  Multiplexer #(.select(3), .width(6)) multiplexer_20 (
    .in0(in_3), .in1(in_5), .in2(in_8), .in3(in_10), .in4(in_13), .in5(in_15), .out(multiplexer_20_out),
    .sel(row_up4));  // open: in6, in7, en
  zero_or_not zero_or_not_10 (.in_1(pull_resistor_10_node), .out_2(zero_or_not_10_out_2));
  compare_6bit compare_6bit_26 (.in_1(max_column_lu), .in_2(pull_resistor_10_node), .out_3(compare_6bit_26_out_3));
  Multiplexer #(.select(3), .width(6)) multiplexer_21 (
    .in0(in_2), .in1(in_4), .in2(in_7), .in3(in_9), .in4(in_12), .in5(in_14), .out(multiplexer_21_out),
    .sel(row_down4));  // open: in6, in7, en
  Multiplexer #(.select(3), .width(6)) multiplexer_22 (
    .in0(in_3), .in1(in_5), .in2(in_8), .in3(in_10), .in4(in_13), .in5(in_15), .out(multiplexer_22_out),
    .sel(row_down4));  // open: in6, in7, en
  zero_or_not zero_or_not_11 (.in_1(pull_resistor_11_node), .out_2(zero_or_not_11_out_2));
  compare_6bit compare_6bit_27 (.in_1(max_column_ld), .in_2(pull_resistor_11_node), .out_3(compare_6bit_27_out_3));
  Multiplexer #(.select(3), .width(6)) multiplexer_23 (
    .in0(in_2), .in1(in_4), .in2(in_7), .in3(in_9), .in4(in_12), .in5(in_14), .out(multiplexer_23_out),
    .sel(row_down4));  // open: in6, in7, en
  Multiplexer #(.select(3), .width(6)) multiplexer_24 (
    .in0(in_3), .in1(in_5), .in2(in_8), .in3(in_10), .in4(in_13), .in5(in_15), .out(multiplexer_24_out),
    .sel(row_down4));  // open: in6, in7, en
  zero_or_not zero_or_not_12 (.in_1(transistor_12_out), .out_2(zero_or_not_12_out_2));
  compare_6bit compare_6bit_28 (.in_1(max_column_rd), .in_2(transistor_12_out), .out_3(compare_6bit_28_out_3));
  Shifter #(.width(6), .shift("lr")) shifter_20 (
    .in(shifter_13_out), .\dist (bit_extender_19_out), .out(shifter_20_out));
  compare_6bit compare_6bit_29 (.in_1(6'b000001), .in_2(shifter_20_out), .out_3(compare_6bit_29_out_3));
  compare_6bit compare_6bit_30 (.in_1(6'b100000), .in_2(shifter_19_out), .out_3(compare_6bit_30_out_3));
  assign res4_w_ru = multiplexer_17_out | transistor_9_out;  // OR_Gate or_9, 6 bits wide
  and and_13 (and_13_out, max_ru_not_0, zero_or_not_9_out_2, compare_6bit_25_out_3);
  assign bit_extender_21_out = {{2{1'b0}}, and_13_out};  // Bit_Extender bit_extender_21
  not not_19 (_4break_ru, and_13_out);
  assign res4_w_lu = multiplexer_19_out | pull_resistor_10_node;  // OR_Gate or_10, 6 bits wide
  and and_14 (and_14_out, max_lu_not_0, zero_or_not_10_out_2, compare_6bit_26_out_3);
  assign bit_extender_22_out = {{2{1'b0}}, and_14_out};  // Bit_Extender bit_extender_22
  not not_20 (_4break_lu, and_14_out);
  assign res4_w_ld = multiplexer_21_out | pull_resistor_11_node;  // OR_Gate or_11, 6 bits wide
  and and_15 (and_15_out, max_ld_not_0, zero_or_not_11_out_2, compare_6bit_27_out_3);
  assign bit_extender_23_out = {{2{1'b0}}, and_15_out};  // Bit_Extender bit_extender_23
  not not_21 (_4break_ld, and_15_out);
  assign res4_w_rd = multiplexer_23_out | transistor_12_out;  // OR_Gate or_12, 6 bits wide
  assign bit_extender_24_out = {{2{1'b0}}, and_16_out};  // Bit_Extender bit_extender_24
  and and_16 (and_16_out, max_rd_not_0, zero_or_not_12_out_2, compare_6bit_28_out_3);
  not not_22 (_4break_rd, and_16_out);
  _6numRow_to_3numRow u_6numrow_to_3numrow_7 (.in_1(shifter_20_out), .out_2(row_up5));
  assign bit_extender_25_out = {{2{1'b0}}, compare_6bit_29_out_3};  // Bit_Extender bit_extender_25
  not not_23 (_5break_up, compare_6bit_29_out_3);
  _6numRow_to_3numRow u_6numrow_to_3numrow_8 (.in_1(shifter_19_out), .out_2(row_down5));
  assign bit_extender_26_out = {{2{1'b0}}, compare_6bit_30_out_3};  // Bit_Extender bit_extender_26
  not not_24 (_5break_down, compare_6bit_30_out_3);
  assign or_13_out = res2_w_ru | res2_w_lu;  // OR_Gate or_13, 6 bits wide
  Demultiplexer #(.select(3), .width(6)) demultiplexer_1 (
    .out0(_0w_ou), .out1(_1w_ou), .out2(_2w_ou), .out3(_3w_ou), .out4(_4w_ou), .out5(_5w_ou), .in(or_13_out),
    .sel(row_up2));  // open: out6, out7, en
  assign and_17_out = res2_b_ru & res2_b_lu;  // AND_Gate and_17, 6 bits wide
  Demultiplexer #(.select(3), .width(6)) demultiplexer_2 (
    .out0(_0b_ou), .out1(_1b_ou), .out2(_2b_ou), .out3(_3b_ou), .out4(_4b_ou), .out5(_5b_ou),
    .in(and_17_out), .sel(row_up2));  // open: out6, out7, en
  assign res4_b_ru = multiplexer_18_out ^ transistor_9_out;  // XOR_Gate xor_9, 6 bits wide
  Shifter #(.width(6), .shift("lr")) shifter_21 (
    .in(transistor_9_out), .\dist (bit_extender_21_out), .out(shifter_21_out));
  assign res4_b_lu = pull_resistor_10_node ^ multiplexer_20_out;  // XOR_Gate xor_10, 6 bits wide
  Shifter #(.width(6)) shifter_22 (.in(pull_resistor_10_node), .\dist (bit_extender_22_out), .out(shifter_22_out));
  assign res4_b_ld = pull_resistor_11_node ^ multiplexer_22_out;  // XOR_Gate xor_11, 6 bits wide
  Shifter #(.width(6)) shifter_23 (.in(pull_resistor_11_node), .\dist (bit_extender_23_out), .out(shifter_23_out));
  assign res4_b_rd = transistor_12_out ^ multiplexer_24_out;  // XOR_Gate xor_12, 6 bits wide
  Shifter #(.width(6), .shift("lr")) shifter_24 (
    .in(transistor_12_out), .\dist (bit_extender_24_out), .out(shifter_24_out));
  Shifter #(.width(6), .shift("lr")) shifter_25 (
    .in(shifter_20_out), .\dist (bit_extender_25_out), .out(shifter_25_out));
  Shifter #(.width(6)) shifter_26 (.in(shifter_19_out), .\dist (bit_extender_26_out), .out(shifter_26_out));
  Multiplexer #(.select(3), .width(6)) multiplexer_25 (
    .in0(in_3), .in1(in_5), .in2(in_8), .in3(in_10), .in4(in_13), .in5(in_15), .out(multiplexer_25_out),
    .sel(row_up5));  // open: in6, in7, en
  Pull_Resistor pull_resistor_13 (.node(pull_resistor_13_node));
  Transistor #(.width(6)) transistor_13 (.in(shifter_21_out), .out(pull_resistor_13_node), .gate(_4break_ru));
  Multiplexer #(.select(3), .width(6)) multiplexer_26 (
    .in0(in_3), .in1(in_5), .in2(in_8), .in3(in_10), .in4(in_13), .in5(in_15), .out(multiplexer_26_out),
    .sel(row_up5));  // open: in6, in7, en
  Transistor #(.width(6)) transistor_14 (.in(shifter_22_out), .out(transistor_14_out), .gate(_4break_lu));
  Pull_Resistor pull_resistor_14 (.node(transistor_14_out));
  Multiplexer #(.select(3), .width(6)) multiplexer_27 (
    .in0(in_3), .in1(in_5), .in2(in_8), .in3(in_10), .in4(in_13), .in5(in_15), .out(multiplexer_27_out),
    .sel(row_down5));  // open: in6, in7, en
  Transistor #(.width(6)) transistor_15 (.in(shifter_23_out), .out(transistor_15_out), .gate(_4break_ld));
  Pull_Resistor pull_resistor_15 (.node(transistor_15_out));
  Multiplexer #(.select(3), .width(6)) multiplexer_28 (
    .in0(in_3), .in1(in_5), .in2(in_8), .in3(in_10), .in4(in_13), .in5(in_15), .out(multiplexer_28_out),
    .sel(row_down5));  // open: in6, in7, en
  Pull_Resistor pull_resistor_16 (.node(pull_resistor_16_node));
  Transistor #(.width(6)) transistor_16 (.in(shifter_24_out), .out(pull_resistor_16_node), .gate(_4break_rd));
  _6numRow_to_3numRow u_6numrow_to_3numrow_9 (.in_1(shifter_25_out), .out_2(row_up6));
  compare_6bit compare_6bit_31 (.in_1(6'b000001), .in_2(shifter_25_out), .out_3(compare_6bit_31_out_3));
  not not_25 (_6break_up, compare_6bit_31_out_3);
  _6numRow_to_3numRow u_6numrow_to_3numrow_10 (.in_1(shifter_26_out), .out_2(row_down6));
  compare_6bit compare_6bit_32 (.in_1(6'b100000), .in_2(shifter_26_out), .out_3(compare_6bit_32_out_3));
  not not_26 (_6break_down, compare_6bit_32_out_3);
  assign or_14_out = res3_w_ru | res3_w_lu;  // OR_Gate or_14, 6 bits wide
  Demultiplexer #(.select(3), .width(6)) demultiplexer_3 (
    .out0(_0w_ou), .out1(_1w_ou), .out2(_2w_ou), .out3(_3w_ou), .out4(_4w_ou), .out5(_5w_ou), .in(or_14_out),
    .sel(row_up3));  // open: out6, out7, en
  Demultiplexer #(.select(3), .width(6)) demultiplexer_4 (
    .out0(_0b_ou), .out1(_1b_ou), .out2(_2b_ou), .out3(_3b_ou), .out4(_4b_ou), .out5(_5b_ou),
    .in(and_18_out), .sel(row_up3));  // open: out6, out7, en
  assign and_18_out = res3_b_ru & res3_b_lu;  // AND_Gate and_18, 6 bits wide
  Multiplexer #(.select(3), .width(6)) multiplexer_29 (
    .in0(in_2), .in1(in_4), .in2(in_7), .in3(in_9), .in4(in_12), .in5(in_14), .out(multiplexer_29_out),
    .sel(row_up5));  // open: in6, in7, en
  zero_or_not zero_or_not_13 (.in_1(pull_resistor_13_node), .out_2(zero_or_not_13_out_2));
  and and_19 (and_19_out, max_ru_not_0, zero_or_not_13_out_2, compare_6bit_33_out_3);
  compare_6bit compare_6bit_33 (.in_1(max_column_ru), .in_2(pull_resistor_13_node), .out_3(compare_6bit_33_out_3));
  not not_27 (_5break_ru, and_19_out);
  Multiplexer #(.select(3), .width(6)) multiplexer_30 (
    .in0(in_2), .in1(in_4), .in2(in_7), .in3(in_9), .in4(in_12), .in5(in_14), .out(multiplexer_30_out),
    .sel(row_up5));  // open: in6, in7, en
  zero_or_not zero_or_not_14 (.in_1(transistor_14_out), .out_2(zero_or_not_14_out_2));
  and and_20 (and_20_out, max_lu_not_0, zero_or_not_14_out_2, compare_6bit_34_out_3);
  compare_6bit compare_6bit_34 (.in_1(max_column_lu), .in_2(transistor_14_out), .out_3(compare_6bit_34_out_3));
  not not_28 (_5break_lu, and_20_out);
  Multiplexer #(.select(3), .width(6)) multiplexer_31 (
    .in0(in_2), .in1(in_4), .in2(in_7), .in3(in_9), .in4(in_12), .in5(in_14), .out(multiplexer_31_out),
    .sel(row_down5));  // open: in6, in7, en
  zero_or_not zero_or_not_15 (.in_1(transistor_15_out), .out_2(zero_or_not_15_out_2));
  and and_21 (and_21_out, max_ld_not_0, zero_or_not_15_out_2, compare_6bit_35_out_3);
  compare_6bit compare_6bit_35 (.in_1(max_column_ld), .in_2(transistor_15_out), .out_3(compare_6bit_35_out_3));
  not not_29 (_5break_ld, and_21_out);
  Multiplexer #(.select(3), .width(6)) multiplexer_32 (
    .in0(in_2), .in1(in_4), .in2(in_7), .in3(in_9), .in4(in_12), .in5(in_14), .out(multiplexer_32_out),
    .sel(row_down5));  // open: in6, in7, en
  zero_or_not zero_or_not_16 (.in_1(pull_resistor_16_node), .out_2(zero_or_not_16_out_2));
  and and_22 (and_22_out, max_rd_not_0, zero_or_not_16_out_2, compare_6bit_36_out_3);
  not not_30 (_5break_rd, and_22_out);
  compare_6bit compare_6bit_36 (.in_1(max_column_rd), .in_2(pull_resistor_16_node), .out_3(compare_6bit_36_out_3));
  assign res5_w_ru = multiplexer_29_out | pull_resistor_13_node;  // OR_Gate or_15, 6 bits wide
  assign res5_b_ru = pull_resistor_13_node ^ multiplexer_25_out;  // XOR_Gate xor_13, 6 bits wide
  Shifter #(.width(6), .shift("lr")) shifter_27 (
    .in(pull_resistor_13_node), .\dist (bit_extender_27_out), .out(shifter_27_out));
  assign bit_extender_27_out = {{2{1'b0}}, and_19_out};  // Bit_Extender bit_extender_27
  assign res5_w_lu = multiplexer_30_out | transistor_14_out;  // OR_Gate or_16, 6 bits wide
  assign res5_b_lu = transistor_14_out ^ multiplexer_26_out;  // XOR_Gate xor_14, 6 bits wide
  Shifter #(.width(6)) shifter_28 (.in(transistor_14_out), .\dist (bit_extender_28_out), .out(shifter_28_out));
  assign bit_extender_28_out = {{2{1'b0}}, and_20_out};  // Bit_Extender bit_extender_28
  assign res5_w_ld = multiplexer_31_out | transistor_15_out;  // OR_Gate or_17, 6 bits wide
  assign res5_b_ld = transistor_15_out ^ multiplexer_27_out;  // XOR_Gate xor_15, 6 bits wide
  Shifter #(.width(6)) shifter_29 (.in(transistor_15_out), .\dist (bit_extender_29_out), .out(shifter_29_out));
  assign bit_extender_29_out = {{2{1'b0}}, and_21_out};  // Bit_Extender bit_extender_29
  assign res5_w_rd = multiplexer_32_out | pull_resistor_16_node;  // OR_Gate or_18, 6 bits wide
  assign res5_b_rd = pull_resistor_16_node ^ multiplexer_28_out;  // XOR_Gate xor_16, 6 bits wide
  Shifter #(.width(6), .shift("lr")) shifter_30 (
    .in(pull_resistor_16_node), .\dist (bit_extender_30_out), .out(shifter_30_out));
  assign bit_extender_30_out = {{2{1'b0}}, and_22_out};  // Bit_Extender bit_extender_30
  Transistor #(.width(6)) transistor_17 (.in(shifter_27_out), .out(transistor_17_out), .gate(_5break_ru));
  Pull_Resistor pull_resistor_17 (.node(transistor_17_out));
  Pull_Resistor pull_resistor_18 (.node(pull_resistor_18_node));
  Transistor #(.width(6)) transistor_18 (.in(shifter_28_out), .out(pull_resistor_18_node), .gate(_5break_lu));
  Pull_Resistor pull_resistor_19 (.node(pull_resistor_19_node));
  Transistor #(.width(6)) transistor_19 (.in(shifter_29_out), .out(pull_resistor_19_node), .gate(_5break_ld));
  Transistor #(.width(6)) transistor_20 (.in(shifter_30_out), .out(transistor_20_out), .gate(_5break_rd));
  Pull_Resistor pull_resistor_20 (.node(transistor_20_out));
  Demultiplexer #(.select(3), .width(6)) demultiplexer_5 (
    .out0(_0w_ou), .out1(_1w_ou), .out2(_2w_ou), .out3(_3w_ou), .out4(_4w_ou), .out5(_5w_ou), .in(or_19_out),
    .sel(row_up4));  // open: out6, out7, en
  assign or_19_out = res4_w_ru | res4_w_lu;  // OR_Gate or_19, 6 bits wide
  Demultiplexer #(.select(3), .width(6)) demultiplexer_6 (
    .out0(_0b_ou), .out1(_1b_ou), .out2(_2b_ou), .out3(_3b_ou), .out4(_4b_ou), .out5(_5b_ou),
    .in(and_23_out), .sel(row_up4));  // open: out6, out7, en
  assign and_23_out = res4_b_ru & res4_b_lu;  // AND_Gate and_23, 6 bits wide
  Multiplexer #(.select(3), .width(6)) multiplexer_33 (
    .in0(in_3), .in1(in_5), .in2(in_8), .in3(in_10), .in4(in_13), .in5(in_15), .out(multiplexer_33_out),
    .sel(row_up6));  // open: in6, in7, en
  Multiplexer #(.select(3), .width(6)) multiplexer_34 (
    .in0(in_3), .in1(in_5), .in2(in_8), .in3(in_10), .in4(in_13), .in5(in_15), .out(multiplexer_34_out),
    .sel(row_up6));  // open: in6, in7, en
  Multiplexer #(.select(3), .width(6)) multiplexer_35 (
    .in0(in_3), .in1(in_5), .in2(in_8), .in3(in_10), .in4(in_13), .in5(in_15), .out(multiplexer_35_out),
    .sel(row_down6));  // open: in6, in7, en
  Multiplexer #(.select(3), .width(6)) multiplexer_36 (
    .in0(in_3), .in1(in_5), .in2(in_8), .in3(in_10), .in4(in_13), .in5(in_15), .out(multiplexer_36_out),
    .sel(row_down6));  // open: in6, in7, en
  Multiplexer #(.select(3), .width(6)) multiplexer_37 (
    .in0(in_2), .in1(in_4), .in2(in_7), .in3(in_9), .in4(in_12), .in5(in_14), .out(multiplexer_37_out),
    .sel(row_up6));  // open: in6, in7, en
  and and_24 (and_24_out, max_ru_not_0, zero_or_not_17_out_2, compare_6bit_37_out_3);
  not not_31 (_6break_ru, and_24_out);
  zero_or_not zero_or_not_17 (.in_1(transistor_17_out), .out_2(zero_or_not_17_out_2));
  compare_6bit compare_6bit_37 (.in_1(max_column_ru), .in_2(transistor_17_out), .out_3(compare_6bit_37_out_3));
  Multiplexer #(.select(3), .width(6)) multiplexer_38 (
    .in0(in_2), .in1(in_4), .in2(in_7), .in3(in_9), .in4(in_12), .in5(in_14), .out(multiplexer_38_out),
    .sel(row_up6));  // open: in6, in7, en
  not not_32 (_6break_lu, and_25_out);
  zero_or_not zero_or_not_18 (.in_1(pull_resistor_18_node), .out_2(zero_or_not_18_out_2));
  and and_25 (and_25_out, max_lu_not_0, zero_or_not_18_out_2, compare_6bit_38_out_3);
  compare_6bit compare_6bit_38 (.in_1(max_column_lu), .in_2(pull_resistor_18_node), .out_3(compare_6bit_38_out_3));
  Multiplexer #(.select(3), .width(6)) multiplexer_39 (
    .in0(in_2), .in1(in_4), .in2(in_7), .in3(in_9), .in4(in_12), .in5(in_14), .out(multiplexer_39_out),
    .sel(row_down6));  // open: in6, in7, en
  and and_26 (and_26_out, max_ld_not_0, zero_or_not_19_out_2, compare_6bit_39_out_3);
  not not_33 (_6break_ld, and_26_out);
  zero_or_not zero_or_not_19 (.in_1(pull_resistor_19_node), .out_2(zero_or_not_19_out_2));
  compare_6bit compare_6bit_39 (.in_1(max_column_ld), .in_2(pull_resistor_19_node), .out_3(compare_6bit_39_out_3));
  Multiplexer #(.select(3), .width(6)) multiplexer_40 (
    .in0(in_2), .in1(in_4), .in2(in_7), .in3(in_9), .in4(in_12), .in5(in_14), .out(multiplexer_40_out),
    .sel(row_down6));  // open: in6, in7, en
  not not_34 (_6break_rd, and_27_out);
  zero_or_not zero_or_not_20 (.in_1(transistor_20_out), .out_2(zero_or_not_20_out_2));
  and and_27 (and_27_out, max_rd_not_0, zero_or_not_20_out_2, compare_6bit_40_out_3);
  compare_6bit compare_6bit_40 (.in_1(max_column_rd), .in_2(transistor_20_out), .out_3(compare_6bit_40_out_3));
  assign or_20_out = res5_w_ru | res5_w_lu;  // OR_Gate or_20, 6 bits wide
  Demultiplexer #(.select(3), .width(6)) demultiplexer_7 (
    .out0(_0w_ou), .out1(_1w_ou), .out2(_2w_ou), .out3(_3w_ou), .out4(_4w_ou), .out5(_5w_ou), .in(or_20_out),
    .sel(row_up5));  // open: out6, out7, en
  assign and_28_out = res5_b_ru & res5_b_lu;  // AND_Gate and_28, 6 bits wide
  Demultiplexer #(.select(3), .width(6)) demultiplexer_8 (
    .out0(_0b_ou), .out1(_1b_ou), .out2(_2b_ou), .out3(_3b_ou), .out4(_4b_ou), .out5(_5b_ou),
    .in(and_28_out), .sel(row_up5));  // open: out6, out7, en
  assign res6_w_ru = multiplexer_37_out | transistor_17_out;  // OR_Gate or_21, 6 bits wide
  assign res6_b_ru = transistor_17_out ^ multiplexer_33_out;  // XOR_Gate xor_17, 6 bits wide
  assign res6_w_lu = multiplexer_38_out | pull_resistor_18_node;  // OR_Gate or_22, 6 bits wide
  assign res6_b_lu = pull_resistor_18_node ^ multiplexer_34_out;  // XOR_Gate xor_18, 6 bits wide
  assign res6_w_ld = multiplexer_39_out | pull_resistor_19_node;  // OR_Gate or_23, 6 bits wide
  assign res6_b_ld = pull_resistor_19_node ^ multiplexer_35_out;  // XOR_Gate xor_19, 6 bits wide
  assign res6_w_rd = multiplexer_40_out | transistor_20_out;  // OR_Gate or_24, 6 bits wide
  assign res6_b_rd = transistor_20_out ^ multiplexer_36_out;  // XOR_Gate xor_20, 6 bits wide
  Demultiplexer #(.select(3), .width(6)) demultiplexer_9 (
    .out0(_0w_ou), .out1(_1w_ou), .out2(_2w_ou), .out3(_3w_ou), .out4(_4w_ou), .out5(_5w_ou), .in(or_25_out),
    .sel(row_down2));  // open: out6, out7, en
  assign or_25_out = res2_w_rd | res2_w_ld;  // OR_Gate or_25, 6 bits wide
  assign and_29_out = res2_b_rd & res2_b_ld;  // AND_Gate and_29, 6 bits wide
  Demultiplexer #(.select(3), .width(6)) demultiplexer_10 (
    .out0(_0b_ou), .out1(_1b_ou), .out2(_2b_ou), .out3(_3b_ou), .out4(_4b_ou), .out5(_5b_ou),
    .in(and_29_out), .sel(row_down2));  // open: out6, out7, en
  Demultiplexer #(.select(3), .width(6)) demultiplexer_11 (
    .out0(_0w_ou), .out1(_1w_ou), .out2(_2w_ou), .out3(_3w_ou), .out4(_4w_ou), .out5(_5w_ou), .in(or_26_out),
    .sel(row_up6));  // open: out6, out7, en
  assign or_26_out = res6_w_ru | res6_w_lu;  // OR_Gate or_26, 6 bits wide
  assign and_30_out = res6_b_ru & res6_b_lu;  // AND_Gate and_30, 6 bits wide
  Demultiplexer #(.select(3), .width(6)) demultiplexer_12 (
    .out0(_0b_ou), .out1(_1b_ou), .out2(_2b_ou), .out3(_3b_ou), .out4(_4b_ou), .out5(_5b_ou),
    .in(and_30_out), .sel(row_up6));  // open: out6, out7, en
  assign or_27_out = res3_w_rd | res3_w_ld;  // OR_Gate or_27, 6 bits wide
  Demultiplexer #(.select(3), .width(6)) demultiplexer_13 (
    .out0(_0w_ou), .out1(_1w_ou), .out2(_2w_ou), .out3(_3w_ou), .out4(_4w_ou), .out5(_5w_ou), .in(or_27_out),
    .sel(row_down3));  // open: out6, out7, en
  assign and_31_out = res3_b_rd & res3_b_ld;  // AND_Gate and_31, 6 bits wide
  Demultiplexer #(.select(3), .width(6)) demultiplexer_14 (
    .out0(_0b_ou), .out1(_1b_ou), .out2(_2b_ou), .out3(_3b_ou), .out4(_4b_ou), .out5(_5b_ou),
    .in(and_31_out), .sel(row_down3));  // open: out6, out7, en
  assign or_28_out = res4_w_rd | res4_w_ld;  // OR_Gate or_28, 6 bits wide
  Demultiplexer #(.select(3), .width(6)) demultiplexer_15 (
    .out0(_0w_ou), .out1(_1w_ou), .out2(_2w_ou), .out3(_3w_ou), .out4(_4w_ou), .out5(_5w_ou), .in(or_28_out),
    .sel(row_down4));  // open: out6, out7, en
  assign and_32_out = res4_b_rd & res4_b_ld;  // AND_Gate and_32, 6 bits wide
  Demultiplexer #(.select(3), .width(6)) demultiplexer_16 (
    .out0(_0b_ou), .out1(_1b_ou), .out2(_2b_ou), .out3(_3b_ou), .out4(_4b_ou), .out5(_5b_ou),
    .in(and_32_out), .sel(row_down4));  // open: out6, out7, en
  Demultiplexer #(.select(3), .width(6)) demultiplexer_17 (
    .out0(_0w_ou), .out1(_1w_ou), .out2(_2w_ou), .out3(_3w_ou), .out4(_4w_ou), .out5(_5w_ou), .in(or_29_out),
    .sel(row_down5));  // open: out6, out7, en
  assign or_29_out = res5_w_rd | res5_w_ld;  // OR_Gate or_29, 6 bits wide
  Demultiplexer #(.select(3), .width(6)) demultiplexer_18 (
    .out0(_0b_ou), .out1(_1b_ou), .out2(_2b_ou), .out3(_3b_ou), .out4(_4b_ou), .out5(_5b_ou),
    .in(and_33_out), .sel(row_down5));  // open: out6, out7, en
  assign and_33_out = res5_b_rd & res5_b_ld;  // AND_Gate and_33, 6 bits wide
  Demultiplexer #(.select(3), .width(6)) demultiplexer_19 (
    .out0(_0w_ou), .out1(_1w_ou), .out2(_2w_ou), .out3(_3w_ou), .out4(_4w_ou), .out5(_5w_ou), .in(or_30_out),
    .sel(row_down6));  // open: out6, out7, en
  assign or_30_out = res6_w_rd | res6_w_ld;  // OR_Gate or_30, 6 bits wide
  assign and_34_out = res6_b_rd & res6_b_ld;  // AND_Gate and_34, 6 bits wide
  Demultiplexer #(.select(3), .width(6)) demultiplexer_20 (
    .out0(_0b_ou), .out1(_1b_ou), .out2(_2b_ou), .out3(_3b_ou), .out4(_4b_ou), .out5(_5b_ou),
    .in(and_34_out), .sel(row_down6));  // open: out6, out7, en

  // Other names for the same wires on the sheet: _0b[5:0] = in_3; _0w[5:0] = in_2; _1b[5:0] = in_5; _1w[5:0] = in_4;
  //   _2b[5:0] = in_8; _2w[5:0] = in_7; _3b[5:0] = in_10; _3w[5:0] = in_9; _4b[5:0] = in_13; _4w[5:0] = in_12;
  //   _5b[5:0] = in_15; _5w[5:0] = in_14; max_ld[5:0] = max_column_ld; max_lu[5:0] = max_column_lu;
  //   max_rd[5:0] = max_column_rd; max_ru[5:0] = max_column_ru
endmodule

module row_to_column_for_white (
  input  [5:0] column_white,
  input  [5:0] column_num,
  output [5:0] out_3,
  output [5:0] out_4,
  output [5:0] out_5,
  output [5:0] out_6,
  output [5:0] out_7,
  output [5:0] out_8
);

  wire [5:0] bit_extender_1_out, bit_extender_2_out, bit_extender_3_out, bit_extender_4_out,
       bit_extender_5_out, bit_extender_6_out;

  assign bit_extender_1_out = {{5{column_white[0]}}, column_white[0]};  // Bit_Extender bit_extender_1
  assign bit_extender_2_out = {{5{column_white[1]}}, column_white[1]};  // Bit_Extender bit_extender_2
  assign bit_extender_3_out = {{5{column_white[2]}}, column_white[2]};  // Bit_Extender bit_extender_3
  assign bit_extender_4_out = {{5{column_white[3]}}, column_white[3]};  // Bit_Extender bit_extender_4
  assign bit_extender_5_out = {{5{column_white[4]}}, column_white[4]};  // Bit_Extender bit_extender_5
  assign bit_extender_6_out = {{5{column_white[5]}}, column_white[5]};  // Bit_Extender bit_extender_6
  assign out_3 = bit_extender_1_out & column_num;  // AND_Gate and_1, 6 bits wide
  assign out_4 = bit_extender_2_out & column_num;  // AND_Gate and_2, 6 bits wide
  assign out_5 = bit_extender_3_out & column_num;  // AND_Gate and_3, 6 bits wide
  assign out_6 = bit_extender_4_out & column_num;  // AND_Gate and_4, 6 bits wide
  assign out_7 = bit_extender_5_out & column_num;  // AND_Gate and_5, 6 bits wide
  assign out_8 = bit_extender_6_out & column_num;  // AND_Gate and_6, 6 bits wide
endmodule

module row_to_column_for_black (
  input  [5:0] column_black,
  input  [5:0] column_num,
  output [5:0] out_3,
  output [5:0] out_4,
  output [5:0] out_5,
  output [5:0] out_6,
  output [5:0] out_7,
  output [5:0] out_8
);

  wire [5:0] and_1_out, and_2_out, and_3_out, and_4_out, and_5_out, and_6_out, and_7_out, and_8_out,
       and_9_out, and_10_out, and_11_out, and_12_out, nor_1_out, nor_2_out, nor_3_out, nor_4_out, nor_5_out,
       nor_6_out;
  wire [5:5] not_1_out, not_2_out, not_3_out, not_4_out, not_5_out, not_6_out;

  not not_1 (not_1_out[5], column_black[0]);
  not not_2 (not_2_out[5], column_black[1]);
  not not_3 (not_3_out[5], column_black[2]);
  not not_4 (not_4_out[5], column_black[3]);
  not not_5 (not_5_out[5], column_black[4]);
  not not_6 (not_6_out[5], column_black[5]);
  assign nor_1_out = ~(column_num | {6{1'b0}});  // NOR_Gate nor_1, 6 bits wide
  assign and_1_out = nor_1_out & {6{not_1_out[5]}};  // AND_Gate and_1, 6 bits wide
  assign and_2_out = {6{column_black[0]}} & {6{1'b1}};  // AND_Gate and_2, 6 bits wide
  assign nor_2_out = ~(column_num | {6{1'b0}});  // NOR_Gate nor_2, 6 bits wide
  assign and_3_out = nor_2_out & {6{not_2_out[5]}};  // AND_Gate and_3, 6 bits wide
  assign and_4_out = {6{column_black[1]}} & {6{1'b1}};  // AND_Gate and_4, 6 bits wide
  assign nor_3_out = ~(column_num | {6{1'b0}});  // NOR_Gate nor_3, 6 bits wide
  assign and_5_out = nor_3_out & {6{not_3_out[5]}};  // AND_Gate and_5, 6 bits wide
  assign and_6_out = {6{column_black[2]}} & {6{1'b1}};  // AND_Gate and_6, 6 bits wide
  assign nor_4_out = ~(column_num | {6{1'b0}});  // NOR_Gate nor_4, 6 bits wide
  assign and_7_out = nor_4_out & {6{not_4_out[5]}};  // AND_Gate and_7, 6 bits wide
  assign and_8_out = {6{column_black[3]}} & {6{1'b1}};  // AND_Gate and_8, 6 bits wide
  assign nor_5_out = ~(column_num | {6{1'b0}});  // NOR_Gate nor_5, 6 bits wide
  assign and_9_out = nor_5_out & {6{not_5_out[5]}};  // AND_Gate and_9, 6 bits wide
  assign and_10_out = {6{column_black[4]}} & {6{1'b1}};  // AND_Gate and_10, 6 bits wide
  assign nor_6_out = ~(column_num | {6{1'b0}});  // NOR_Gate nor_6, 6 bits wide
  assign and_11_out = nor_6_out & {6{not_6_out[5]}};  // AND_Gate and_11, 6 bits wide
  assign and_12_out = {6{column_black[5]}} & {6{1'b1}};  // AND_Gate and_12, 6 bits wide
  assign out_3 = and_1_out | and_2_out;  // OR_Gate or_1, 6 bits wide
  assign out_4 = and_3_out | and_4_out;  // OR_Gate or_2, 6 bits wide
  assign out_5 = and_5_out | and_6_out;  // OR_Gate or_3, 6 bits wide
  assign out_6 = and_7_out | and_8_out;  // OR_Gate or_4, 6 bits wide
  assign out_7 = and_9_out | and_10_out;  // OR_Gate or_5, 6 bits wide
  assign out_8 = and_11_out | and_12_out;  // OR_Gate or_6, 6 bits wide

  // Other names for the same wires on the sheet: c_n[5:0] = column_num
endmodule

module E_to_one_6bit (
  input  [5:0] in_1,
  output [5:0] out_2
);

  wire and_1_out, and_2_out, and_3_out, and_4_out, and_5_out, and_6_out, and_7_out, and_9_out, and_10_out,
       and_11_out, and_12_out, and_13_out, and_16_out, and_17_out, and_18_out, and_19_out, and_22_out,
       and_24_out, bitselector_1_out, bitselector_2_out, bitselector_3_out, bitselector_4_out,
       bitselector_5_out, bitselector_6_out, bitselector_7_out, bitselector_8_out, bitselector_9_out,
       bitselector_10_out, bitselector_11_out, bitselector_12_out, buffer_1_out, buffer_2_out, buffer_3_out,
       buffer_4_out, buffer_5_out, buffer_6_out, buffer_11_out, buffer_13_out, buffer_16_out, buffer_18_out,
       buffer_19_out, buffer_20_out, buffer_22_out, buffer_23_out, buffer_24_out, buffer_26_out,
       buffer_27_out, buffer_28_out, buffer_31_out, buffer_32_out, buffer_34_out, pull_resistor_2_node,
       pull_resistor_3_node, pull_resistor_4_node, pull_resistor_5_node, pull_resistor_8_node,
       pull_resistor_9_node, pull_resistor_10_node, pull_resistor_11_node, pull_resistor_14_node,
       pull_resistor_19_node, pull_resistor_23_node, pull_resistor_24_node, pull_resistor_27_node,
       pull_resistor_29_node, pull_resistor_30_node;

  buf buffer_1 (buffer_1_out, in_1[0]);
  buf buffer_2 (buffer_2_out, in_1[0]);
  BitSelector #(.width(1)) bitselector_1 (.in(1'b0), .out(bitselector_1_out), .sel(in_1[0]));
  and and_1 (and_1_out, ~buffer_1_out, buffer_2_out);  // AND_Gate
  Pull_Resistor #(.pull(1)) pull_resistor_1 (.node(buffer_2_out));
  buf buffer_3 (buffer_3_out, in_1[1]);
  buf buffer_4 (buffer_4_out, in_1[1]);
  buf buffer_5 (buffer_5_out, in_1[2]);
  buf buffer_6 (buffer_6_out, in_1[2]);
  Pull_Resistor pull_resistor_2 (.node(pull_resistor_2_node));
  buf buffer_7 (pull_resistor_2_node, bitselector_1_out);
  Pull_Resistor #(.pull(1)) pull_resistor_3 (.node(pull_resistor_3_node));
  buf buffer_8 (pull_resistor_3_node, bitselector_1_out);
  Pull_Resistor pull_resistor_4 (.node(pull_resistor_4_node));
  buf buffer_9 (pull_resistor_4_node, bitselector_2_out);
  BitSelector #(.width(1)) bitselector_2 (.out(bitselector_2_out), .sel(and_1_out));  // open: in
  Pull_Resistor #(.pull(1)) pull_resistor_5 (.node(pull_resistor_5_node));
  buf buffer_10 (pull_resistor_5_node, bitselector_2_out);
  BitSelector #(.width(1)) bitselector_3 (.in(1'b0), .out(bitselector_3_out), .sel(in_1[1]));
  and and_2 (and_2_out, ~buffer_3_out, buffer_4_out);  // AND_Gate
  Pull_Resistor #(.pull(1)) pull_resistor_6 (.node(buffer_4_out));
  BitSelector #(.width(1)) bitselector_4 (.in(1'b0), .out(bitselector_4_out), .sel(in_1[2]));
  and and_3 (and_3_out, ~buffer_5_out, buffer_6_out);  // AND_Gate
  Pull_Resistor #(.pull(1)) pull_resistor_7 (.node(buffer_6_out));
  buf buffer_11 (buffer_11_out, in_1[4]);
  Pull_Resistor #(.pull(1)) pull_resistor_8 (.node(pull_resistor_8_node));
  buf buffer_12 (pull_resistor_8_node, in_1[4]);
  buf buffer_13 (buffer_13_out, in_1[5]);
  Pull_Resistor #(.pull(1)) pull_resistor_9 (.node(pull_resistor_9_node));
  buf buffer_14 (pull_resistor_9_node, in_1[5]);
  and and_4 (and_4_out, ~pull_resistor_2_node, pull_resistor_3_node);  // AND_Gate
  and and_5 (and_5_out, ~pull_resistor_4_node, pull_resistor_5_node);  // AND_Gate
  Pull_Resistor pull_resistor_10 (.node(pull_resistor_10_node));
  buf buffer_15 (pull_resistor_10_node, bitselector_3_out);
  buf buffer_16 (buffer_16_out, bitselector_3_out);
  Pull_Resistor pull_resistor_11 (.node(pull_resistor_11_node));
  buf buffer_17 (pull_resistor_11_node, bitselector_5_out);
  BitSelector #(.width(1)) bitselector_5 (.out(bitselector_5_out), .sel(and_2_out));  // open: in
  buf buffer_18 (buffer_18_out, bitselector_5_out);
  buf buffer_19 (buffer_19_out, bitselector_4_out);
  Pull_Resistor pull_resistor_12 (.node(buffer_19_out));
  buf buffer_20 (buffer_20_out, bitselector_4_out);
  Pull_Resistor #(.pull(1)) pull_resistor_13 (.node(buffer_20_out));
  Pull_Resistor pull_resistor_14 (.node(pull_resistor_14_node));
  buf buffer_21 (pull_resistor_14_node, bitselector_6_out);
  BitSelector #(.width(1)) bitselector_6 (.out(bitselector_6_out), .sel(and_3_out));  // open: in
  buf buffer_22 (buffer_22_out, bitselector_6_out);
  Pull_Resistor #(.pull(1)) pull_resistor_15 (.node(buffer_22_out));
  buf buffer_23 (buffer_23_out, in_1[3]);
  buf buffer_24 (buffer_24_out, in_1[3]);
  BitSelector #(.width(1)) bitselector_7 (.in(1'b0), .out(bitselector_7_out), .sel(in_1[4]));
  and and_6 (and_6_out, ~buffer_11_out, pull_resistor_8_node);  // AND_Gate
  BitSelector #(.width(1)) bitselector_8 (.in(1'b0), .out(bitselector_8_out), .sel(in_1[5]));
  and and_7 (and_7_out, ~buffer_13_out, pull_resistor_9_node);  // AND_Gate
  and and_8 (out_2[0], and_4_out, and_5_out);
  and and_9 (and_9_out, ~pull_resistor_10_node, buffer_16_out);  // AND_Gate
  Pull_Resistor #(.pull(1)) pull_resistor_16 (.node(buffer_16_out));
  and and_10 (and_10_out, ~pull_resistor_11_node, buffer_18_out);  // AND_Gate
  Pull_Resistor #(.pull(1)) pull_resistor_17 (.node(buffer_18_out));
  and and_11 (and_11_out, ~buffer_19_out, buffer_20_out);  // AND_Gate
  and and_12 (and_12_out, ~pull_resistor_14_node, buffer_22_out);  // AND_Gate
  and and_13 (and_13_out, ~buffer_23_out, buffer_24_out);  // AND_Gate
  Pull_Resistor #(.pull(1)) pull_resistor_18 (.node(buffer_24_out));
  Pull_Resistor pull_resistor_19 (.node(pull_resistor_19_node));
  buf buffer_25 (pull_resistor_19_node, bitselector_7_out);
  buf buffer_26 (buffer_26_out, bitselector_7_out);
  Pull_Resistor #(.pull(1)) pull_resistor_20 (.node(buffer_26_out));
  buf buffer_27 (buffer_27_out, bitselector_9_out);
  Pull_Resistor pull_resistor_21 (.node(buffer_27_out));
  BitSelector #(.width(1)) bitselector_9 (.out(bitselector_9_out), .sel(and_6_out));  // open: in
  buf buffer_28 (buffer_28_out, bitselector_9_out);
  Pull_Resistor #(.pull(1)) pull_resistor_22 (.node(buffer_28_out));
  Pull_Resistor pull_resistor_23 (.node(pull_resistor_23_node));
  buf buffer_29 (pull_resistor_23_node, bitselector_8_out);
  Pull_Resistor #(.pull(1)) pull_resistor_24 (.node(pull_resistor_24_node));
  buf buffer_30 (pull_resistor_24_node, bitselector_8_out);
  buf buffer_31 (buffer_31_out, bitselector_10_out);
  Pull_Resistor pull_resistor_25 (.node(buffer_31_out));
  BitSelector #(.width(1)) bitselector_10 (.out(bitselector_10_out), .sel(and_7_out));  // open: in
  buf buffer_32 (buffer_32_out, bitselector_10_out);
  Pull_Resistor #(.pull(1)) pull_resistor_26 (.node(buffer_32_out));
  and and_14 (out_2[1], and_9_out, and_10_out);
  and and_15 (out_2[2], and_11_out, and_12_out);
  BitSelector #(.width(1)) bitselector_11 (.in(1'b0), .out(bitselector_11_out), .sel(in_1[3]));
  BitSelector #(.width(1)) bitselector_12 (.out(bitselector_12_out), .sel(and_13_out));  // open: in
  and and_16 (and_16_out, ~pull_resistor_19_node, buffer_26_out);  // AND_Gate
  and and_17 (and_17_out, ~buffer_27_out, buffer_28_out);  // AND_Gate
  and and_18 (and_18_out, ~pull_resistor_23_node, pull_resistor_24_node);  // AND_Gate
  and and_19 (and_19_out, ~buffer_31_out, buffer_32_out);  // AND_Gate
  Pull_Resistor pull_resistor_27 (.node(pull_resistor_27_node));
  buf buffer_33 (pull_resistor_27_node, bitselector_11_out);
  buf buffer_34 (buffer_34_out, bitselector_11_out);
  Pull_Resistor #(.pull(1)) pull_resistor_28 (.node(buffer_34_out));
  Pull_Resistor pull_resistor_29 (.node(pull_resistor_29_node));
  buf buffer_35 (pull_resistor_29_node, bitselector_12_out);
  Pull_Resistor #(.pull(1)) pull_resistor_30 (.node(pull_resistor_30_node));
  buf buffer_36 (pull_resistor_30_node, bitselector_12_out);
  and and_20 (out_2[4], and_16_out, and_17_out);
  and and_21 (out_2[5], and_18_out, and_19_out);
  and and_22 (and_22_out, ~pull_resistor_27_node, buffer_34_out);  // AND_Gate
  and and_23 (out_2[3], and_22_out, and_24_out);
  and and_24 (and_24_out, ~pull_resistor_29_node, pull_resistor_30_node);  // AND_Gate
endmodule

module game_over (
  input  [5:0] in_1,
  input  [5:0] in_2,
  output white_win,
  output draw,
  output black_win,
  output game_over
);

  wire comparator_1_eq, comparator_1_gt, comparator_1_lt;
  wire [5:0] adder_1_out;

  Adder #(.width(6)) adder_1 (.a(in_1), .b(in_2), .out(adder_1_out));  // open: cin, cout
  Transistor #(.\type ("n")) transistor_1 (.in(comparator_1_gt), .out(white_win), .gate(game_over));
  Pull_Resistor pull_resistor_1 (.node(white_win));
  Pull_Resistor pull_resistor_2 (.node(draw));
  Comparator #(.width(6), .mode("unsigned")) comparator_1 (
    .a(in_1), .b(in_2), .gt(comparator_1_gt), .eq(comparator_1_eq), .lt(comparator_1_lt));
  Transistor #(.\type ("n")) transistor_2 (.in(comparator_1_eq), .out(draw), .gate(game_over));
  Pull_Resistor pull_resistor_3 (.node(black_win));
  Transistor #(.\type ("n")) transistor_3 (.in(comparator_1_lt), .out(black_win), .gate(game_over));
  Comparator #(.width(6), .mode("unsigned")) comparator_2 (
    .a(adder_1_out), .b(6'b100100), .eq(game_over));  // open: gt, lt
endmodule

module progres_bar (
  input  [5:0] in_1,
  output [23:0] out_2
);

  wire [4:0] bit_extender_1_out;

  Multiplexer #(.select(5), .width(24)) multiplexer_1 (
    .in0({24{1'b0}}), .in1(24'h800000), .in2(24'hc00000), .in3(24'he00000), .in4(24'hf00000),
    .in5(24'hf80000), .in6(24'hfc0000), .in7(24'hfe0000), .in8(24'hff0000), .in9(24'hff8000),
    .in10(24'hffc000), .in11(24'hffe000), .in12(24'hfff000), .in13(24'hfff800), .in14(24'hfffc00),
    .in15(24'hfffe00), .in16(24'hffff00), .in17(24'hffff80), .in18(24'hffffc0), .in19(24'hffffe0),
    .in20(24'hfffff0), .in21(24'hfffff8), .in22(24'hfffffc), .in23(24'hfffffe), .in24({24{1'b1}}),
    .in25({24{1'b1}}), .in26({24{1'b1}}), .in27({24{1'b1}}), .in28({24{1'b1}}), .in29({24{1'b1}}),
    .in30({24{1'b1}}), .in31({24{1'b1}}), .out(out_2), .sel(bit_extender_1_out));  // open: en
  Bit_Extender #(.in_width(6), .out_width(5)) bit_extender_1 (.in(in_1), .out(bit_extender_1_out));
endmodule
